// Logisim project alarm.circ as structural Verilog: 2 circuits, main circuit alarme
module alarme (
  input  donneuneimpulsion,
  output out_2
);

  wire alarmComparator5Bits_1_i, alarmComparator5Bits_2_i, alarmComparator5Bits_3_i,
       alarmComparator5Bits_4_i, alarmComparator5Bits_5_i, alarmComparator5Bits_6_i;
  wire [5:0] undriven, undriven_2, undriven_3, undriven_4, undriven_5, undriven_6, undriven_7, undriven_8,
       undriven_9, undriven_10, undriven_11, undriven_12;

  comparator5Bits alarmComparator5Bits_1 (.in_1(undriven), .in_2(undriven_7), .i(alarmComparator5Bits_1_i));
  comparator5Bits alarmComparator5Bits_2 (.in_1(undriven_2), .in_2(undriven_11), .i(alarmComparator5Bits_2_i));
  comparator5Bits alarmComparator5Bits_3 (.in_1(undriven_3), .in_2(undriven_12), .i(alarmComparator5Bits_3_i));
  comparator5Bits alarmComparator5Bits_4 (.in_1(undriven_4), .in_2(undriven_8), .i(alarmComparator5Bits_4_i));
  comparator5Bits alarmComparator5Bits_5 (.in_1(undriven_5), .in_2(undriven_9), .i(alarmComparator5Bits_5_i));
  comparator5Bits alarmComparator5Bits_6 (.in_1(undriven_6), .in_2(undriven_10), .i(alarmComparator5Bits_6_i));
  and and_1 (out_2, alarmComparator5Bits_1_i, alarmComparator5Bits_2_i, alarmComparator5Bits_3_i, alarmComparator5Bits_4_i, alarmComparator5Bits_5_i, alarmComparator5Bits_6_i);
endmodule

module comparator5Bits (
  input  [5:0] in_1,
  input  [5:0] in_2,
  output i
);

  wire xnor_1_out, xnor_2_out, xnor_3_out, xnor_4_out, xnor_5_out;

  xnor xnor_1 (xnor_1_out, in_1[1], in_2[1]);
  xnor xnor_2 (xnor_2_out, in_1[2], in_2[2]);
  xnor xnor_3 (xnor_3_out, in_1[3], in_2[3]);
  xnor xnor_4 (xnor_4_out, in_1[4], in_2[4]);
  xnor xnor_5 (xnor_5_out, in_1[5], in_2[5]);
  and and_1 (i, xnor_1_out, xnor_2_out, xnor_3_out, xnor_4_out, xnor_5_out);
endmodule
