// Logisim project buttons.circ as structural Verilog: 3 circuits, main circuit buttonManager
module buttonManager (
  input  buttonNext,
  input  buttonAction,
  output longActionPress,
  output longNextPress,
  output shortActionPress,
  output shortNextPress
);

  detectLongPress buttonsDetectLongPress_1 (
    .buttonInput(buttonNext), .shortPress(shortNextPress), .LongPress(longNextPress));
  detectLongPress buttonsDetectLongPress_2 (
    .buttonInput(buttonAction), .shortPress(shortActionPress), .LongPress(longActionPress));
endmodule

module debouncerButton (
  input  buttonInput,
  input  clock,
  output buttonOutput
);

  wire d_ff_1_q, d_ff_2_q, undriven, xor_1_out;

  D_Flip_Flop d_ff_1 (.D(buttonInput), .clk(clock), .Q(d_ff_1_q));  // open: Qn, preset, reset
  D_Flip_Flop d_ff_2 (.D(d_ff_1_q), .clk(clock), .Q(d_ff_2_q));  // open: Qn, preset, reset
  xor xor_1 (xor_1_out, d_ff_2_q, d_ff_1_q);
  and and_1 (buttonOutput, d_ff_2_q, undriven);
endmodule

module detectLongPress (
  input  buttonInput,
  output shortPress,
  output LongPress
);

  wire and_1_out, buttonsLevelDetect_1_leveldown, buttonsLevelDetect_1_levelup,
       buttonsThreeBitsCounter_1_carryoutorstopped, clock_1_out, clock_2_out, clock_3_out;

  Clock clock_1 (.out(clock_1_out));
  levelDetect buttonsLevelDetect_1 (
    .signalInput(buttonInput), .clockSignal(clock_1_out), .levelUp(buttonsLevelDetect_1_levelup),
    .levelDown(buttonsLevelDetect_1_leveldown));
  Clock #(.highDuration(14285), .lowDuration(14285)) clock_2 (.out(clock_2_out));
  threeBitsCounter buttonsThreeBitsCounter_1 (
    .enable(1'b1), .reset(buttonsLevelDetect_1_levelup), .clock(clock_2_out), .stopEnd(1'b1),
    .carryOutOrStopped(buttonsThreeBitsCounter_1_carryoutorstopped));  // open: Output_bus_1
  and and_1 (and_1_out, buttonInput, buttonsThreeBitsCounter_1_carryoutorstopped);
  Clock clock_3 (.out(clock_3_out));
  and and_2 (shortPress, buttonsLevelDetect_1_leveldown, ~buttonsThreeBitsCounter_1_carryoutorstopped);  // AND_Gate
  levelDetect buttonLevelDetect_2 (
    .signalInput(and_1_out), .clockSignal(clock_3_out), .levelUp(LongPress));  // open: levelDown
endmodule
