// Logisim project counters.circ as structural Verilog
module threeBitsCounter (
  input  enable,
  input  reset,
  input  clock,
  input  stopEnd,
  output [2:0] Output_bus_1,
  output carryOutOrStopped
);

  wire countersThreeBitsCounterTransistion_1_d0, countersThreeBitsCounterTransistion_1_d1,
       countersThreeBitsCounterTransistion_1_d2;

  threeBitsCounterTransition countersThreeBitsCounterTransistion_1 (
    .stopEnd(stopEnd), .enable(enable), .C2(Output_bus_1[2]), .C1(Output_bus_1[1]), .C0(Output_bus_1[0]),
    .D2(countersThreeBitsCounterTransistion_1_d2), .D1(countersThreeBitsCounterTransistion_1_d1),
    .D0(countersThreeBitsCounterTransistion_1_d0), .carryOutOrStopped(carryOutOrStopped));
  D_Flip_Flop d_ff_1 (
    .D(countersThreeBitsCounterTransistion_1_d2), .clk(clock), .Q(Output_bus_1[2]), .reset(reset));  // open: Qn, preset
  D_Flip_Flop d_ff_2 (
    .D(countersThreeBitsCounterTransistion_1_d1), .clk(clock), .Q(Output_bus_1[1]), .reset(reset));  // open: Qn, preset
  D_Flip_Flop d_ff_3 (
    .D(countersThreeBitsCounterTransistion_1_d0), .clk(clock), .Q(Output_bus_1[0]), .reset(reset));  // open: Qn, preset
endmodule

module threeBitsCounterTransition (
  input  stopEnd,
  input  enable,
  input  C2,
  input  C1,
  input  C0,
  output D2,
  output D1,
  output D0,
  output carryOutOrStopped
);

  wire and_1_out, and_2_out, and_3_out, and_4_out, and_5_out, and_6_out, and_7_out, and_8_out, and_9_out,
       and_10_out, and_11_out, and_12_out, and_13_out, and_14_out, not_1_out, not_2_out, not_3_out,
       not_4_out, not_5_out, not_6_out, not_7_out, not_8_out, not_9_out;

  not not_1 (not_1_out, enable);
  not not_2 (not_2_out, C1);
  not not_3 (not_3_out, C0);
  not not_4 (not_4_out, C2);
  not not_5 (not_5_out, enable);
  not not_6 (not_6_out, C0);
  not not_7 (not_7_out, C1);
  not not_8 (not_8_out, enable);
  not not_9 (not_9_out, C0);
  and and_1 (and_1_out, enable, C2, C1, C0);
  and and_2 (and_2_out, stopEnd, C2, C1, C0);
  and and_3 (and_3_out, not_1_out, C2);
  and and_4 (and_4_out, C2, not_2_out);
  and and_5 (and_5_out, C2, not_3_out);
  and and_6 (and_6_out, enable, not_4_out, C1, C0);
  and and_7 (and_7_out, stopEnd, C2);
  and and_8 (and_8_out, not_5_out, C1);
  and and_9 (and_9_out, C1, not_6_out);
  and and_10 (and_10_out, enable, not_7_out, C0);
  and and_11 (and_11_out, stopEnd, C2, C1);
  and and_12 (and_12_out, not_8_out, C0);
  and and_13 (and_13_out, enable, not_9_out);
  and and_14 (and_14_out, stopEnd, enable, C2, C1);
  or or_1 (carryOutOrStopped, and_1_out, and_2_out);
  or or_2 (D2, and_3_out, and_4_out, and_5_out, and_6_out, and_7_out);
  or or_3 (D1, and_8_out, and_9_out, and_10_out, and_11_out);
  or or_4 (D0, and_12_out, and_13_out, and_14_out);
endmodule

module adder0_5Transition (
  input  Carry1,
  input  enable,
  input  D2,
  input  D1,
  input  D0,
  output Q2,
  output Q1,
  output Q0,
  output Carry2
);

  wire and_2_out, and_3_out, and_4_out, and_5_out, and_6_out, and_7_out, and_8_out, and_9_out, and_10_out,
       and_11_out, and_12_out, not_1_out, not_2_out, not_3_out, not_4_out, not_5_out, not_6_out, not_7_out,
       not_8_out, not_9_out, not_10_out, not_11_out;

  not not_1 (not_1_out, Carry1);
  not not_2 (not_2_out, enable);
  not not_3 (not_3_out, D0);
  not not_4 (not_4_out, Carry1);
  not not_5 (not_5_out, enable);
  not not_6 (not_6_out, D0);
  not not_7 (not_7_out, D2);
  not not_8 (not_8_out, D1);
  not not_9 (not_9_out, Carry1);
  not not_10 (not_10_out, enable);
  not not_11 (not_11_out, D0);
  and and_1 (Carry2, Carry1, enable, D2, D0);
  and and_2 (and_2_out, not_1_out, D2);
  and and_3 (and_3_out, not_2_out, D2);
  and and_4 (and_4_out, D2, not_3_out);
  and and_5 (and_5_out, Carry1, enable, D1, D0);
  and and_6 (and_6_out, not_4_out, D1);
  and and_7 (and_7_out, not_5_out, D1);
  and and_8 (and_8_out, D1, not_6_out);
  and and_9 (and_9_out, Carry1, enable, not_7_out, not_8_out, D0);
  and and_10 (and_10_out, not_9_out, D0);
  and and_11 (and_11_out, not_10_out, D0);
  and and_12 (and_12_out, Carry1, enable, not_11_out);
  or or_1 (Q2, and_2_out, and_3_out, and_4_out, and_5_out);
  or or_2 (Q1, and_6_out, and_7_out, and_8_out, and_9_out);
  or or_3 (Q0, and_10_out, and_11_out, and_12_out);
endmodule

module adder0_9Transition (
  input  stopEnd,
  input  enable,
  input  carryIn,
  input  d3,
  input  d2,
  input  d1,
  input  d0,
  output q3,
  output q2,
  output q1,
  output q0,
  output carryOut
);

  wire and_1_out, and_2_out, and_3_out, and_4_out, and_5_out, and_6_out, and_7_out, and_8_out, and_9_out,
       and_10_out, and_11_out, and_12_out, and_13_out, and_14_out, and_15_out, and_16_out, and_17_out,
       and_18_out, not_1_out, not_2_out, not_3_out, not_4_out, not_5_out, not_6_out, not_7_out, not_8_out,
       not_9_out, not_10_out, not_11_out, not_12_out, not_13_out, not_14_out, not_15_out, not_16_out,
       not_17_out, not_18_out, not_19_out, not_20_out;

  not not_1 (not_1_out, d2);
  not not_2 (not_2_out, d1);
  not not_3 (not_3_out, d2);
  not not_4 (not_4_out, d3);
  not not_5 (not_5_out, d1);
  not not_6 (not_6_out, d2);
  not not_7 (not_7_out, d1);
  not not_8 (not_8_out, enable);
  and and_1 (and_1_out, not_8_out, d3);
  not not_9 (not_9_out, carryIn);
  and and_2 (and_2_out, not_9_out, d3);
  and and_3 (and_3_out, d3, not_10_out);
  not not_10 (not_10_out, d0);
  and and_4 (and_4_out, enable, carryIn, d2, d1, d0);
  and and_5 (and_5_out, stopEnd, d3, not_1_out, not_2_out);
  not not_11 (not_11_out, carryIn);
  and and_6 (and_6_out, not_11_out, d2);
  not not_12 (not_12_out, enable);
  and and_7 (and_7_out, not_12_out, d2);
  and and_8 (and_8_out, d2, not_13_out);
  not not_13 (not_13_out, d1);
  and and_9 (and_9_out, d2, not_14_out);
  not not_14 (not_14_out, d0);
  and and_10 (and_10_out, carryIn, enable, not_3_out, d1, d0);
  not not_15 (not_15_out, carryIn);
  and and_11 (and_11_out, not_15_out, d1);
  not not_16 (not_16_out, enable);
  and and_12 (and_12_out, not_16_out, d1);
  and and_13 (and_13_out, d1, not_17_out);
  not not_17 (not_17_out, d0);
  and and_14 (and_14_out, carryIn, enable, not_4_out, not_5_out, d0);
  not not_18 (not_18_out, enable);
  and and_15 (and_15_out, not_18_out, d0);
  not not_19 (not_19_out, carryIn);
  and and_16 (and_16_out, not_19_out, d0);
  and and_17 (and_17_out, enable, carryIn, not_20_out);
  not not_20 (not_20_out, d0);
  and and_18 (and_18_out, stopEnd, d3, not_6_out, not_7_out, d0);
  and and_19 (carryOut, carryIn, enable, d3, d0);
  or or_1 (q3, and_1_out, and_2_out, and_3_out, and_4_out, and_5_out);
  or or_2 (q2, and_6_out, and_7_out, and_8_out, and_9_out, and_10_out);
  or or_3 (q1, and_11_out, and_12_out, and_13_out, and_14_out);
  or or_4 (q0, and_15_out, and_16_out, and_17_out, and_18_out);
endmodule

module adder0_23Transition (
  input  Carry,
  input  D4,
  input  D3,
  input  D2,
  input  D1,
  input  D0,
  input  enable,
  output Q4,
  output Q3,
  output Q2,
  output Q1,
  output Q0
);

  wire and_1_out, and_2_out, and_3_out, and_4_out, and_5_out, and_6_out, and_7_out, and_8_out, and_9_out,
       and_10_out, and_11_out, and_12_out, and_13_out, and_14_out, and_15_out, and_16_out, and_17_out,
       and_18_out, and_19_out, and_20_out, and_21_out, and_22_out, and_23_out, and_24_out, and_25_out,
       and_26_out, and_27_out, not_1_out, not_2_out, not_3_out, not_4_out, not_5_out, not_6_out, not_7_out,
       not_8_out, not_9_out, not_10_out, not_11_out, not_12_out, not_13_out, not_14_out, not_15_out,
       not_16_out, not_17_out, not_18_out, not_19_out, not_20_out, not_21_out, not_22_out, not_23_out,
       not_24_out, not_25_out, not_26_out, not_27_out, not_28_out, not_29_out, not_30_out;

  not not_1 (not_1_out, Carry);
  not not_2 (not_2_out, D2);
  not not_3 (not_3_out, D1);
  not not_4 (not_4_out, D0);
  not not_5 (not_5_out, enable);
  not not_6 (not_6_out, D4);
  not not_7 (not_7_out, Carry);
  not not_8 (not_8_out, D2);
  not not_9 (not_9_out, D1);
  not not_10 (not_10_out, D0);
  not not_11 (not_11_out, D4);
  not not_12 (not_12_out, D3);
  not not_13 (not_13_out, enable);
  not not_14 (not_14_out, D4);
  not not_15 (not_15_out, Carry);
  not not_16 (not_16_out, D1);
  not not_17 (not_17_out, D0);
  not not_18 (not_18_out, D2);
  not not_19 (not_19_out, D2);
  not not_20 (not_20_out, enable);
  not not_21 (not_21_out, D4);
  not not_22 (not_22_out, Carry);
  not not_23 (not_23_out, D0);
  not not_24 (not_24_out, D1);
  not not_25 (not_25_out, D1);
  not not_26 (not_26_out, enable);
  not not_27 (not_27_out, D4);
  not not_28 (not_28_out, Carry);
  not not_29 (not_29_out, D0);
  not not_30 (not_30_out, D0);
  and and_1 (and_1_out, not_1_out, D4);
  and and_2 (and_2_out, D4, not_2_out);
  and and_3 (and_3_out, D4, not_3_out);
  and and_4 (and_4_out, D4, not_4_out);
  and and_5 (and_5_out, D4, D3);
  and and_6 (and_6_out, enable, Carry, D3, D2, D1, D0);
  and and_7 (and_7_out, not_5_out, not_6_out, D3);
  and and_8 (and_8_out, not_7_out, D3);
  and and_9 (and_9_out, D3, not_8_out);
  and and_10 (and_10_out, D3, not_9_out);
  and and_11 (and_11_out, D3, not_10_out);
  and and_12 (and_12_out, enable, Carry, not_11_out, not_12_out, D2, D1, D0);
  and and_13 (and_13_out, not_13_out, not_14_out, D2);
  and and_14 (and_14_out, not_15_out, D2);
  and and_15 (and_15_out, D2, not_16_out);
  and and_16 (and_16_out, D2, not_17_out);
  and and_17 (and_17_out, Carry, D4, not_18_out, D1, D0);
  and and_18 (and_18_out, enable, Carry, not_19_out, D1, D0);
  and and_19 (and_19_out, not_20_out, not_21_out, D1);
  and and_20 (and_20_out, not_22_out, D1);
  and and_21 (and_21_out, D1, not_23_out);
  and and_22 (and_22_out, Carry, D4, not_24_out, D0);
  and and_23 (and_23_out, enable, Carry, not_25_out, D0);
  and and_24 (and_24_out, not_26_out, not_27_out, D0);
  and and_25 (and_25_out, not_28_out, D0);
  and and_26 (and_26_out, Carry, D4, not_29_out);
  and and_27 (and_27_out, enable, Carry, not_30_out);
  or or_1 (Q4, and_1_out, and_2_out, and_3_out, and_4_out, and_5_out, and_6_out);
  or or_2 (Q3, and_7_out, and_8_out, and_9_out, and_10_out, and_11_out, and_12_out);
  or or_3 (Q2, and_13_out, and_14_out, and_15_out, and_16_out, and_17_out, and_18_out);
  or or_4 (Q1, and_19_out, and_20_out, and_21_out, and_22_out, and_23_out);
  or or_5 (Q0, and_24_out, and_25_out, and_26_out, and_27_out);
endmodule

module adder0_6Transition (
  input  baction,
  input  b2,
  input  b1,
  input  b0,
  output q2,
  output q1,
  output q0
);

  wire and_1_out, and_2_out, and_3_out, and_4_out, and_5_out, and_6_out, and_7_out, and_8_out, and_9_out,
       and_10_out, not_1_out, not_2_out, not_3_out, not_4_out, not_5_out, not_6_out, not_7_out, not_8_out;

  not not_1 (not_1_out, baction);
  not not_2 (not_2_out, b0);
  not not_3 (not_3_out, baction);
  not not_4 (not_4_out, b0);
  not not_5 (not_5_out, b2);
  not not_6 (not_6_out, b1);
  not not_7 (not_7_out, baction);
  not not_8 (not_8_out, b0);
  and and_1 (and_1_out, not_1_out, b2);
  and and_2 (and_2_out, b2, not_2_out);
  or or_1 (q2, and_1_out, and_2_out, and_3_out);
  and and_3 (and_3_out, baction, b1, b0);
  and and_4 (and_4_out, not_3_out, b1);
  and and_5 (and_5_out, b1, not_4_out);
  and and_6 (and_6_out, b2, b1);
  and and_7 (and_7_out, baction, not_5_out, not_6_out, b0);
  and and_8 (and_8_out, not_7_out, b0);
  or or_2 (q0, and_8_out, and_9_out, and_10_out);
  and and_9 (and_9_out, b2, b1);
  and and_10 (and_10_out, baction, not_8_out);
  or or_3 (q1, and_4_out, and_5_out, and_6_out, and_7_out);
endmodule

module subtractor5_0Transition (
  input  carry1,
  input  b2,
  input  b1,
  input  b0,
  input  enable,
  output q2,
  output q1,
  output q0,
  output carry2
);

  wire and_1_out, and_2_out, and_3_out, and_4_out, and_5_out, and_6_out, and_7_out, and_8_out, and_9_out,
       and_10_out, and_11_out, not_1_out, not_2_out, not_3_out, not_4_out, not_5_out, not_6_out, not_7_out,
       not_8_out, not_9_out, not_10_out, not_11_out, not_12_out, not_13_out, not_14_out;

  not not_1 (not_1_out, enable);
  not not_2 (not_2_out, carry1);
  not not_3 (not_3_out, b2);
  not not_4 (not_4_out, b1);
  not not_5 (not_5_out, b0);
  not not_6 (not_6_out, enable);
  not not_7 (not_7_out, carry1);
  not not_8 (not_8_out, b0);
  not not_9 (not_9_out, enable);
  not not_10 (not_10_out, carry1);
  not not_11 (not_11_out, b0);
  not not_12 (not_12_out, b2);
  not not_13 (not_13_out, b1);
  not not_14 (not_14_out, b0);
  and and_1 (and_1_out, not_1_out, b2);
  and and_2 (and_2_out, not_2_out, b2);
  and and_3 (and_3_out, b2, b0);
  and and_4 (and_4_out, enable, carry1, not_3_out, not_4_out, not_5_out);
  and and_5 (and_5_out, not_6_out, b1);
  and and_6 (and_6_out, not_7_out, b1);
  and and_7 (and_7_out, b1, b0);
  and and_8 (and_8_out, enable, carry1, b2, not_8_out);
  and and_9 (and_9_out, not_9_out, b0);
  and and_10 (and_10_out, not_10_out, b0);
  and and_11 (and_11_out, enable, carry1, not_11_out);
  and and_12 (carry2, carry1, not_12_out, not_13_out, not_14_out);
  or or_1 (q2, and_1_out, and_2_out, and_3_out, and_4_out);
  or or_2 (q1, and_5_out, and_6_out, and_7_out, and_8_out);
  or or_3 (q0, and_9_out, and_10_out, and_11_out);
endmodule

module subtractor9_0Transition (
  input  carry2,
  input  b3,
  input  b2,
  input  b1,
  input  b0,
  input  enable,
  output q3,
  output q2,
  output q1,
  output q0,
  output carry3
);

  wire and_1_out, and_2_out, and_3_out, and_4_out, and_5_out, and_6_out, and_7_out, and_8_out, and_9_out,
       and_10_out, and_11_out, and_12_out, and_13_out, and_14_out, and_15_out, and_16_out, and_17_out,
       not_1_out, not_2_out, not_3_out, not_4_out, not_5_out, not_6_out, not_7_out, not_8_out, not_9_out,
       not_10_out, not_11_out, not_12_out, not_13_out, not_14_out, not_15_out, not_16_out, not_17_out,
       not_18_out, not_19_out, not_20_out, not_21_out, not_22_out;

  not not_1 (not_1_out, enable);
  not not_2 (not_2_out, carry2);
  not not_3 (not_3_out, b3);
  not not_4 (not_4_out, b2);
  not not_5 (not_5_out, b1);
  not not_6 (not_6_out, b0);
  not not_7 (not_7_out, enable);
  not not_8 (not_8_out, carry2);
  not not_9 (not_9_out, b0);
  not not_10 (not_10_out, enable);
  not not_11 (not_11_out, carry2);
  not not_12 (not_12_out, b1);
  not not_13 (not_13_out, b0);
  not not_14 (not_14_out, b1);
  not not_15 (not_15_out, b0);
  not not_16 (not_16_out, enable);
  not not_17 (not_17_out, carry2);
  not not_18 (not_18_out, b0);
  not not_19 (not_19_out, b3);
  not not_20 (not_20_out, b2);
  not not_21 (not_21_out, b1);
  not not_22 (not_22_out, b0);
  and and_1 (and_1_out, not_1_out, b3);
  and and_2 (and_2_out, not_2_out, b3);
  and and_3 (and_3_out, b3, b0);
  and and_4 (and_4_out, enable, carry2, not_3_out, not_4_out, not_5_out, not_6_out);
  and and_5 (and_5_out, not_7_out, b2);
  and and_6 (and_6_out, not_8_out, b2);
  and and_7 (and_7_out, b2, b0);
  and and_8 (and_8_out, b2, b1);
  and and_9 (and_9_out, enable, carry2, b3, not_9_out);
  and and_10 (and_10_out, not_10_out, b1);
  and and_11 (and_11_out, not_11_out, b1);
  and and_12 (and_12_out, b1, b0);
  and and_13 (and_13_out, enable, carry2, b2, not_12_out, not_13_out);
  and and_14 (and_14_out, enable, carry2, b3, not_14_out, not_15_out);
  and and_15 (and_15_out, not_16_out, b0);
  and and_16 (and_16_out, not_17_out, b0);
  and and_17 (and_17_out, enable, carry2, not_18_out);
  and and_18 (carry3, carry2, not_19_out, not_20_out, not_21_out, not_22_out);
  or or_1 (q3, and_1_out, and_2_out, and_3_out, and_4_out);
  or or_2 (q2, and_5_out, and_6_out, and_7_out, and_8_out, and_9_out);
  or or_3 (q1, and_10_out, and_11_out, and_12_out, and_13_out, and_14_out);
  or or_4 (q0, and_15_out, and_16_out, and_17_out);
endmodule

module subtractor23_0Transition (
  input  carry4,
  input  b4,
  input  b3,
  input  b2,
  input  b1,
  input  b0,
  input  enable,
  output q4,
  output q3,
  output q2,
  output q1,
  output q0
);

  wire and_1_out, and_2_out, and_3_out, and_4_out, and_5_out, and_6_out, and_7_out, and_8_out, and_9_out,
       and_10_out, and_11_out, and_12_out, and_13_out, and_14_out, and_15_out, and_16_out, and_17_out,
       and_18_out, and_19_out, and_20_out, and_21_out, and_22_out, and_23_out, and_24_out, not_1_out,
       not_2_out, not_3_out, not_4_out, not_5_out, not_6_out, not_7_out, not_8_out, not_9_out, not_10_out,
       not_11_out, not_12_out, not_13_out, not_14_out, not_15_out, not_16_out, not_17_out, not_18_out,
       not_19_out, not_20_out, not_21_out, not_22_out, not_23_out, not_24_out;

  not not_1 (not_1_out, b4);
  not not_2 (not_2_out, b3);
  not not_3 (not_3_out, b2);
  not not_4 (not_4_out, b1);
  not not_5 (not_5_out, b0);
  not not_6 (not_6_out, b2);
  not not_7 (not_7_out, b1);
  not not_8 (not_8_out, b0);
  not not_9 (not_9_out, enable);
  not not_10 (not_10_out, carry4);
  not not_11 (not_11_out, b2);
  not not_12 (not_12_out, b1);
  not not_13 (not_13_out, b0);
  not not_14 (not_14_out, enable);
  not not_15 (not_15_out, carry4);
  not not_16 (not_16_out, b1);
  not not_17 (not_17_out, b0);
  not not_18 (not_18_out, enable);
  not not_19 (not_19_out, carry4);
  not not_20 (not_20_out, b0);
  not not_21 (not_21_out, enable);
  and and_1 (and_1_out, not_21_out, b4);
  not not_22 (not_22_out, carry4);
  and and_2 (and_2_out, not_22_out, b4);
  and and_3 (and_3_out, b4, b0);
  and and_4 (and_4_out, b4, b1);
  and and_5 (and_5_out, b4, b2);
  and and_6 (and_6_out, enable, carry4, not_1_out, not_2_out, not_3_out, not_4_out, not_5_out);
  not not_23 (not_23_out, enable);
  and and_7 (and_7_out, not_23_out, b3);
  not not_24 (not_24_out, carry4);
  and and_8 (and_8_out, not_24_out, b3);
  and and_9 (and_9_out, b3, b0);
  and and_10 (and_10_out, b3, b1);
  and and_11 (and_11_out, b3, b2);
  and and_12 (and_12_out, enable, carry4, b4, not_6_out, not_7_out, not_8_out);
  and and_13 (and_13_out, not_9_out, b2);
  and and_14 (and_14_out, not_10_out, b2);
  and and_15 (and_15_out, b2, b0);
  and and_16 (and_16_out, b2, b1);
  and and_17 (and_17_out, enable, carry4, not_11_out, not_12_out, not_13_out);
  and and_18 (and_18_out, not_14_out, b1);
  and and_19 (and_19_out, not_15_out, b1);
  and and_20 (and_20_out, b1, b0);
  and and_21 (and_21_out, enable, carry4, not_16_out, not_17_out);
  and and_22 (and_22_out, not_18_out, b0);
  and and_23 (and_23_out, not_19_out, b0);
  and and_24 (and_24_out, enable, carry4, not_20_out);
  or or_1 (q2, and_13_out, and_14_out, and_15_out, and_16_out, and_17_out);
  or or_2 (q1, and_18_out, and_19_out, and_20_out, and_21_out);
  or or_3 (q0, and_22_out, and_23_out, and_24_out);
  or or_4 (q4, and_1_out, and_2_out, and_3_out, and_4_out, and_5_out, and_6_out);
  or or_5 (q3, and_7_out, and_8_out, and_9_out, and_10_out, and_11_out, and_12_out);
endmodule

module adder0_9 (
  input  enable,
  input  carryIn,
  input  clock,
  input  stopEnd,
  input  reset,
  output [3:0] outBits,
  output carryOut
);

  wire countersAdder0_9Transition_1_q0, countersAdder0_9Transition_1_q1, countersAdder0_9Transition_1_q2,
       countersAdder0_9Transition_1_q3;

  adder0_9Transition countersAdder0_9Transition_1 (
    .stopEnd(stopEnd), .enable(enable), .carryIn(carryIn), .d3(outBits[3]), .d2(outBits[2]), .d1(outBits[1]),
    .d0(outBits[0]), .q3(countersAdder0_9Transition_1_q3), .q2(countersAdder0_9Transition_1_q2),
    .q1(countersAdder0_9Transition_1_q1), .q0(countersAdder0_9Transition_1_q0), .carryOut(carryOut));
  D_Flip_Flop d_ff_1 (
    .D(countersAdder0_9Transition_1_q3), .clk(clock), .Q(outBits[3]), .reset(reset));  // open: Qn, preset
  D_Flip_Flop d_ff_2 (
    .D(countersAdder0_9Transition_1_q2), .clk(clock), .Q(outBits[2]), .reset(reset));  // open: Qn, preset
  D_Flip_Flop d_ff_3 (
    .D(countersAdder0_9Transition_1_q1), .clk(clock), .Q(outBits[1]), .reset(reset));  // open: Qn, preset
  D_Flip_Flop d_ff_4 (
    .D(countersAdder0_9Transition_1_q0), .clk(clock), .Q(outBits[0]), .reset(reset));  // open: Qn, preset
endmodule

module adder0_5 (
  input  carryIn,
  input  enable,
  input  reset,
  input  clock,
  output [2:0] outBits,
  output carryOut
);

  wire countersAdder0_5Transition_1_q0, countersAdder0_5Transition_1_q1, countersAdder0_5Transition_1_q2;

  adder0_5Transition countersAdder0_5Transition_1 (
    .Carry1(carryIn), .enable(enable), .D2(outBits[2]), .D1(outBits[1]), .D0(outBits[0]),
    .Q2(countersAdder0_5Transition_1_q2), .Q1(countersAdder0_5Transition_1_q1),
    .Q0(countersAdder0_5Transition_1_q0), .Carry2(carryOut));
  D_Flip_Flop d_ff_1 (
    .D(countersAdder0_5Transition_1_q2), .clk(clock), .Q(outBits[2]), .reset(reset));  // open: Qn, preset
  D_Flip_Flop d_ff_2 (
    .D(countersAdder0_5Transition_1_q1), .clk(clock), .Q(outBits[1]), .reset(reset));  // open: Qn, preset
  D_Flip_Flop d_ff_3 (
    .D(countersAdder0_5Transition_1_q0), .clk(clock), .Q(outBits[0]), .reset(reset));  // open: Qn, preset
endmodule

module adder0_60 (
  input  carryIn,
  input  enable,
  input  clock,
  output [3:0] outBits1,
  output [2:0] outBits2,
  output carryOut
);

  wire countersAdder0_9_1_carryout;

  adder0_9 countersAdder0_9_1 (
    .enable(carryIn), .carryIn(enable), .clock(clock), .stopEnd(1'b0), .reset(1'b0), .outBits(outBits1),
    .carryOut(countersAdder0_9_1_carryout));
  adder0_5 Countersadder0_5_2 (
    .carryIn(countersAdder0_9_1_carryout), .enable(enable), .reset(1'b0), .clock(clock), .outBits(outBits2),
    .carryOut(carryOut));
endmodule

module adder0_23 (
  input  carryIn,
  input  enable,
  input  clock,
  output [4:0] outBits
);

  wire countersAdder0_23Transition_1_q0, countersAdder0_23Transition_1_q1, countersAdder0_23Transition_1_q2,
       countersAdder0_23Transition_1_q3, countersAdder0_23Transition_1_q4;

  adder0_23Transition countersAdder0_23Transition_1 (
    .Carry(carryIn), .D4(outBits[4]), .D3(outBits[3]), .D2(outBits[2]), .D1(outBits[1]), .D0(outBits[0]),
    .enable(enable), .Q4(countersAdder0_23Transition_1_q4), .Q3(countersAdder0_23Transition_1_q3),
    .Q2(countersAdder0_23Transition_1_q2), .Q1(countersAdder0_23Transition_1_q1),
    .Q0(countersAdder0_23Transition_1_q0));
  D_Flip_Flop d_ff_1 (.D(countersAdder0_23Transition_1_q4), .clk(clock), .Q(outBits[4]));  // open: Qn, preset, reset
  D_Flip_Flop d_ff_2 (.D(countersAdder0_23Transition_1_q3), .clk(clock), .Q(outBits[3]));  // open: Qn, preset, reset
  D_Flip_Flop d_ff_3 (.D(countersAdder0_23Transition_1_q2), .clk(clock), .Q(outBits[2]));  // open: Qn, preset, reset
  D_Flip_Flop d_ff_4 (.D(countersAdder0_23Transition_1_q1), .clk(clock), .Q(outBits[1]));  // open: Qn, preset, reset
  D_Flip_Flop d_ff_5 (.D(countersAdder0_23Transition_1_q0), .clk(clock), .Q(outBits[0]));  // open: Qn, preset, reset
endmodule
