// Logisim project displaySegment.circ as structural Verilog: 3 circuits, main circuit displaySegment
module displaySegment (
  input  [5:0] S0,
  input  [5:0] S1,
  input  [5:0] S2,
  input  [5:0] S3,
  input  [5:0] S4,
  input  [5:0] S5,
  input  [5:0] pointData
);

  wire display_5_a, display_5_b, display_5_c, display_5_d, display_5_e, display_5_f, display_5_g,
       display_6_a, display_6_b, display_6_c, display_6_d, display_6_e, display_6_f, display_6_g,
       displaySegmentDisplay_1_a, displaySegmentDisplay_1_b, displaySegmentDisplay_1_c,
       displaySegmentDisplay_1_d, displaySegmentDisplay_1_e, displaySegmentDisplay_1_f,
       displaySegmentDisplay_1_g, displaySegmentDisplay_2_a, displaySegmentDisplay_2_b,
       displaySegmentDisplay_2_c, displaySegmentDisplay_2_d, displaySegmentDisplay_2_e,
       displaySegmentDisplay_2_f, displaySegmentDisplay_2_g, displaySegmentDisplay_3_a,
       displaySegmentDisplay_3_b, displaySegmentDisplay_3_c, displaySegmentDisplay_3_d,
       displaySegmentDisplay_3_e, displaySegmentDisplay_3_f, displaySegmentDisplay_3_g,
       displaySegmentDisplay_4_a, displaySegmentDisplay_4_b, displaySegmentDisplay_4_c,
       displaySegmentDisplay_4_d, displaySegmentDisplay_4_e, displaySegmentDisplay_4_f,
       displaySegmentDisplay_4_g;

  display displaySegmentDisplay_1 (
    .B4(S0[0]), .B3(S0[4]), .B2(S0[3]), .B1(S0[2]), .B0(S0[1]), .enable(S0[5]),
    .a(displaySegmentDisplay_1_a), .b(displaySegmentDisplay_1_b), .c(displaySegmentDisplay_1_c),
    .d(displaySegmentDisplay_1_d), .e(displaySegmentDisplay_1_e), .f(displaySegmentDisplay_1_f),
    .g(displaySegmentDisplay_1_g));
  display displaySegmentDisplay_2 (
    .B4(S1[0]), .B3(S1[4]), .B2(S1[3]), .B1(S1[2]), .B0(S1[1]), .enable(S1[5]),
    .a(displaySegmentDisplay_2_a), .b(displaySegmentDisplay_2_b), .c(displaySegmentDisplay_2_c),
    .d(displaySegmentDisplay_2_d), .e(displaySegmentDisplay_2_e), .f(displaySegmentDisplay_2_f),
    .g(displaySegmentDisplay_2_g));
  display displaySegmentDisplay_3 (
    .B4(S2[0]), .B3(S2[4]), .B2(S2[3]), .B1(S2[2]), .B0(S2[1]), .enable(S2[5]),
    .a(displaySegmentDisplay_3_a), .b(displaySegmentDisplay_3_b), .c(displaySegmentDisplay_3_c),
    .d(displaySegmentDisplay_3_d), .e(displaySegmentDisplay_3_e), .f(displaySegmentDisplay_3_f),
    .g(displaySegmentDisplay_3_g));
  display displaySegmentDisplay_4 (
    .B4(S3[0]), .B3(S3[4]), .B2(S3[3]), .B1(S3[2]), .B0(S3[1]), .enable(S3[5]),
    .a(displaySegmentDisplay_4_a), .b(displaySegmentDisplay_4_b), .c(displaySegmentDisplay_4_c),
    .d(displaySegmentDisplay_4_d), .e(displaySegmentDisplay_4_e), .f(displaySegmentDisplay_4_f),
    .g(displaySegmentDisplay_4_g));
  display display_5 (
    .B4(S4[0]), .B3(S4[4]), .B2(S4[3]), .B1(S4[2]), .B0(S4[1]), .enable(S4[5]), .a(display_5_a),
    .b(display_5_b), .c(display_5_c), .d(display_5_d), .e(display_5_e), .f(display_5_f), .g(display_5_g));
  display display_6 (
    .B4(S5[0]), .B3(S5[4]), .B2(S5[3]), .B1(S5[2]), .B0(S5[1]), .enable(S5[5]), .a(display_6_a),
    .b(display_6_b), .c(display_6_c), .d(display_6_d), .e(display_6_e), .f(display_6_f), .g(display_6_g));
  _7_Segment_Display L_7_Segment_Display_1 (
    .g(displaySegmentDisplay_1_g), .f(displaySegmentDisplay_1_f), .a(displaySegmentDisplay_1_a),
    .b(displaySegmentDisplay_1_b), .e(displaySegmentDisplay_1_e), .d(displaySegmentDisplay_1_d),
    .c(displaySegmentDisplay_1_c), .dp(pointData[0]));
  _7_Segment_Display L_7_Segment_Display_2 (
    .g(displaySegmentDisplay_2_g), .f(displaySegmentDisplay_2_f), .a(displaySegmentDisplay_2_a),
    .b(displaySegmentDisplay_2_b), .e(displaySegmentDisplay_2_e), .d(displaySegmentDisplay_2_d),
    .c(displaySegmentDisplay_2_c), .dp(pointData[1]));
  _7_Segment_Display L_7_Segment_Display_3 (
    .g(displaySegmentDisplay_3_g), .f(displaySegmentDisplay_3_f), .a(displaySegmentDisplay_3_a),
    .b(displaySegmentDisplay_3_b), .e(displaySegmentDisplay_3_e), .d(displaySegmentDisplay_3_d),
    .c(displaySegmentDisplay_3_c), .dp(pointData[2]));
  _7_Segment_Display L_7_Segment_Display_4 (
    .g(displaySegmentDisplay_4_g), .f(displaySegmentDisplay_4_f), .a(displaySegmentDisplay_4_a),
    .b(displaySegmentDisplay_4_b), .e(displaySegmentDisplay_4_e), .d(displaySegmentDisplay_4_d),
    .c(displaySegmentDisplay_4_c), .dp(pointData[3]));
  _7_Segment_Display L_7_Segment_Display_5 (
    .g(display_5_g), .f(display_5_f), .a(display_5_a), .b(display_5_b), .e(display_5_e), .d(display_5_d),
    .c(display_5_c), .dp(pointData[4]));
  _7_Segment_Display L_7_Segment_Display_6 (
    .g(display_6_g), .f(display_6_f), .a(display_6_a), .b(display_6_b), .e(display_6_e), .d(display_6_d),
    .c(display_6_c), .dp(pointData[5]));
endmodule

module display (
  input  B4,
  input  B3,
  input  B2,
  input  B1,
  input  B0,
  input  enable,
  output a,
  output b,
  output c,
  output d,
  output e,
  output f,
  output g
);

  wire and_1_out, and_2_out, and_3_out, and_4_out, and_5_out, and_6_out, and_7_out, and_8_out, and_9_out,
       and_10_out, and_11_out, and_12_out, and_13_out, and_14_out, and_15_out, and_16_out, and_17_out,
       and_18_out, and_19_out, and_20_out, and_21_out, and_22_out, and_23_out, and_24_out, and_25_out,
       and_26_out, and_27_out, and_28_out, and_29_out, and_30_out, and_31_out, and_32_out, and_33_out,
       and_34_out, and_35_out, and_36_out, and_37_out, and_38_out, and_39_out, and_40_out, and_41_out,
       and_42_out, and_43_out, and_44_out, and_45_out, and_46_out, and_47_out, and_48_out, and_49_out,
       and_50_out, and_51_out, and_52_out, and_53_out, and_54_out, and_55_out, not_1_out, not_2_out,
       not_3_out, not_4_out, not_5_out, not_6_out, not_7_out, not_8_out, not_9_out, not_10_out, not_11_out,
       not_12_out, not_13_out, not_14_out, not_15_out, not_16_out, not_17_out, not_18_out, not_19_out,
       not_20_out, not_21_out, not_22_out, not_23_out, not_24_out, not_25_out, not_26_out, not_27_out,
       not_28_out, not_29_out, not_30_out, not_31_out, not_32_out, not_33_out, not_34_out, not_35_out,
       not_36_out, not_37_out, not_38_out, not_39_out, not_40_out, not_41_out, not_42_out, not_43_out,
       not_44_out, not_45_out, not_46_out, not_47_out, not_48_out, not_49_out, not_50_out, not_51_out,
       not_52_out, not_53_out, not_54_out, not_55_out, not_56_out, not_57_out, not_58_out, not_59_out,
       not_60_out, not_61_out, not_62_out, not_63_out, not_64_out, not_65_out, not_66_out, not_67_out,
       not_68_out, not_69_out, not_70_out, not_71_out, not_72_out, not_73_out, not_74_out, not_75_out,
       not_76_out, not_77_out, not_78_out, not_79_out, not_80_out, not_81_out, not_82_out, not_83_out,
       not_84_out, not_85_out, not_86_out, not_87_out, not_88_out, not_89_out, not_90_out, not_91_out,
       not_92_out, or_1_out, or_2_out, or_3_out, or_4_out, or_5_out, or_6_out;

  not not_1 (not_1_out, B2);
  not not_2 (not_2_out, B1);
  not not_3 (not_3_out, B0);
  not not_4 (not_4_out, B4);
  not not_5 (not_5_out, B3);
  not not_6 (not_6_out, B3);
  not not_7 (not_7_out, B2);
  not not_8 (not_8_out, B3);
  not not_9 (not_9_out, B1);
  not not_10 (not_10_out, B4);
  not not_11 (not_11_out, B3);
  not not_12 (not_12_out, B0);
  not not_13 (not_13_out, B4);
  not not_14 (not_14_out, B0);
  not not_15 (not_15_out, B2);
  not not_16 (not_16_out, B1);
  not not_17 (not_17_out, B2);
  not not_18 (not_18_out, B0);
  not not_19 (not_19_out, B4);
  not not_20 (not_20_out, B3);
  not not_21 (not_21_out, B2);
  not not_22 (not_22_out, B4);
  not not_23 (not_23_out, B3);
  not not_24 (not_24_out, B1);
  not not_25 (not_25_out, B0);
  not not_26 (not_26_out, B2);
  not not_27 (not_27_out, B1);
  not not_28 (not_28_out, B4);
  not not_29 (not_29_out, B3);
  not not_30 (not_30_out, B2);
  not not_31 (not_31_out, B0);
  not not_32 (not_32_out, B1);
  not not_33 (not_33_out, B0);
  not not_34 (not_34_out, B4);
  not not_35 (not_35_out, B3);
  not not_36 (not_36_out, B1);
  not not_37 (not_37_out, B3);
  not not_38 (not_38_out, B2);
  not not_39 (not_39_out, B1);
  not not_40 (not_40_out, B3);
  not not_41 (not_41_out, B1);
  not not_42 (not_42_out, B3);
  not not_43 (not_43_out, B4);
  not not_44 (not_44_out, B2);
  not not_45 (not_45_out, B1);
  not not_46 (not_46_out, B4);
  not not_47 (not_47_out, B3);
  not not_48 (not_48_out, B2);
  not not_49 (not_49_out, B0);
  not not_50 (not_50_out, B4);
  not not_51 (not_51_out, B3);
  not not_52 (not_52_out, B0);
  not not_53 (not_53_out, B4);
  not not_54 (not_54_out, B2);
  not not_55 (not_55_out, B4);
  not not_56 (not_56_out, B1);
  not not_57 (not_57_out, B4);
  not not_58 (not_58_out, B1);
  not not_59 (not_59_out, B2);
  not not_60 (not_60_out, B1);
  not not_61 (not_61_out, B0);
  not not_62 (not_62_out, B3);
  not not_63 (not_63_out, B1);
  not not_64 (not_64_out, B0);
  not not_65 (not_65_out, B2);
  not not_66 (not_66_out, B0);
  not not_67 (not_67_out, B3);
  not not_68 (not_68_out, B0);
  not not_69 (not_69_out, B2);
  not not_70 (not_70_out, B4);
  not not_71 (not_71_out, B3);
  not not_72 (not_72_out, B1);
  not not_73 (not_73_out, B0);
  not not_74 (not_74_out, B1);
  not not_75 (not_75_out, B0);
  not not_76 (not_76_out, B4);
  not not_77 (not_77_out, B3);
  not not_78 (not_78_out, B1);
  not not_79 (not_79_out, B0);
  not not_80 (not_80_out, B2);
  not not_81 (not_81_out, B2);
  not not_82 (not_82_out, B4);
  not not_83 (not_83_out, B2);
  not not_84 (not_84_out, B4);
  not not_85 (not_85_out, B0);
  not not_86 (not_86_out, B4);
  not not_87 (not_87_out, B3);
  not not_88 (not_88_out, B1);
  not not_89 (not_89_out, B2);
  not not_90 (not_90_out, B1);
  not not_91 (not_91_out, B4);
  not not_92 (not_92_out, B2);
  and and_1 (and_1_out, not_1_out, not_2_out, not_3_out);
  and and_2 (and_2_out, not_4_out, not_5_out, B1);
  and and_3 (and_3_out, not_6_out, not_7_out, B1, B0);
  and and_4 (and_4_out, not_8_out, B2, not_9_out, B0);
  and and_5 (and_5_out, not_10_out, B2, B1);
  and and_6 (and_6_out, not_11_out, B2, B1, not_12_out);
  and and_7 (and_7_out, not_13_out, B3, not_14_out);
  and and_8 (and_8_out, B3, not_15_out, not_16_out);
  and and_9 (and_9_out, B3, not_17_out, not_18_out);
  and and_10 (and_10_out, not_19_out, not_20_out, not_21_out);
  and and_11 (and_11_out, not_22_out, not_23_out, not_24_out, not_25_out);
  and and_12 (and_12_out, not_26_out, not_27_out, B0);
  and and_13 (and_13_out, not_28_out, not_29_out, B1, B0);
  and and_14 (and_14_out, B3, not_30_out, not_31_out);
  and and_15 (and_15_out, B3, not_32_out, B0);
  and and_16 (and_16_out, B4, B2, B1, not_33_out);
  and and_17 (and_17_out, B4, B3, B2);
  and and_18 (and_18_out, not_34_out, not_35_out, not_36_out);
  and and_19 (and_19_out, not_37_out, not_38_out, not_39_out);
  and and_20 (and_20_out, not_40_out, B0);
  and and_21 (and_21_out, not_41_out, B0);
  and and_22 (and_22_out, not_42_out, B2, B1);
  and and_23 (and_23_out, not_43_out, B3, not_44_out);
  and and_24 (and_24_out, B4, B2, B0);
  and and_25 (and_25_out, B4, B3, B2, not_45_out);
  and and_26 (and_26_out, not_46_out, not_47_out, not_48_out, not_49_out);
  and and_27 (and_27_out, not_50_out, not_51_out, B1, not_52_out);
  and and_28 (and_28_out, not_53_out, not_54_out, B1, B0);
  and and_29 (and_29_out, not_55_out, B2, not_56_out, B0);
  and and_30 (and_30_out, not_57_out, B3, not_58_out);
  and and_31 (and_31_out, B3, not_59_out, B1, B0);
  and and_32 (and_32_out, B3, B2, not_60_out);
  and and_33 (and_33_out, B3, B2, not_61_out);
  and and_34 (and_34_out, B4, not_62_out, not_63_out, not_64_out);
  and and_35 (and_35_out, B4, B2, B1, B0);
  and and_36 (and_36_out, not_65_out, not_66_out);
  and and_37 (and_37_out, not_67_out, B1, not_68_out);
  and and_38 (and_38_out, B3, not_69_out, B1);
  and and_39 (and_39_out, not_70_out, B3, B2);
  and and_40 (and_40_out, B4, not_71_out);
  and and_41 (and_41_out, B4, not_72_out, not_73_out);
  and and_42 (and_42_out, not_74_out, not_75_out);
  and and_43 (and_43_out, not_76_out, not_77_out, B2, not_78_out);
  and and_44 (and_44_out, B2, not_79_out);
  and and_45 (and_45_out, B3, not_80_out);
  and and_46 (and_46_out, B3, B1);
  and and_47 (and_47_out, B4, not_81_out);
  and and_48 (and_48_out, B4, B3);
  and and_49 (and_49_out, not_82_out, not_83_out, B1, enable);
  and and_50 (and_50_out, not_84_out, B1, not_85_out, enable);
  and and_51 (and_51_out, not_86_out, not_87_out, B2, not_88_out, enable);
  and and_52 (and_52_out, B3, not_89_out, not_90_out, enable);
  and and_53 (and_53_out, not_91_out, B3, B0, enable);
  and and_54 (and_54_out, B4, not_92_out, B0, enable);
  and and_55 (and_55_out, B4, B1, B0, enable);
  or or_1 (or_1_out, and_1_out, and_2_out, and_3_out, and_4_out, and_5_out, and_6_out, and_7_out, and_8_out, and_9_out);
  or or_2 (or_2_out, and_10_out, and_11_out, and_12_out, and_13_out, and_14_out, and_15_out, and_16_out, and_17_out);
  or or_3 (or_3_out, and_18_out, and_19_out, and_20_out, and_21_out, and_22_out, and_23_out, and_24_out, and_25_out);
  or or_4 (or_4_out, and_26_out, and_27_out, and_28_out, and_29_out, and_30_out, and_31_out, and_32_out, and_33_out, and_34_out, and_35_out);
  or or_5 (or_5_out, and_36_out, and_37_out, and_38_out, and_39_out, and_40_out, and_41_out);
  or or_6 (or_6_out, and_42_out, and_43_out, and_44_out, and_45_out, and_46_out, and_47_out, and_48_out);
  or or_7 (g, and_49_out, and_50_out, and_51_out, and_52_out, and_53_out, and_54_out, and_55_out);
  and and_56 (a, or_1_out, enable);
  and and_57 (b, or_2_out, enable);
  and and_58 (c, or_3_out, enable);
  and and_59 (d, or_4_out, enable);
  and and_60 (e, or_5_out, enable);
  and and_61 (f, or_6_out, enable);
endmodule

module displayManager (
  input  [29:0] segmentData1,
  input  [29:0] segmentData2,
  input  [29:0] segmentData3,
  input  [29:0] segmentData4,
  input  [29:0] segmentData5,
  input  [29:0] segmentData6,
  input  [29:0] segmentData7,
  input  [29:0] segmentData8,
  input  [29:0] segmentData9,
  input  [3:0] state,
  output [5:0] s0,
  output [5:0] s1,
  output [5:0] s2,
  output [5:0] s3,
  output [5:0] s4,
  output [5:0] s5,
  output [5:0] pointDataSelected
);

  Multiplexer #(.select(4), .width(30), .enable("false")) multiplexer_1 (
    .in0(segmentData1), .in1(segmentData2), .in2(segmentData3), .in3(segmentData4), .in4(segmentData5),
    .in5(segmentData6), .in6(segmentData7), .in7(segmentData8), .in8(segmentData9),
    .out({s5[4:0], s4[4:0], s3[4:0], s2[4:0], s1[4:0], s0[4:0]}), .sel(state));  // open: in9, in10, in11, in12, in13, in14, in15
  Multiplexer #(.select(4), .width(6), .enable("false")) multiplexer_2 (
    .in0(6'b010100), .out(pointDataSelected), .sel(state));  // open: in1, in2, in3, in4, in5, in6, in7, in8, in9, in10, in11, in12, in13, in14, in15

  assign s0[5] = 1'b1;
  assign s1[5] = 1'b1;
  assign s2[5] = 1'b1;
  assign s3[5] = 1'b1;
  assign s4[5] = 1'b1;
  assign s5[5] = 1'b1;
endmodule
