// Logisim project game.circ as structural Verilog: 6 circuits, main circuit game
module game (
  input  buttonInput,
  output [4:0] s5,
  output [4:0] s4,
  output [4:0] s3,
  output [4:0] s2,
  output [4:0] s1,
  output [4:0] s0
);

  wire clock_1_out, clock_2_out, clock_3_out, clock_4_out, clock_5_out, clock_6_out, clock_7_out,
       gameFilter_1_out1, gameFilter_1_out2, gameLevelDetect_1_levelup, gameLevelDetect_2_levelup,
       gamePlayerManager_S1_endgame, gamerRandom_1_random1, gamerRandom_1_random2, gameS2_out1, gameS2_out2,
       gameS3_out1, gameS3_out2, gameS4_out1, gameS4_out2, gameS5_out1, gameS5_out2, multiplexer_1_out;
  wire [3:0] gameAdder0_9_1_outbits, gamePlayerManager_S1_out7segment, gameS2_out7segment,
       gameS3_out7segment, gameS4_out7segment, gameS5_out7segment;

  Clock #(.highDuration(500000), .lowDuration(500000)) clock_1 (.out(clock_1_out));
  adder0_9 gameAdder0_9_1 (
    .enable(1'b1), .carryIn(1'b1), .clock(clock_1_out), .stopEnd(1'b1), .reset(gamePlayerManager_S1_endgame),
    .outBits(gameAdder0_9_1_outbits));  // open: carryOut
  Clock #(.highDuration(125000), .lowDuration(125000)) clock_2 (.out(clock_2_out));
  Clock #(.highDuration(62500), .lowDuration(62500)) clock_3 (.out(clock_3_out));
  Clock #(.highDuration(31250), .lowDuration(31250)) clock_4 (.out(clock_4_out));
  Clock #(.highDuration(15625), .lowDuration(15625)) clock_5 (.out(clock_5_out));
  Multiplexer #(.select(4), .enable("false")) multiplexer_1 (
    .in0(clock_2_out), .in1(clock_2_out), .in2(clock_3_out), .in3(clock_3_out), .in4(clock_4_out),
    .in5(clock_4_out), .in6(clock_4_out), .in7(clock_5_out), .in8(clock_5_out), .in9(clock_5_out),
    .in10(1'b0), .in11(1'b0), .in12(1'b0), .in13(1'b0), .in14(1'b0), .in15(1'b0), .out(multiplexer_1_out),
    .sel(gameAdder0_9_1_outbits));
  gamerRandom gamerRandom_1 (
    .clock(multiplexer_1_out), .reset(gamePlayerManager_S1_endgame), .random1(gamerRandom_1_random1),
    .random2(gamerRandom_1_random2));
  Clock #(.highDuration(10000), .lowDuration(10000)) clock_6 (.out(clock_6_out));
  gameFilter gameFilter_1 (
    .in1(gamerRandom_1_random1), .in2(gamerRandom_1_random2), .pIn1(gameS5_out7segment[0]),
    .pIn2(gameS5_out7segment[1]), .out1(gameFilter_1_out1), .out2(gameFilter_1_out2));
  Clock #(.highDuration(8000), .lowDuration(8000)) clock_7 (.out(clock_7_out));
  levelDetect gameLevelDetect_1 (
    .signalInput(gameFilter_1_out1), .clockSignal(clock_7_out), .levelUp(gameLevelDetect_1_levelup));  // open: levelDown
  levelDetect gameLevelDetect_2 (
    .signalInput(gameFilter_1_out2), .clockSignal(clock_7_out), .levelUp(gameLevelDetect_2_levelup));  // open: levelDown
  game7Segment gameS5 (
    .in1(gameLevelDetect_1_levelup), .in2(gameLevelDetect_2_levelup), .reset(gamePlayerManager_S1_endgame),
    .clock(clock_6_out), .out7Segment(gameS5_out7segment), .out1(gameS5_out1), .out2(gameS5_out2));
  game7Segment gameS4 (
    .in1(gameS5_out1), .in2(gameS5_out2), .reset(gamePlayerManager_S1_endgame), .clock(clock_6_out),
    .out7Segment(gameS4_out7segment), .out1(gameS4_out1), .out2(gameS4_out2));
  game7Segment gameS3 (
    .in1(gameS4_out1), .in2(gameS4_out2), .reset(gamePlayerManager_S1_endgame), .clock(clock_6_out),
    .out7Segment(gameS3_out7segment), .out1(gameS3_out1), .out2(gameS3_out2));
  game7Segment gameS2 (
    .in1(gameS3_out1), .in2(gameS3_out2), .reset(gamePlayerManager_S1_endgame), .clock(clock_6_out),
    .out7Segment(gameS2_out7segment), .out1(gameS2_out1), .out2(gameS2_out2));
  gamePlayerManager gamePlayerManager_S1 (
    .buttonInput(buttonInput), .in1(gameS2_out1), .in2(gameS2_out2), .reset(gamePlayerManager_S1_endgame),
    .clock(clock_6_out), .endGame(gamePlayerManager_S1_endgame),
    .out7Segment(gamePlayerManager_S1_out7segment));
  convert4_6 gameConvert4_6_1 (.inBits(gameS5_out7segment), .outBits(s5));
  convert4_6 gameConvert4_6_2 (.inBits(gameS4_out7segment), .outBits(s4));
  convert4_6 gameConvert4_6_3 (.inBits(gameS3_out7segment), .outBits(s3));
  convert4_6 gameConvert4_6_4 (.inBits(gameS2_out7segment), .outBits(s2));
  convert4_6 gameConvert4_6_5 (.inBits(gamePlayerManager_S1_out7segment), .outBits(s1));
  convert4_6 gameConvert4_6_6 (.inBits(gameAdder0_9_1_outbits), .outBits(s0));
endmodule

module game7Segment (
  input  in1,
  input  in2,
  input  reset,
  input  clock,
  output [3:0] out7Segment,
  output out1,
  output out2
);

  D_Flip_Flop d_ff_1 (.D(in1), .clk(clock), .Q(out7Segment[0]), .reset(reset));  // open: Qn, preset
  D_Flip_Flop d_ff_2 (.D(in2), .clk(clock), .Q(out7Segment[1]), .reset(reset));  // open: Qn, preset
  D_Flip_Flop d_ff_3 (.D(out7Segment[0]), .clk(clock), .Q(out1), .reset(reset));  // open: Qn, preset
  D_Flip_Flop d_ff_4 (.D(out7Segment[1]), .clk(clock), .Q(out2), .reset(reset));  // open: Qn, preset

  assign out7Segment[3:2] = {out2, out1};
endmodule

module gamePlayerManager (
  input  buttonInput,
  input  in1,
  input  in2,
  input  reset,
  input  clock,
  output endGame,
  output [3:0] out7Segment
);

  wire and_1_out, and_2_out, d_ff_1_q, d_ff_2_q, d_ff_3_q, not_1_out;

  D_Flip_Flop d_ff_1 (.D(buttonInput), .clk(clock), .Q(d_ff_1_q), .reset(reset));  // open: Qn, preset
  D_Flip_Flop d_ff_2 (.D(in1), .clk(clock), .Q(d_ff_2_q), .reset(reset));  // open: Qn, preset
  D_Flip_Flop d_ff_3 (.D(in2), .clk(clock), .Q(d_ff_3_q), .reset(reset));  // open: Qn, preset
  or or_1 (out7Segment[0], d_ff_1_q, d_ff_2_q);
  or or_2 (out7Segment[1], ~d_ff_1_q, d_ff_3_q);  // OR_Gate
  not not_1 (not_1_out, d_ff_1_q);
  and and_1 (and_1_out, d_ff_1_q, d_ff_2_q);
  or or_3 (endGame, and_1_out, and_2_out);
  and and_2 (and_2_out, not_1_out, d_ff_3_q);
  D_Flip_Flop d_ff_4 (.D(d_ff_2_q), .clk(clock), .Q(out7Segment[2]), .reset(reset));  // open: Qn, preset
  D_Flip_Flop d_ff_5 (.D(d_ff_3_q), .clk(clock), .Q(out7Segment[3]), .reset(reset));  // open: Qn, preset
endmodule

module gameCounter (
  input  reset,
  input  clock
);
endmodule

module gamerRandom (
  input  clock,
  input  reset,
  output random1,
  output random2
);

  wire d_ff_1_q, d_ff_2_q, d_ff_3_q, d_ff_4_q, d_ff_5_q, d_ff_6_q, d_ff_7_q, d_ff_8_q, xor_1_out, xor_2_out;

  xor xor_1 (xor_1_out, random1, d_ff_3_q);
  D_Flip_Flop d_ff_1 (.D(xor_1_out), .clk(clock), .Q(d_ff_1_q), .reset(reset));  // open: Qn, preset
  xor xor_2 (xor_2_out, random2, d_ff_4_q);
  D_Flip_Flop d_ff_2 (.D(xor_2_out), .clk(clock), .Q(d_ff_2_q), .preset(reset));  // open: Qn, reset
  D_Flip_Flop d_ff_3 (.D(d_ff_1_q), .clk(clock), .Q(d_ff_3_q), .reset(reset));  // open: Qn, preset
  D_Flip_Flop d_ff_4 (.D(d_ff_2_q), .clk(clock), .Q(d_ff_4_q), .reset(reset));  // open: Qn, preset
  D_Flip_Flop d_ff_5 (.D(d_ff_3_q), .clk(clock), .Q(d_ff_5_q), .reset(reset));  // open: Qn, preset
  D_Flip_Flop d_ff_6 (.D(d_ff_4_q), .clk(clock), .Q(d_ff_6_q), .reset(reset));  // open: Qn, preset
  D_Flip_Flop d_ff_7 (.D(d_ff_5_q), .clk(clock), .Q(d_ff_7_q), .reset(reset));  // open: Qn, preset
  D_Flip_Flop d_ff_8 (.D(d_ff_6_q), .clk(clock), .Q(d_ff_8_q), .reset(reset));  // open: Qn, preset
  D_Flip_Flop d_ff_9 (.D(d_ff_7_q), .clk(clock), .Q(random1), .preset(reset));  // open: Qn, reset
  D_Flip_Flop d_ff_10 (.D(d_ff_8_q), .clk(clock), .Q(random2), .reset(reset));  // open: Qn, preset
endmodule

module gameFilter (
  input  in1,
  input  in2,
  input  pIn1,
  input  pIn2,
  output out1,
  output out2
);

  wire not_1_out, not_2_out, not_3_out, not_4_out;

  not not_1 (not_1_out, in2);
  not not_2 (not_2_out, pIn2);
  not not_3 (not_3_out, in1);
  not not_4 (not_4_out, pIn1);
  and and_1 (out1, in1, not_1_out, not_2_out);
  and and_2 (out2, not_3_out, in2, not_4_out);
endmodule
