// Logisim project hours.circ as structural Verilog: 1 circuit, main circuit hour
module hour (
  output [29:0] segmentData
);

  wire clock_1_out, hourAdder0_60_1_carryout, hourAdder0_60_2_carryout;
  wire [2:0] hourAdder0_60_1_outbits2, hourAdder0_60_2_outbits2;
  wire [3:0] hourAdder0_60_1_outbits1, hourAdder0_60_2_outbits1;
  wire [4:0] hourAdder0_60_3_outbits;

  Clock clock_1 (.out(clock_1_out));
  adder0_60 hourAdder0_60_1 (
    .carryIn(1'b1), .enable(1'b1), .clock(clock_1_out), .outBits1(hourAdder0_60_1_outbits1),
    .outBits2(hourAdder0_60_1_outbits2), .carryOut(hourAdder0_60_1_carryout));
  adder0_60 hourAdder0_60_2 (
    .carryIn(hourAdder0_60_1_carryout), .enable(1'b1), .clock(clock_1_out),
    .outBits1(hourAdder0_60_2_outbits1), .outBits2(hourAdder0_60_2_outbits2),
    .carryOut(hourAdder0_60_2_carryout));
  adder0_23 hourAdder0_60_3 (
    .carryIn(hourAdder0_60_2_carryout), .enable(1'b1), .clock(clock_1_out), .outBits(hourAdder0_60_3_outbits));
  converterB24 hourConverterB24_1 (
    .inBits(hourAdder0_60_3_outbits), .outBits1(segmentData[24:20]), .outBits2(segmentData[29:25]));
  convert4_6 hourConvert4_6_1 (.inBits(hourAdder0_60_1_outbits1), .outBits(segmentData[4:0]));
  convert3_6 hourConvert3_6_1 (.inBits(hourAdder0_60_1_outbits2), .outBits(segmentData[9:5]));
  convert4_6 hourConvert4_6_2 (.inBits(hourAdder0_60_2_outbits1), .outBits(segmentData[14:10]));
  convert3_6 hourConvert3_6_2 (.inBits(hourAdder0_60_2_outbits2), .outBits(segmentData[19:15]));

  // Notes on the sheet:
  //   qu'on aura fixé avec time setting 
  //   ce sera envoyé ici avec un appui long sur action
  //   ici avec les set on donnera a chaque bit une valeur de départ 
endmodule
