// Logisim project main.circ as structural Verilog: 2 circuits, main circuit mainBis
module mainBis (
  input  buttonNext,
  input  buttonAction,
  output [3:0] testOut
);

  wire clock_1_out, decoder_1_out1, DipSwitch_1_sw8, finish, longActionPress, longNextPress,
       mainMainTransistion_1_d0, mainMainTransistion_1_d1, mainMainTransistion_1_d2,
       mainMainTransistion_1_d3, shortActionPress, shortNextPress;
  wire [5:0] mainDisplayManager_1_pointdataselected, mainDisplayManager_1_s0, mainDisplayManager_1_s1,
       mainDisplayManager_1_s2, mainDisplayManager_1_s3, mainDisplayManager_1_s4, mainDisplayManager_1_s5;
  wire [29:0] mainHour_1_segmentdata, mainTimeSetting_1_segmentdata;

  buttonManager mainButtonManager_1 (
    .buttonNext(buttonNext), .buttonAction(buttonAction), .longActionPress(longActionPress),
    .longNextPress(longNextPress), .shortActionPress(shortActionPress), .shortNextPress(shortNextPress));
  mainTransistion mainMainTransistion_1 (
    .C3(testOut[3]), .C2(testOut[2]), .C1(testOut[1]), .C0(testOut[0]), .LAP(longActionPress),
    .LNP(longNextPress), .SAP(shortActionPress), .SNP(shortNextPress), .FS(finish),
    .D3(mainMainTransistion_1_d3), .D2(mainMainTransistion_1_d2), .D1(mainMainTransistion_1_d1),
    .D0(mainMainTransistion_1_d0));
  Clock clock_1 (.out(clock_1_out));
  DipSwitch DipSwitch_1 (.sw8(DipSwitch_1_sw8));  // open: sw1, sw2, sw3, sw4, sw5, sw6, sw7
  D_Flip_Flop d_ff_1 (
    .D(mainMainTransistion_1_d3), .clk(clock_1_out), .Q(testOut[3]), .reset(DipSwitch_1_sw8));  // open: Qn, preset
  D_Flip_Flop d_ff_2 (
    .D(mainMainTransistion_1_d2), .clk(clock_1_out), .Q(testOut[2]), .reset(DipSwitch_1_sw8));  // open: Qn, preset
  D_Flip_Flop d_ff_3 (
    .D(mainMainTransistion_1_d1), .clk(clock_1_out), .Q(testOut[1]), .reset(DipSwitch_1_sw8));  // open: Qn, preset
  D_Flip_Flop d_ff_4 (
    .D(mainMainTransistion_1_d0), .clk(clock_1_out), .Q(testOut[0]), .reset(DipSwitch_1_sw8));  // open: Qn, preset
  Decoder #(.select(4), .enable("false")) decoder_1 (
    .out1(decoder_1_out1), .sel(testOut));  // open: out0, out2, out3, out4, out5, out6, out7, out8, out9, out10, out11, out12, out13, out14, out15
  hour mainHour_1 (.segmentData(mainHour_1_segmentdata));
  timeSetting mainTimeSetting_1 (
    .bentremettouta0(decoder_1_out1), .bnexton(shortNextPress), .baction(shortActionPress),
    .boutonprolongefin(longActionPress), .segmentData(mainTimeSetting_1_segmentdata), .onafini(finish));
  displayManager mainDisplayManager_1 (
    .segmentData1(mainHour_1_segmentdata), .segmentData2(mainTimeSetting_1_segmentdata), .state(testOut),
    .s0(mainDisplayManager_1_s0), .s1(mainDisplayManager_1_s1), .s2(mainDisplayManager_1_s2),
    .s3(mainDisplayManager_1_s3), .s4(mainDisplayManager_1_s4), .s5(mainDisplayManager_1_s5),
    .pointDataSelected(mainDisplayManager_1_pointdataselected));  // open: segmentData3, segmentData4, segmentData5, segmentData6, segmentData7, segmentData8, segmentData9
  displaySegment mainDisplaySegment_1 (
    .S0(mainDisplayManager_1_s0), .S1(mainDisplayManager_1_s1), .S2(mainDisplayManager_1_s2),
    .S3(mainDisplayManager_1_s3), .S4(mainDisplayManager_1_s4), .S5(mainDisplayManager_1_s5),
    .pointData(mainDisplayManager_1_pointdataselected));
endmodule

module mainTransistion (
  input  C3,
  input  C2,
  input  C1,
  input  C0,
  input  LAP,
  input  LNP,
  input  SAP,
  input  SNP,
  input  FS,
  output D3,
  output D2,
  output D1,
  output D0
);

  wire and_1_out, and_2_out, and_3_out, and_4_out, and_5_out, and_6_out, and_7_out, and_8_out, and_9_out,
       and_10_out, and_11_out, and_12_out, and_13_out, and_14_out, and_15_out, and_16_out, and_17_out,
       and_18_out, and_19_out, and_20_out, and_21_out, and_22_out, and_23_out, and_24_out, and_25_out,
       and_26_out, and_27_out, and_28_out, and_29_out, and_30_out, and_31_out, and_32_out, and_33_out,
       not_1_out, not_2_out, not_3_out, not_4_out, not_5_out, not_6_out, not_7_out, not_8_out, not_9_out,
       not_10_out, not_11_out, not_12_out, not_13_out, not_14_out, not_15_out, not_16_out, not_17_out,
       not_18_out, not_19_out, not_20_out, not_21_out, not_22_out, not_23_out, not_24_out, not_25_out,
       not_26_out, not_27_out, not_28_out, not_29_out, not_30_out, not_31_out, not_32_out, not_33_out,
       not_34_out, not_35_out, not_36_out, not_37_out, not_38_out, not_39_out, not_40_out, not_41_out,
       not_42_out, not_43_out, not_44_out, not_45_out, not_46_out, not_47_out;

  not not_1 (not_1_out, C0);
  not not_2 (not_2_out, LAP);
  not not_3 (not_3_out, LNP);
  not not_4 (not_4_out, SAP);
  not not_5 (not_5_out, FS);
  not not_6 (not_6_out, C2);
  not not_7 (not_7_out, C0);
  not not_8 (not_8_out, LAP);
  not not_9 (not_9_out, LNP);
  not not_10 (not_10_out, SAP);
  not not_11 (not_11_out, FS);
  not not_12 (not_12_out, C3);
  not not_13 (not_13_out, C2);
  not not_14 (not_14_out, C1);
  not not_15 (not_15_out, C0);
  not not_16 (not_16_out, LAP);
  not not_17 (not_17_out, LNP);
  not not_18 (not_18_out, SAP);
  not not_19 (not_19_out, FS);
  not not_20 (not_20_out, C1);
  not not_21 (not_21_out, C0);
  not not_22 (not_22_out, LAP);
  not not_23 (not_23_out, LNP);
  not not_24 (not_24_out, SAP);
  not not_25 (not_25_out, FS);
  not not_26 (not_26_out, SNP);
  not not_27 (not_27_out, C1);
  not not_28 (not_28_out, SNP);
  not not_29 (not_29_out, SNP);
  not not_30 (not_30_out, LAP);
  not not_31 (not_31_out, LNP);
  not not_32 (not_32_out, SAP);
  not not_33 (not_33_out, FS);
  not not_34 (not_34_out, C3);
  not not_35 (not_35_out, C2);
  not not_36 (not_36_out, LNP);
  not not_37 (not_37_out, SAP);
  not not_38 (not_38_out, SNP);
  not not_39 (not_39_out, FS);
  not not_40 (not_40_out, SNP);
  not not_41 (not_41_out, FS);
  not not_42 (not_42_out, C2);
  not not_43 (not_43_out, LNP);
  not not_44 (not_44_out, SAP);
  not not_45 (not_45_out, SNP);
  not not_46 (not_46_out, FS);
  not not_47 (not_47_out, C1);
  and and_1 (and_1_out, C2, C1, not_1_out, not_2_out, not_3_out, not_4_out, SNP, not_5_out);
  and and_2 (and_2_out, C3, not_26_out);
  and and_3 (and_3_out, C3, FS);
  and and_4 (and_4_out, C3, SAP);
  and and_5 (and_5_out, C3, LNP);
  and and_6 (and_6_out, C3, LAP);
  and and_7 (and_7_out, C3, C1);
  and and_8 (and_8_out, not_6_out, C1, not_7_out, not_8_out, not_9_out, not_10_out, SNP, not_11_out);
  and and_9 (and_9_out, C2, not_27_out);
  and and_10 (and_10_out, C2, not_28_out);
  and and_11 (and_11_out, C2, FS);
  and and_12 (and_12_out, C2, SAP);
  and and_13 (and_13_out, C2, LNP);
  and and_14 (and_14_out, C2, LAP);
  and and_15 (and_15_out, C2, C0);
  and and_16 (and_16_out, not_12_out, not_13_out, not_14_out, not_15_out, not_16_out, not_17_out, not_18_out, SNP, not_19_out);
  and and_17 (and_17_out, C1, not_29_out);
  and and_18 (and_18_out, C1, FS);
  and and_19 (and_19_out, C1, SAP);
  and and_20 (and_20_out, C1, LNP);
  and and_21 (and_21_out, C1, LAP);
  and and_22 (and_22_out, C1, C0);
  and and_23 (and_23_out, C2, C0, not_30_out, not_31_out, not_32_out, SNP, not_33_out);
  and and_24 (and_24_out, not_34_out, not_35_out, LAP, not_36_out, not_37_out, not_38_out, not_39_out);
  and and_25 (and_25_out, C0, not_40_out, not_41_out);
  and and_26 (and_26_out, not_42_out, C0, SNP);
  and and_27 (and_27_out, C0, SAP);
  and and_28 (and_28_out, C0, LNP);
  and and_29 (and_29_out, C0, LAP);
  and and_30 (and_30_out, C1, LAP, not_43_out, not_44_out, not_45_out, not_46_out);
  and and_31 (and_31_out, C1, C0, SNP);
  and and_32 (and_32_out, C2, not_20_out, not_21_out, not_22_out, not_23_out, not_24_out, SNP, not_25_out);
  and and_33 (and_33_out, C2, not_47_out, C0, FS);
  or or_1 (D3, and_1_out, and_2_out, and_3_out, and_4_out, and_5_out, and_6_out, and_7_out);
  or or_2 (D2, and_8_out, and_9_out, and_10_out, and_11_out, and_12_out, and_13_out, and_14_out, and_15_out);
  or or_3 (D1, and_16_out, and_17_out, and_18_out, and_19_out, and_20_out, and_21_out, and_22_out, and_23_out);
  or or_4 (D0, and_24_out, and_25_out, and_26_out, and_27_out, and_28_out, and_29_out, and_30_out, and_31_out, and_32_out, and_33_out);
endmodule
