// Logisim project music.circ as structural Verilog: 3 circuits, main circuit ancienNoteGenerator
module ancienNoteGenerator (
  input  [4:0] codeNote,
  output signalOutput
);

  wire A1_out, A1Sharp_out, A_out, ASharp_out, B1_out, B_out, C1_out, C1Sharp_out, C2_out, C_out, CSharp_out,
       D1_out, D1Sharp_out, D_out, DSharp_out, E1_out, E_out, F1_out, F1Sharp_out, F_out, FSharp_out, G1_out,
       G1Sharp_out, G_out, GSharp_out;

  Clock sysclk ();  // open: out
  Clock clk ();  // open: out
  Clock #(.highDuration(191), .lowDuration(191)) C (.out(C_out));
  Clock #(.highDuration(180), .lowDuration(180)) CSharp (.out(CSharp_out));
  Clock #(.highDuration(170), .lowDuration(170)) D (.out(D_out));
  Clock #(.highDuration(161), .lowDuration(161)) DSharp (.out(DSharp_out));
  Clock #(.highDuration(152), .lowDuration(152)) E (.out(E_out));
  Clock #(.highDuration(143), .lowDuration(143)) F (.out(F_out));
  Clock #(.highDuration(135), .lowDuration(135)) FSharp (.out(FSharp_out));
  Clock #(.highDuration(128), .lowDuration(128)) G (.out(G_out));
  Clock #(.highDuration(120), .lowDuration(120)) GSharp (.out(GSharp_out));
  Clock #(.highDuration(114), .lowDuration(114)) A (.out(A_out));
  Clock #(.highDuration(107), .lowDuration(107)) ASharp (.out(ASharp_out));
  Clock #(.highDuration(101), .lowDuration(101)) B (.out(B_out));
  Clock #(.highDuration(96), .lowDuration(96)) C1 (.out(C1_out));
  Clock #(.highDuration(90), .lowDuration(90)) C1Sharp (.out(C1Sharp_out));
  Clock #(.highDuration(85), .lowDuration(85)) D1 (.out(D1_out));
  Clock #(.highDuration(80), .lowDuration(80)) D1Sharp (.out(D1Sharp_out));
  Clock #(.highDuration(76), .lowDuration(76)) E1 (.out(E1_out));
  Clock #(.highDuration(72), .lowDuration(72)) F1 (.out(F1_out));
  Clock #(.highDuration(68), .lowDuration(68)) F1Sharp (.out(F1Sharp_out));
  Clock #(.highDuration(64), .lowDuration(64)) G1 (.out(G1_out));
  Clock #(.highDuration(60), .lowDuration(60)) G1Sharp (.out(G1Sharp_out));
  Clock #(.highDuration(57), .lowDuration(57)) A1 (.out(A1_out));
  Clock #(.highDuration(54), .lowDuration(54)) A1Sharp (.out(A1Sharp_out));
  Clock #(.highDuration(51), .lowDuration(51)) B1 (.out(B1_out));
  Clock #(.highDuration(48), .lowDuration(48)) C2 (.out(C2_out));
  Multiplexer #(.select(5), .enable("false")) multiplexer_1 (
    .in0(1'b0), .in1(C_out), .in2(CSharp_out), .in3(D_out), .in4(DSharp_out), .in5(E_out), .in6(F_out),
    .in7(FSharp_out), .in8(G_out), .in9(GSharp_out), .in10(A_out), .in11(ASharp_out), .in12(B_out),
    .in13(C1_out), .in14(C1Sharp_out), .in15(D1_out), .in16(D1Sharp_out), .in17(E1_out), .in18(F1_out),
    .in19(F1Sharp_out), .in20(G1_out), .in21(G1Sharp_out), .in22(A1_out), .in23(A1Sharp_out), .in24(B1_out),
    .in25(C2_out), .in26(1'b0), .in27(1'b0), .in28(1'b0), .in29(1'b0), .in30(1'b0), .in31(1'b0),
    .out(signalOutput), .sel(codeNote));

  // Notes on the sheet:
  //   For chronogram
endmodule

module harryPotterLogicTransistion (
  input  C3,
  input  C2,
  input  C1,
  input  C0,
  input  T2,
  input  T1,
  input  T0,
  output D3,
  output D2,
  output D1,
  output D0,
  output Reset
);

  wire and_1_out, and_2_out, and_3_out, and_4_out, and_5_out, and_6_out, and_7_out, and_8_out, and_9_out,
       and_10_out, and_11_out, and_12_out, and_13_out, and_14_out, and_15_out, and_16_out, and_17_out,
       and_18_out, and_19_out, and_20_out, and_21_out, and_22_out, and_23_out, and_24_out, and_25_out,
       and_26_out, and_27_out, and_28_out, and_29_out, and_30_out, and_31_out, and_32_out, and_33_out,
       and_34_out, and_35_out, and_36_out, and_37_out, and_38_out, and_39_out, and_40_out, and_41_out,
       and_42_out, and_43_out, and_44_out, and_45_out, and_46_out, and_47_out, and_48_out, and_49_out,
       and_50_out, and_51_out, and_52_out, and_53_out, and_54_out, and_55_out, and_56_out, not_1_out,
       not_2_out, not_3_out, not_4_out, not_5_out, not_6_out, not_7_out, not_8_out, not_9_out, not_10_out,
       not_11_out, not_12_out, not_13_out, not_14_out, not_15_out, not_16_out, not_17_out, not_18_out,
       not_19_out, not_20_out, not_21_out, not_22_out, not_23_out, not_24_out, not_25_out, not_26_out,
       not_27_out, not_28_out, not_29_out, not_30_out, not_31_out, not_32_out, not_33_out, not_34_out,
       not_35_out, not_36_out, not_37_out, not_38_out, not_39_out, not_40_out, not_41_out, not_42_out,
       not_43_out, not_44_out, not_45_out, not_46_out, not_47_out, not_48_out, not_49_out, not_50_out,
       not_51_out, not_52_out, not_53_out, not_54_out, not_55_out, not_56_out, not_57_out, not_58_out,
       not_59_out, not_60_out, not_61_out, not_62_out, not_63_out, not_64_out, not_65_out, not_66_out,
       not_67_out, not_68_out, not_69_out, not_70_out, not_71_out, not_72_out, not_73_out, not_74_out,
       not_75_out, not_76_out, not_77_out, not_78_out, not_79_out, not_80_out, not_81_out, not_82_out,
       not_83_out, not_84_out, not_85_out, not_86_out, not_87_out, not_88_out, not_89_out, not_90_out,
       not_91_out, not_92_out, not_93_out, not_94_out, not_95_out, not_96_out, not_97_out, not_98_out,
       not_99_out, not_100_out, not_101_out, not_102_out, not_103_out, not_104_out, not_105_out, not_106_out,
       not_107_out, not_108_out, not_109_out, not_110_out, not_111_out, not_112_out, not_113_out,
       not_114_out, not_115_out, not_116_out, not_117_out, not_118_out, not_119_out, not_120_out,
       not_121_out, not_122_out, not_123_out, not_124_out, not_125_out;

  not not_1 (not_1_out, T1);
  not not_2 (not_2_out, C2);
  not not_3 (not_3_out, C0);
  not not_4 (not_4_out, T2);
  not not_5 (not_5_out, T0);
  not not_6 (not_6_out, C3);
  not not_7 (not_7_out, T2);
  not not_8 (not_8_out, T0);
  not not_9 (not_9_out, C3);
  not not_10 (not_10_out, C1);
  not not_11 (not_11_out, C0);
  not not_12 (not_12_out, T2);
  not not_13 (not_13_out, T0);
  not not_14 (not_14_out, T1);
  not not_15 (not_15_out, T0);
  not not_16 (not_16_out, C3);
  not not_17 (not_17_out, C2);
  not not_18 (not_18_out, T2);
  not not_19 (not_19_out, C3);
  not not_20 (not_20_out, T1);
  not not_21 (not_21_out, T0);
  not not_22 (not_22_out, C0);
  not not_23 (not_23_out, T2);
  not not_24 (not_24_out, T1);
  not not_25 (not_25_out, C2);
  not not_26 (not_26_out, C3);
  not not_27 (not_27_out, T2);
  not not_28 (not_28_out, T0);
  not not_29 (not_29_out, T2);
  not not_30 (not_30_out, T0);
  not not_31 (not_31_out, C2);
  not not_32 (not_32_out, T2);
  not not_33 (not_33_out, T1);
  not not_34 (not_34_out, C3);
  not not_35 (not_35_out, C2);
  not not_36 (not_36_out, C1);
  not not_37 (not_37_out, T2);
  not not_38 (not_38_out, T0);
  not not_39 (not_39_out, C3);
  not not_40 (not_40_out, C2);
  not not_41 (not_41_out, T1);
  not not_42 (not_42_out, C3);
  not not_43 (not_43_out, C1);
  not not_44 (not_44_out, T1);
  not not_45 (not_45_out, T2);
  not not_46 (not_46_out, T1);
  not not_47 (not_47_out, T0);
  not not_48 (not_48_out, C2);
  not not_49 (not_49_out, C1);
  not not_50 (not_50_out, C3);
  not not_51 (not_51_out, C2);
  not not_52 (not_52_out, T2);
  not not_53 (not_53_out, T1);
  not not_54 (not_54_out, C2);
  not not_55 (not_55_out, C3);
  not not_56 (not_56_out, C1);
  not not_57 (not_57_out, T1);
  not not_58 (not_58_out, T0);
  not not_59 (not_59_out, T2);
  not not_60 (not_60_out, C3);
  not not_61 (not_61_out, C0);
  not not_62 (not_62_out, T1);
  not not_63 (not_63_out, T0);
  not not_64 (not_64_out, C2);
  not not_65 (not_65_out, C1);
  not not_66 (not_66_out, T2);
  not not_67 (not_67_out, C1);
  not not_68 (not_68_out, T0);
  not not_69 (not_69_out, C2);
  not not_70 (not_70_out, T2);
  not not_71 (not_71_out, T0);
  not not_72 (not_72_out, C1);
  not not_73 (not_73_out, T2);
  not not_74 (not_74_out, T0);
  not not_75 (not_75_out, C3);
  not not_76 (not_76_out, C2);
  not not_77 (not_77_out, C1);
  not not_78 (not_78_out, C0);
  not not_79 (not_79_out, T2);
  not not_80 (not_80_out, T0);
  not not_81 (not_81_out, C3);
  not not_82 (not_82_out, C2);
  not not_83 (not_83_out, C1);
  not not_84 (not_84_out, T2);
  not not_85 (not_85_out, C3);
  not not_86 (not_86_out, C2);
  not not_87 (not_87_out, C0);
  not not_88 (not_88_out, T2);
  not not_89 (not_89_out, T1);
  not not_90 (not_90_out, C3);
  not not_91 (not_91_out, C2);
  not not_92 (not_92_out, T2);
  not not_93 (not_93_out, T0);
  not not_94 (not_94_out, C3);
  not not_95 (not_95_out, C1);
  not not_96 (not_96_out, C0);
  not not_97 (not_97_out, T1);
  not not_98 (not_98_out, T0);
  not not_99 (not_99_out, C3);
  not not_100 (not_100_out, C1);
  not not_101 (not_101_out, T2);
  not not_102 (not_102_out, T0);
  not not_103 (not_103_out, C3);
  not not_104 (not_104_out, T1);
  not not_105 (not_105_out, C2);
  not not_106 (not_106_out, C1);
  not not_107 (not_107_out, C0);
  not not_108 (not_108_out, T2);
  not not_109 (not_109_out, C2);
  not not_110 (not_110_out, C1);
  not not_111 (not_111_out, T2);
  not not_112 (not_112_out, T1);
  not not_113 (not_113_out, C2);
  not not_114 (not_114_out, C0);
  not not_115 (not_115_out, T2);
  not not_116 (not_116_out, T0);
  not not_117 (not_117_out, C2);
  not not_118 (not_118_out, T1);
  not not_119 (not_119_out, T0);
  not not_120 (not_120_out, C1);
  not not_121 (not_121_out, C0);
  not not_122 (not_122_out, T2);
  not not_123 (not_123_out, T0);
  not not_124 (not_124_out, C1);
  not not_125 (not_125_out, T1);
  and and_1 (and_1_out, C2, C1, C0, T2, not_1_out, T0);
  and and_2 (and_2_out, C3, not_2_out);
  and and_3 (and_3_out, C3, not_3_out);
  and and_4 (and_4_out, C3, not_4_out);
  and and_5 (and_5_out, C3, not_5_out);
  and and_6 (and_6_out, C3, T1);
  and and_7 (and_7_out, not_6_out, C1, C0, not_7_out, T1, not_8_out);
  and and_8 (and_8_out, not_9_out, C2, not_10_out);
  and and_9 (and_9_out, C2, not_11_out);
  and and_10 (and_10_out, C2, not_12_out);
  and and_11 (and_11_out, C2, not_13_out);
  and and_12 (and_12_out, C2, T1);
  and and_13 (and_13_out, C3, C1, C0, T2, not_14_out, not_15_out);
  and and_14 (and_14_out, C3, C2, C1);
  and and_15 (and_15_out, not_16_out, not_17_out, C0, not_18_out, T1, T0);
  and and_16 (and_16_out, not_19_out, C1, not_20_out, not_21_out);
  and and_17 (and_17_out, C1, not_22_out);
  and and_18 (and_18_out, C1, not_23_out, not_24_out);
  and and_19 (and_19_out, not_25_out, C1, T0);
  and and_20 (and_20_out, C1, T2, T1);
  and and_21 (and_21_out, not_26_out, C2, C0, not_27_out, T1, not_28_out);
  and and_22 (and_22_out, C2, C1, not_29_out);
  and and_23 (and_23_out, C2, C1, not_30_out);
  and and_24 (and_24_out, C3, not_31_out, C0, not_32_out, not_33_out, T0);
  and and_25 (and_25_out, C3, C1, T1);
  and and_26 (and_26_out, C3, C2, C1);
  and and_27 (and_27_out, not_34_out, not_35_out, not_36_out, not_37_out, T1, not_38_out);
  and and_28 (and_28_out, not_39_out, not_40_out, C0, not_41_out);
  and and_29 (and_29_out, not_42_out, not_43_out, C0, not_44_out);
  and and_30 (and_30_out, C0, not_45_out, not_46_out, not_47_out);
  and and_31 (and_31_out, not_48_out, not_49_out, C0, T2);
  and and_32 (and_32_out, C0, T2, T1);
  and and_33 (and_33_out, not_50_out, not_51_out, C1, not_52_out, not_53_out, T0);
  and and_34 (and_34_out, not_54_out, C1, C0, T0);
  and and_35 (and_35_out, not_55_out, C2, not_56_out, T2, not_57_out, not_58_out);
  and and_36 (and_36_out, C2, C0, not_59_out, T0);
  and and_37 (and_37_out, not_60_out, C2, C1, not_61_out, T2, not_62_out, T0);
  and and_38 (and_38_out, C2, C1, C0, not_63_out);
  and and_39 (and_39_out, C3, not_64_out, not_65_out, not_66_out, T1, T0);
  and and_40 (and_40_out, C3, not_67_out, C0, not_68_out);
  and and_41 (and_41_out, C3, not_69_out, C1, not_70_out, T1, not_71_out);
  and and_42 (and_42_out, C3, C1, C0, T0);
  and and_43 (and_43_out, C3, C2, not_72_out, not_73_out, T1, not_74_out);
  and and_44 (and_44_out, not_75_out, not_76_out, not_77_out, not_78_out, not_79_out, T1, not_80_out);
  and and_45 (and_45_out, not_81_out, not_82_out, not_83_out, C0, not_84_out, T1, T0);
  and and_46 (and_46_out, not_85_out, not_86_out, C1, not_87_out, not_88_out, not_89_out, T0);
  and and_47 (and_47_out, not_90_out, not_91_out, C1, C0, not_92_out, T1, not_93_out);
  and and_48 (and_48_out, not_94_out, C2, not_95_out, not_96_out, T2, not_97_out, not_98_out);
  and and_49 (and_49_out, not_99_out, C2, not_100_out, C0, not_101_out, T1, not_102_out);
  and and_50 (and_50_out, not_103_out, C2, C1, T2, not_104_out, T0);
  and and_51 (and_51_out, C3, not_105_out, not_106_out, not_107_out, not_108_out, T1, T0);
  and and_52 (and_52_out, C3, not_109_out, not_110_out, C0, not_111_out, not_112_out, T0);
  and and_53 (and_53_out, C3, not_113_out, C1, not_114_out, not_115_out, T1, not_116_out);
  and and_54 (and_54_out, C3, not_117_out, C1, C0, T2, not_118_out, not_119_out);
  and and_55 (and_55_out, C3, C2, not_120_out, not_121_out, not_122_out, T1, not_123_out);
  and and_56 (and_56_out, C3, C2, not_124_out, C0, T2, not_125_out, T0);
  or or_1 (D3, and_1_out, and_2_out, and_3_out, and_4_out, and_5_out, and_6_out);
  or or_2 (D2, and_7_out, and_8_out, and_9_out, and_10_out, and_11_out, and_12_out, and_13_out, and_14_out);
  or or_3 (D1, and_15_out, and_16_out, and_17_out, and_18_out, and_19_out, and_20_out, and_21_out, and_22_out, and_23_out, and_24_out, and_25_out, and_26_out);
  or or_4 (Reset, and_44_out, and_45_out, and_46_out, and_47_out, and_48_out, and_49_out, and_50_out, and_51_out, and_52_out, and_53_out, and_54_out, and_55_out, and_56_out);
  or or_5 (D0, and_27_out, and_28_out, and_29_out, and_30_out, and_31_out, and_32_out, and_33_out, and_34_out, and_35_out, and_36_out, and_37_out, and_38_out, and_39_out, and_40_out, and_41_out, and_42_out, and_43_out);
endmodule

module harryPotterFSM (
  input  Input_1,
  output signalOutput,
  output ground
);

  wire and_1_out, clock_1_out, clock_2_out, clock_3_out, clock_4_out, clock_5_out, clock_6_out, clock_7_out,
       clock_8_out, clock_9_out, clock_10_out, clock_11_out, clock_12_out, clock_13_out, clock_14_out,
       clock_15_out, harryPotterFSMHarryPotterLogicTransistion_1_d0,
       harryPotterFSMHarryPotterLogicTransistion_1_d1, harryPotterFSMHarryPotterLogicTransistion_1_d2,
       harryPotterFSMHarryPotterLogicTransistion_1_d3, harryPotterFSMHarryPotterLogicTransistion_1_reset,
       not_1_out;
  wire [2:0] harryPotterFSMThreeBitsCounter_1_output_bus_1;
  wire [3:0] d_ff_4_q;

  Clock #(.highDuration(20000), .lowDuration(20000)) clock_1 (.out(clock_1_out));
  threeBitsCounter harryPotterFSMThreeBitsCounter_1 (
    .enable(1'b1), .reset(and_1_out), .clock(clock_1_out), .stopEnd(1'b0),
    .Output_bus_1(harryPotterFSMThreeBitsCounter_1_output_bus_1));  // open: carryOutOrStopped
  and and_1 (and_1_out, harryPotterFSMHarryPotterLogicTransistion_1_reset, not_1_out);
  not not_1 (not_1_out, clock_1_out);
  harryPotterLogicTransistion harryPotterFSMHarryPotterLogicTransistion_1 (
    .C3(d_ff_4_q[3]), .C2(d_ff_4_q[2]), .C1(d_ff_4_q[1]), .C0(d_ff_4_q[0]),
    .T2(harryPotterFSMThreeBitsCounter_1_output_bus_1[2]),
    .T1(harryPotterFSMThreeBitsCounter_1_output_bus_1[1]),
    .T0(harryPotterFSMThreeBitsCounter_1_output_bus_1[0]),
    .D3(harryPotterFSMHarryPotterLogicTransistion_1_d3), .D2(harryPotterFSMHarryPotterLogicTransistion_1_d2),
    .D1(harryPotterFSMHarryPotterLogicTransistion_1_d1), .D0(harryPotterFSMHarryPotterLogicTransistion_1_d0),
    .Reset(harryPotterFSMHarryPotterLogicTransistion_1_reset));
  D_Flip_Flop d_ff_1 (
    .D(harryPotterFSMHarryPotterLogicTransistion_1_d3), .clk(not_1_out), .Q(d_ff_4_q[3]), .reset(Input_1));  // open: Qn, preset
  D_Flip_Flop d_ff_2 (
    .D(harryPotterFSMHarryPotterLogicTransistion_1_d2), .clk(not_1_out), .Q(d_ff_4_q[2]), .reset(Input_1));  // open: Qn, preset
  D_Flip_Flop d_ff_3 (
    .D(harryPotterFSMHarryPotterLogicTransistion_1_d1), .clk(not_1_out), .Q(d_ff_4_q[1]), .reset(Input_1));  // open: Qn, preset
  D_Flip_Flop d_ff_4 (
    .D(harryPotterFSMHarryPotterLogicTransistion_1_d0), .clk(not_1_out), .Q(d_ff_4_q[0]), .reset(Input_1));  // open: Qn, preset
  Clock #(.highDuration(162), .lowDuration(162)) clock_2 (.out(clock_2_out));
  Clock #(.highDuration(121), .lowDuration(121)) clock_3 (.out(clock_3_out));
  Clock #(.highDuration(102), .lowDuration(102)) clock_4 (.out(clock_4_out));
  Clock #(.highDuration(115), .lowDuration(115)) clock_5 (.out(clock_5_out));
  Clock #(.highDuration(121), .lowDuration(121)) clock_6 (.out(clock_6_out));
  Clock #(.highDuration(81), .lowDuration(81)) clock_7 (.out(clock_7_out));
  Clock #(.highDuration(91), .lowDuration(91)) clock_8 (.out(clock_8_out));
  Clock #(.highDuration(108), .lowDuration(108)) clock_9 (.out(clock_9_out));
  Clock #(.highDuration(121), .lowDuration(121)) clock_10 (.out(clock_10_out));
  Clock #(.highDuration(102), .lowDuration(102)) clock_11 (.out(clock_11_out));
  Clock #(.highDuration(115), .lowDuration(115)) clock_12 (.out(clock_12_out));
  Clock #(.highDuration(129), .lowDuration(129)) clock_13 (.out(clock_13_out));
  Clock #(.highDuration(115), .lowDuration(115)) clock_14 (.out(clock_14_out));
  Clock #(.highDuration(162), .lowDuration(162)) clock_15 (.out(clock_15_out));
  Multiplexer #(.select(4), .enable("false")) multiplexer_1 (
    .in0(clock_2_out), .in1(clock_3_out), .in2(clock_4_out), .in3(clock_5_out), .in4(clock_6_out),
    .in5(clock_7_out), .in6(clock_8_out), .in7(clock_9_out), .in8(clock_10_out), .in9(clock_11_out),
    .in10(clock_12_out), .in11(clock_13_out), .in12(clock_14_out), .in13(clock_15_out), .in14(1'b0),
    .in15(1'b0), .out(signalOutput), .sel(d_ff_4_q));

  assign ground = 1'b0;
endmodule
