// Logisim project timeSettings.circ as structural Verilog: 2 circuits, main circuit timeSetting
module timeSetting (
  input  bentremettouta0,
  input  bnexton,
  input  baction,
  input  boutonprolongefin,
  output [29:0] segmentData,
  output onafini
);

  wire a1, a2, a3, a4, and_1_out, and_2_out, and_3_out, and_4_out, ao, clock_1_out, clock_2_out;
  wire [2:0] timeSettingAdder0_5_1_outbits, timeSettingAdder0_60_1_outbits2, timeSettingAdder0_60_2_outbits2;
  wire [3:0] timeSettingAdder0_60_1_outbits1, timeSettingAdder0_60_2_outbits1;
  wire [4:0] timeSettingAdder0_23_1_outbits;

  Clock clock_1 (.out(clock_1_out));
  adder0_5 timeSettingAdder0_5_1 (
    .carryIn(baction), .enable(1'b1), .reset(1'b0), .clock(clock_1_out),
    .outBits(timeSettingAdder0_5_1_outbits));  // open: carryOut
  segmentSelected timeSettingSegmentSelected_1 (
    .b2(timeSettingAdder0_5_1_outbits[2]), .b1(timeSettingAdder0_5_1_outbits[1]),
    .b0(timeSettingAdder0_5_1_outbits[0]), .a0(ao), .a1(a1), .a2(a2), .a3(a3), .a4(a4));
  and and_1 (and_1_out, a4, bnexton);
  and and_2 (and_2_out, ao, bnexton);
  and and_3 (and_3_out, a1, bnexton);
  and and_4 (and_4_out, a2, bnexton);
  Clock clock_2 (.out(clock_2_out));
  adder0_60 timeSettingAdder0_60_1 (
    .carryIn(1'b1), .enable(and_2_out), .clock(clock_2_out), .outBits1(timeSettingAdder0_60_1_outbits1),
    .outBits2(timeSettingAdder0_60_1_outbits2));  // open: carryOut
  adder0_60 timeSettingAdder0_60_2 (
    .carryIn(1'b1), .enable(and_3_out), .clock(clock_2_out), .outBits1(timeSettingAdder0_60_2_outbits1),
    .outBits2(timeSettingAdder0_60_2_outbits2));  // open: carryOut
  adder0_23 timeSettingAdder0_23_1 (
    .carryIn(1'b1), .enable(and_4_out), .clock(clock_2_out), .outBits(timeSettingAdder0_23_1_outbits));
  convert4_6 timeSettingAdderConvert4_6_1 (.inBits(timeSettingAdder0_60_1_outbits1), .outBits(segmentData[4:0]));
  convert3_6 timeSettingAdderConvert3_6_1 (.inBits(timeSettingAdder0_60_1_outbits2), .outBits(segmentData[9:5]));
  convert4_6 timeSettingAdderConvert4_6_2 (.inBits(timeSettingAdder0_60_2_outbits1), .outBits(segmentData[14:10]));
  convert3_6 timeSettingAdderConvert3_6_2 (.inBits(timeSettingAdder0_60_2_outbits2), .outBits(segmentData[19:15]));
  converterB24 timeSettingConverterB24_1 (
    .inBits(timeSettingAdder0_23_1_outbits), .outBits1(segmentData[24:20]), .outBits2(segmentData[29:25]));

  assign onafini = boutonprolongefin;

  // Other names for the same wires on the sheet: b0 = bentremettouta0; bnext = bnexton
endmodule

module segmentSelected (
  input  b2,
  input  b1,
  input  b0,
  output a0,
  output a1,
  output a2,
  output a3,
  output a4
);

  wire and_1_out, and_2_out, and_3_out, and_4_out, and_5_out, and_6_out, not_1_out, not_2_out, not_3_out,
       not_4_out;

  not not_1 (not_1_out, b2);
  not not_2 (not_2_out, b1);
  not not_3 (not_3_out, b0);
  and and_1 (and_1_out, b1, b0);
  and and_2 (and_2_out, b2, b1);
  not not_4 (not_4_out, b0);
  and and_3 (and_3_out, b2, b0);
  and and_4 (and_4_out, b2, b1);
  and and_5 (and_5_out, not_1_out, not_2_out, b0);
  and and_6 (and_6_out, b2, b1);
  and and_7 (a1, b1, not_3_out);
  or or_1 (a2, and_1_out, and_2_out);
  and and_8 (a3, b2, not_4_out);
  or or_2 (a4, and_3_out, and_4_out);
  or or_3 (a0, and_5_out, and_6_out);
endmodule
