// Logisim project tools.circ as structural Verilog: 6 circuits, main circuit levelDetect
module levelDetect (
  input  signalInput,
  input  clockSignal,
  output levelUp,
  output levelDown
);

  wire d_ff_1_q, d_ff_2_q, xor_1_out;

  D_Flip_Flop d_ff_1 (.D(signalInput), .clk(clockSignal), .Q(d_ff_1_q));  // open: Qn, preset, reset
  D_Flip_Flop d_ff_2 (.D(d_ff_1_q), .clk(clockSignal), .Q(d_ff_2_q));  // open: Qn, preset, reset
  xor xor_1 (xor_1_out, d_ff_1_q, d_ff_2_q);
  and and_1 (levelUp, xor_1_out, signalInput);
  and and_2 (levelDown, xor_1_out, ~signalInput);  // AND_Gate
endmodule

module fiveBitsDFF (
  input  [4:0] inputBits,
  input  reset,
  input  clock,
  output [4:0] outputBits
);

  D_Flip_Flop d_ff_1 (.D(inputBits[0]), .clk(clock), .Q(outputBits[0]), .reset(reset));  // open: Qn, preset
  D_Flip_Flop d_ff_2 (.D(inputBits[1]), .clk(clock), .Q(outputBits[1]), .reset(reset));  // open: Qn, preset
  D_Flip_Flop d_ff_3 (.D(inputBits[2]), .clk(clock), .Q(outputBits[2]), .reset(reset));  // open: Qn, preset
  D_Flip_Flop d_ff_4 (.D(inputBits[3]), .clk(clock), .Q(outputBits[3]), .reset(reset));  // open: Qn, preset
  D_Flip_Flop d_ff_5 (.D(inputBits[4]), .clk(clock), .Q(outputBits[4]), .reset(reset));  // open: Qn, preset
endmodule

module converterB24 (
  input  [4:0] inBits,
  output [4:0] outBits1,
  output [4:0] outBits2
);

  wire and_2_out, and_3_out, and_4_out, and_5_out, and_6_out, and_7_out, and_8_out, and_9_out, and_10_out,
       and_11_out, and_12_out, and_13_out, not_1_out, not_2_out, not_3_out, not_4_out, not_5_out, not_6_out,
       not_7_out, not_8_out, not_9_out, not_10_out, not_11_out, not_12_out, not_13_out, not_14_out,
       not_15_out;

  and and_1 (outBits1[1], inBits[4], inBits[2]);
  not not_1 (not_1_out, inBits[2]);
  not not_2 (not_2_out, inBits[2]);
  not not_3 (not_3_out, inBits[1]);
  not not_4 (not_4_out, inBits[2]);
  not not_5 (not_5_out, inBits[4]);
  not not_6 (not_6_out, inBits[3]);
  not not_7 (not_7_out, inBits[4]);
  not not_8 (not_8_out, inBits[2]);
  not not_9 (not_9_out, inBits[1]);
  not not_10 (not_10_out, inBits[4]);
  not not_11 (not_11_out, inBits[3]);
  not not_12 (not_12_out, inBits[3]);
  not not_13 (not_13_out, inBits[1]);
  not not_14 (not_14_out, inBits[2]);
  not not_15 (not_15_out, inBits[1]);
  and and_2 (and_2_out, inBits[3], inBits[1]);
  and and_3 (and_3_out, inBits[3], inBits[2]);
  and and_4 (and_4_out, inBits[4], not_1_out);
  and and_5 (and_5_out, inBits[3], not_2_out, not_3_out);
  and and_6 (and_6_out, inBits[4], not_4_out, inBits[1]);
  and and_7 (and_7_out, not_5_out, not_6_out, inBits[2]);
  and and_8 (and_8_out, not_7_out, inBits[2], inBits[1]);
  and and_9 (and_9_out, inBits[4], not_8_out, not_9_out);
  and and_10 (and_10_out, not_10_out, not_11_out, inBits[1]);
  and and_11 (and_11_out, not_12_out, inBits[2], inBits[1]);
  and and_12 (and_12_out, inBits[3], inBits[2], not_13_out);
  and and_13 (and_13_out, inBits[4], not_14_out, not_15_out);
  or or_1 (outBits1[0], and_2_out, and_3_out, and_4_out);
  or or_2 (outBits2[3], and_5_out, and_6_out);
  or or_3 (outBits2[2], and_7_out, and_8_out, and_9_out);
  or or_4 (outBits2[1], and_10_out, and_11_out, and_12_out, and_13_out);

  assign outBits1[4:2] = 3'b100;
  assign {outBits2[4], outBits2[0]} = {1'b0, inBits[0]};
endmodule

module comparator5Bits (
  input  [5:0] in_1,
  input  [5:0] in_2,
  output i
);

  wire xnor_1_out, xnor_2_out, xnor_3_out, xnor_4_out, xnor_5_out;

  xnor xnor_1 (xnor_1_out, in_1[1], in_2[1]);
  xnor xnor_2 (xnor_2_out, in_1[2], in_2[2]);
  xnor xnor_3 (xnor_3_out, in_1[3], in_2[3]);
  xnor xnor_4 (xnor_4_out, in_1[4], in_2[4]);
  xnor xnor_5 (xnor_5_out, in_1[5], in_2[5]);
  and and_1 (i, xnor_1_out, xnor_2_out, xnor_3_out, xnor_4_out, xnor_5_out);
endmodule

module convert4_6 (
  input  [3:0] inBits,
  output [4:0] outBits
);


  assign outBits = {1'b0, inBits};
endmodule

module convert3_6 (
  input  [2:0] inBits,
  output [4:0] outBits
);


  assign outBits = {2'b00, inBits};
endmodule
