// Logisim project projectWatch.circ as structural Verilog: 36 circuits, main circuit timeSetting_main
module main_main (
  input  b0,
  input  b1,
  output sound,
  output ground,
  output [5:0] stateOut
);

  wire alarmPoint, alarmSignal, clock_1_out, coutdownSignal, decoder_1_out1, decoder_1_out3, decoder_1_out5,
       decoder_1_out7, decoder_1_out8, decoder_2_out0, decoder_2_out1, decoder_2_out2, decoder_2_out3,
       decoder_2_out6, decoder_2_out7, enableTimeZoneChange, finishSetAlarm, finishSetCountDown,
       finishSetHour, longActionPress, longNextPress, mainTransistion_1_d0, mainTransistion_1_d1,
       mainTransistion_1_d2, mainTransistion_1_d3, or_1_out, or_5_out, or_6_out, playMusicMario, reset,
       shortActionPress, shortNextPress;
  wire [2:0] capitalSelected;
  wire [3:0] d_ff_4_q;
  wire [5:0] displayManager_1_pointdataselected, game_1_bits, timeSetting_main_1_outbits,
       timeSetting_main_2_outbits, timeSetting_main_3_outbits;
  wire [6:0] displayManager_1_s0, displayManager_1_s1, displayManager_1_s2, displayManager_1_s3,
       displayManager_1_s4, displayManager_1_s5;
  wire [29:0] alarm_1_alarmmemorised, chronometre_1_segmentout, countdown_1_outdata, game_1_outdata,
       hour_main_1_segementdata, timeSetting_main_1_dataout, timeSetting_main_2_dataout,
       timeSetting_main_3_dataout, timeZoneChange_1_modifiedhour, timeZoneChange_goback_1_outhours,
       timeZoneChange_selector_1_capital;

  or or_1 (or_1_out, finishSetHour, finishSetAlarm, finishSetCountDown);
  buttonManager_main buttonManager_1 (
    .buttonNext(b0), .buttonAction(b1), .reset(reset), .longActionPress(longActionPress),
    .longNextPress(longNextPress), .shortActionPress(shortActionPress), .shortNextPress(shortNextPress),
    .resetButton(reset));
  main_mainTransistion mainTransistion_1 (
    .C3(d_ff_4_q[3]), .C2(d_ff_4_q[2]), .C1(d_ff_4_q[1]), .C0(d_ff_4_q[0]), .LAP(longActionPress),
    .LNP(longNextPress), .SAP(shortActionPress), .SNP(shortNextPress), .FS(or_1_out),
    .D3(mainTransistion_1_d3), .D2(mainTransistion_1_d2), .D1(mainTransistion_1_d1), .D0(mainTransistion_1_d0));
  Clock clock_1 (.out(clock_1_out));
  D_Flip_Flop d_ff_1 (.D(mainTransistion_1_d3), .clk(clock_1_out), .Q(d_ff_4_q[3]), .reset(reset));  // open: Qn, preset
  D_Flip_Flop d_ff_2 (.D(mainTransistion_1_d2), .clk(clock_1_out), .Q(d_ff_4_q[2]), .reset(reset));  // open: Qn, preset
  D_Flip_Flop d_ff_3 (.D(mainTransistion_1_d1), .clk(clock_1_out), .Q(d_ff_4_q[1]), .reset(reset));  // open: Qn, preset
  D_Flip_Flop d_ff_4 (.D(mainTransistion_1_d0), .clk(clock_1_out), .Q(d_ff_4_q[0]), .reset(reset));  // open: Qn, preset
  Decoder #(.select(4), .enable("false")) decoder_1 (
    .out1(decoder_1_out1), .out3(decoder_1_out3), .out4(enableTimeZoneChange), .out5(decoder_1_out5),
    .out7(decoder_1_out7), .out8(decoder_1_out8), .sel(d_ff_4_q));  // open: out0, out2, out6, out9, out10, out11, out12, out13, out14, out15
  Decoder #(.select(4), .enable("false")) decoder_2 (
    .out0(decoder_2_out0), .out1(decoder_2_out1), .out2(decoder_2_out2), .out3(decoder_2_out3),
    .out4(stateOut[2]), .out5(stateOut[3]), .out6(decoder_2_out6), .out7(decoder_2_out7), .out8(stateOut[5]),
    .sel(d_ff_4_q));  // open: out9, out10, out11, out12, out13, out14, out15
  timeZoneChange_goback timeZoneChange_goback_1 (
    .setHour(timeSetting_main_1_dataout), .capitalState(capitalSelected),
    .outHours(timeZoneChange_goback_1_outhours));
  or or_2 (stateOut[0], decoder_2_out0, decoder_2_out1);
  or or_3 (stateOut[1], decoder_2_out2, decoder_2_out3);
  or or_4 (stateOut[4], decoder_2_out6, decoder_2_out7);
  hour_main hour_main_1 (
    .enable(1'b1), .dataSet(timeZoneChange_goback_1_outhours), .setSignal(finishSetHour), .reset(reset),
    .segementData(hour_main_1_segementdata));
  timeSetting_main timeSetting_main_1 (
    .enable(decoder_1_out1), .shortNextPress(shortNextPress), .shortActionPress(shortActionPress),
    .reset(reset), .dataOut(timeSetting_main_1_dataout), .finish(finishSetHour),
    .outBits(timeSetting_main_1_outbits));
  alarm_main alarm_1 (
    .alarmSet(timeSetting_main_2_dataout), .actualHour(timeZoneChange_1_modifiedhour),
    .setSignal(finishSetAlarm), .longActionPress(longNextPress), .reset(reset),
    .alarmMemorised(alarm_1_alarmmemorised), .alarmSignal(alarmSignal), .alarmPoint(alarmPoint));
  timeSetting_main timeSetting_main_2 (
    .enable(decoder_1_out3), .shortNextPress(shortNextPress), .shortActionPress(shortActionPress),
    .reset(reset), .dataOut(timeSetting_main_2_dataout), .finish(finishSetAlarm),
    .outBits(timeSetting_main_2_outbits));
  chronometre_main chronometre_1 (
    .enable(decoder_1_out5), .shortAction(shortActionPress), .longAction(longActionPress), .reset(reset),
    .segmentOut(chronometre_1_segmentout));
  countdown_main countdown_1 (
    .enable(1'b1), .shortActionPress(shortActionPress), .inData(timeSetting_main_3_dataout),
    .setSignal(finishSetCountDown), .reset(reset), .musicPlay(coutdownSignal), .outData(countdown_1_outdata));
  timeSetting_main timeSetting_main_3 (
    .enable(decoder_1_out7), .shortNextPress(shortNextPress), .shortActionPress(shortActionPress),
    .reset(reset), .dataOut(timeSetting_main_3_dataout), .finish(finishSetCountDown),
    .outBits(timeSetting_main_3_outbits));
  game_main game_1 (
    .enable(decoder_1_out8), .buttonInput(b1), .reset(reset), .bits(game_1_bits), .outData(game_1_outdata),
    .playMario(playMusicMario));
  or or_5 (or_5_out, alarmSignal, coutdownSignal);
  timeZoneChange_selector timeZoneChange_selector_1 (
    .enable2(enableTimeZoneChange), .button2(shortActionPress), .reset2(reset),
    .capitalSelected(capitalSelected), .capital(timeZoneChange_selector_1_capital));
  timeZoneChange_gofront timeZoneChange_1 (
    .currentHour(hour_main_1_segementdata), .CapitalSelected(capitalSelected),
    .modifiedHour(timeZoneChange_1_modifiedhour));
  musique_main harryPotterFSM_1 (
    .playHarry(or_5_out), .playMario(playMusicMario), .reset(reset), .signalOutput(sound), .ground(ground));
  or or_6 (or_6_out, alarmSignal, coutdownSignal);
  display_displaySegment displaySegment_1 (
    .S0(displayManager_1_s0), .S1(displayManager_1_s1), .S2(displayManager_1_s2), .S3(displayManager_1_s3),
    .S4(displayManager_1_s4), .S5(displayManager_1_s5), .pointData(displayManager_1_pointdataselected));
  display_displayManager displayManager_1 (
    .segmentData1(timeZoneChange_1_modifiedhour), .bitSelectedSegment1({6{1'b0}}),
    .segmentData2(timeSetting_main_1_dataout), .bitSelectedSegment2(timeSetting_main_1_outbits),
    .segmentData3(alarm_1_alarmmemorised), .bitSelectedSegment3({6{1'b0}}),
    .segmentData4(timeSetting_main_2_dataout), .bitSelectedSegment4(timeSetting_main_2_outbits),
    .segmentData5(timeZoneChange_selector_1_capital), .bitSelectedSegment5({6{1'b0}}),
    .segmentData6(chronometre_1_segmentout), .bitSelectedSegment6({6{1'b0}}),
    .segmentData7(countdown_1_outdata), .bitSelectedSegment7({6{1'b0}}),
    .segmentData8(timeSetting_main_3_dataout), .bitSelectedSegment8(timeSetting_main_3_outbits),
    .segmentData9(game_1_outdata), .bitSelectedSegment9(game_1_bits), .state(d_ff_4_q),
    .alarmSignal(or_6_out), .reset(reset), .alarmPoint(alarmPoint), .s0(displayManager_1_s0),
    .s1(displayManager_1_s1), .s2(displayManager_1_s2), .s3(displayManager_1_s3), .s4(displayManager_1_s4),
    .s5(displayManager_1_s5), .pointDataSelected(displayManager_1_pointdataselected));

  // Other names for the same wires on the sheet: buttonActionNotFilter = b1
endmodule

module main_mainTransistion (
  input  C3,
  input  C2,
  input  C1,
  input  C0,
  input  LAP,
  input  LNP,
  input  SAP,
  input  SNP,
  input  FS,
  output D3,
  output D2,
  output D1,
  output D0
);

  wire and_1_out, and_2_out, and_3_out, and_4_out, and_5_out, and_6_out, and_7_out, and_8_out, and_9_out,
       and_10_out, and_11_out, and_12_out, and_13_out, and_14_out, and_15_out, and_16_out, and_17_out,
       and_18_out, and_19_out, and_20_out, and_21_out, and_22_out, and_23_out, and_24_out, and_25_out,
       and_26_out, and_27_out, and_28_out, and_29_out, and_30_out, and_31_out, and_32_out, and_33_out,
       not_1_out, not_2_out, not_3_out, not_4_out, not_5_out, not_6_out, not_7_out, not_8_out, not_9_out,
       not_10_out, not_11_out, not_12_out, not_13_out, not_14_out, not_15_out, not_16_out, not_17_out,
       not_18_out, not_19_out, not_20_out, not_21_out, not_22_out, not_23_out, not_24_out, not_25_out,
       not_26_out, not_27_out, not_28_out, not_29_out, not_30_out, not_31_out, not_32_out, not_33_out,
       not_34_out, not_35_out, not_36_out, not_37_out, not_38_out, not_39_out, not_40_out, not_41_out,
       not_42_out, not_43_out, not_44_out, not_45_out, not_46_out, not_47_out;

  not not_1 (not_1_out, C0);
  not not_2 (not_2_out, LAP);
  not not_3 (not_3_out, LNP);
  not not_4 (not_4_out, SAP);
  not not_5 (not_5_out, FS);
  not not_6 (not_6_out, C2);
  not not_7 (not_7_out, C0);
  not not_8 (not_8_out, LAP);
  not not_9 (not_9_out, LNP);
  not not_10 (not_10_out, SAP);
  not not_11 (not_11_out, FS);
  not not_12 (not_12_out, C3);
  not not_13 (not_13_out, C2);
  not not_14 (not_14_out, C1);
  not not_15 (not_15_out, C0);
  not not_16 (not_16_out, LAP);
  not not_17 (not_17_out, LNP);
  not not_18 (not_18_out, SAP);
  not not_19 (not_19_out, FS);
  not not_20 (not_20_out, C1);
  not not_21 (not_21_out, C0);
  not not_22 (not_22_out, LAP);
  not not_23 (not_23_out, LNP);
  not not_24 (not_24_out, SAP);
  not not_25 (not_25_out, FS);
  not not_26 (not_26_out, SNP);
  not not_27 (not_27_out, C1);
  not not_28 (not_28_out, SNP);
  not not_29 (not_29_out, SNP);
  not not_30 (not_30_out, LAP);
  not not_31 (not_31_out, LNP);
  not not_32 (not_32_out, SAP);
  not not_33 (not_33_out, FS);
  not not_34 (not_34_out, C3);
  not not_35 (not_35_out, C2);
  not not_36 (not_36_out, LNP);
  not not_37 (not_37_out, SAP);
  not not_38 (not_38_out, SNP);
  not not_39 (not_39_out, FS);
  not not_40 (not_40_out, SNP);
  not not_41 (not_41_out, FS);
  not not_42 (not_42_out, C2);
  not not_43 (not_43_out, LNP);
  not not_44 (not_44_out, SAP);
  not not_45 (not_45_out, SNP);
  not not_46 (not_46_out, FS);
  not not_47 (not_47_out, C1);
  and and_1 (and_1_out, C2, C1, not_1_out, not_2_out, not_3_out, not_4_out, SNP, not_5_out);
  and and_2 (and_2_out, C3, not_26_out);
  and and_3 (and_3_out, C3, FS);
  and and_4 (and_4_out, C3, SAP);
  and and_5 (and_5_out, C3, LNP);
  and and_6 (and_6_out, C3, LAP);
  and and_7 (and_7_out, C3, C1);
  and and_8 (and_8_out, not_6_out, C1, not_7_out, not_8_out, not_9_out, not_10_out, SNP, not_11_out);
  and and_9 (and_9_out, C2, not_27_out);
  and and_10 (and_10_out, C2, not_28_out);
  and and_11 (and_11_out, C2, FS);
  and and_12 (and_12_out, C2, SAP);
  and and_13 (and_13_out, C2, LNP);
  and and_14 (and_14_out, C2, LAP);
  and and_15 (and_15_out, C2, C0);
  and and_16 (and_16_out, not_12_out, not_13_out, not_14_out, not_15_out, not_16_out, not_17_out, not_18_out, SNP, not_19_out);
  and and_17 (and_17_out, C1, not_29_out);
  and and_18 (and_18_out, C1, FS);
  and and_19 (and_19_out, C1, SAP);
  and and_20 (and_20_out, C1, LNP);
  and and_21 (and_21_out, C1, LAP);
  and and_22 (and_22_out, C1, C0);
  and and_23 (and_23_out, C2, C0, not_30_out, not_31_out, not_32_out, SNP, not_33_out);
  and and_24 (and_24_out, not_34_out, not_35_out, LAP, not_36_out, not_37_out, not_38_out, not_39_out);
  and and_25 (and_25_out, C0, not_40_out, not_41_out);
  and and_26 (and_26_out, not_42_out, C0, SNP);
  and and_27 (and_27_out, C0, SAP);
  and and_28 (and_28_out, C0, LNP);
  and and_29 (and_29_out, C0, LAP);
  and and_30 (and_30_out, C1, LAP, not_43_out, not_44_out, not_45_out, not_46_out);
  and and_31 (and_31_out, C1, C0, SNP);
  and and_32 (and_32_out, C2, not_20_out, not_21_out, not_22_out, not_23_out, not_24_out, SNP, not_25_out);
  and and_33 (and_33_out, C2, not_47_out, C0, FS);
  or or_1 (D3, and_1_out, and_2_out, and_3_out, and_4_out, and_5_out, and_6_out, and_7_out);
  or or_2 (D2, and_8_out, and_9_out, and_10_out, and_11_out, and_12_out, and_13_out, and_14_out, and_15_out);
  or or_3 (D1, and_16_out, and_17_out, and_18_out, and_19_out, and_20_out, and_21_out, and_22_out, and_23_out);
  or or_4 (D0, and_24_out, and_25_out, and_26_out, and_27_out, and_28_out, and_29_out, and_30_out, and_31_out, and_32_out, and_33_out);
endmodule

module timeSetting_main (
  input  enable,
  input  shortNextPress,
  input  shortActionPress,
  input  reset,
  output [29:0] dataOut,
  output finish,
  output [5:0] outBits
);

  wire or_2_out, or_3_out, over24h_1_over, reset_t, superAdder_1_carryout, superAdder_3_carryout,
       superAdder_5_carryout, tools_logicEdge_1_down, tools_logicEdge_1_up;
  wire [4:0] superAdder_7_outbits;

  tools_logicEdge tools_logicEdge_1 (
    .inSignal(enable), .reset(reset), .up(tools_logicEdge_1_up), .down(tools_logicEdge_1_down));
  tools_superAdder superAdder_7 (
    .enable(enable), .carryIn(shortActionPress), .lastNumber(5'b00011), .clockIn(shortActionPress),
    .setBits({5{1'b0}}), .setSignal(1'b0), .reset(reset_t), .stopEnd(1'b0), .outBits(superAdder_7_outbits));  // open: carryOut
  Decoder #(.select(2), .enable("false")) decoder_1 (
    .out0(outBits[1]), .out1(outBits[3]), .out2(outBits[5]), .out3(finish), .sel(superAdder_7_outbits[1:0]));
  or or_1 (reset_t, tools_logicEdge_1_up, tools_logicEdge_1_down, reset);
  or or_2 (or_2_out, reset_t, over24h_1_over);
  or or_3 (or_3_out, reset_t, over24h_1_over);
  tools_superAdder superAdder_1 (
    .enable(outBits[1]), .carryIn(shortNextPress), .lastNumber(5'b01001), .clockIn(shortNextPress),
    .setBits({5{1'b0}}), .setSignal(1'b0), .reset(reset_t), .stopEnd(1'b0), .outBits(dataOut[4:0]),
    .carryOut(superAdder_1_carryout));
  tools_superAdder superAdder_2 (
    .enable(outBits[1]), .carryIn(superAdder_1_carryout), .lastNumber(5'b00101),
    .clockIn(superAdder_1_carryout), .setBits({5{1'b0}}), .setSignal(1'b0), .reset(reset_t), .stopEnd(1'b0),
    .outBits(dataOut[9:5]));  // open: carryOut
  tools_superAdder superAdder_3 (
    .enable(outBits[3]), .carryIn(shortNextPress), .lastNumber(5'b01001), .clockIn(shortNextPress),
    .setBits({5{1'b0}}), .setSignal(1'b0), .reset(reset_t), .stopEnd(1'b0), .outBits(dataOut[14:10]),
    .carryOut(superAdder_3_carryout));
  tools_superAdder superAdder_4 (
    .enable(outBits[3]), .carryIn(superAdder_3_carryout), .lastNumber(5'b00101),
    .clockIn(superAdder_3_carryout), .setBits({5{1'b0}}), .setSignal(1'b0), .reset(reset_t), .stopEnd(1'b0),
    .outBits(dataOut[19:15]));  // open: carryOut
  tools_superAdder superAdder_5 (
    .enable(outBits[5]), .carryIn(shortNextPress), .lastNumber(5'b01001), .clockIn(shortNextPress),
    .setBits({5{1'b0}}), .setSignal(1'b0), .reset(or_2_out), .stopEnd(1'b0), .outBits(dataOut[24:20]),
    .carryOut(superAdder_5_carryout));
  tools_superAdder superAdder_6 (
    .enable(outBits[5]), .carryIn(superAdder_5_carryout), .lastNumber(5'b00010),
    .clockIn(superAdder_5_carryout), .setBits({5{1'b0}}), .setSignal(1'b0), .reset(or_3_out), .stopEnd(1'b0),
    .outBits(dataOut[29:25]));  // open: carryOut
  timeSetting_over24h over24h_1 (.dataUnit(dataOut[24:20]), .dataTen(dataOut[29:25]), .over(over24h_1_over));

  assign {outBits[4], outBits[2], outBits[0]} = {outBits[5], outBits[3], outBits[1]};

  // Other names for the same wires on the sheet: onPress = shortNextPress
endmodule

module timeSetting_over24h (
  input  [4:0] dataUnit,
  input  [4:0] dataTen,
  output over
);

  wire comparator_1_gt, comparator_2_eq, comparator_2_gt, or_1_out;

  Comparator #(.width(5), .mode("unsigned")) comparator_1 (
    .a(dataUnit), .b(5'b00011), .gt(comparator_1_gt));  // open: eq, lt
  or or_1 (or_1_out, comparator_2_gt, comparator_2_eq);
  Comparator #(.width(5), .mode("unsigned")) comparator_2 (
    .a(dataTen), .b(5'b00010), .gt(comparator_2_gt), .eq(comparator_2_eq));  // open: lt
  and and_1 (over, comparator_1_gt, or_1_out);
endmodule

module hour_main (
  input  enable,
  input  [29:0] dataSet,
  input  setSignal,
  input  reset,
  output [29:0] segementData
);

  wire clock, or_1_out, or_2_out, over24h_1_over, superAdder_1_carryout, superAdder_2_carryout,
       superAdder_3_carryout, superAdder_4_carryout, superAdder_5_carryout;

  Clock #(.highDuration(2), .lowDuration(199998)) clock_1 (.out(clock));
  or or_1 (or_1_out, reset, over24h_1_over);
  or or_2 (or_2_out, reset, over24h_1_over);
  tools_superAdder superAdder_1 (
    .enable(enable), .carryIn(1'b1), .lastNumber(5'b01001), .clockIn(clock), .setBits(dataSet[4:0]),
    .setSignal(setSignal), .reset(reset), .stopEnd(1'b0), .outBits(segementData[4:0]),
    .carryOut(superAdder_1_carryout));
  tools_superAdder superAdder_2 (
    .enable(enable), .carryIn(superAdder_1_carryout), .lastNumber(5'b00101), .clockIn(clock),
    .setBits(dataSet[9:5]), .setSignal(setSignal), .reset(reset), .stopEnd(1'b0),
    .outBits(segementData[9:5]), .carryOut(superAdder_2_carryout));
  tools_superAdder superAdder_3 (
    .enable(enable), .carryIn(superAdder_2_carryout), .lastNumber(5'b01001), .clockIn(clock),
    .setBits(dataSet[14:10]), .setSignal(setSignal), .reset(reset), .stopEnd(1'b0),
    .outBits(segementData[14:10]), .carryOut(superAdder_3_carryout));
  tools_superAdder superAdder_4 (
    .enable(enable), .carryIn(superAdder_3_carryout), .lastNumber(5'b00101), .clockIn(clock),
    .setBits(dataSet[19:15]), .setSignal(setSignal), .reset(reset), .stopEnd(1'b0),
    .outBits(segementData[19:15]), .carryOut(superAdder_4_carryout));
  tools_superAdder superAdder_5 (
    .enable(enable), .carryIn(superAdder_4_carryout), .lastNumber(5'b01001), .clockIn(clock),
    .setBits(dataSet[24:20]), .setSignal(setSignal), .reset(or_1_out), .stopEnd(1'b0),
    .outBits(segementData[24:20]), .carryOut(superAdder_5_carryout));
  tools_superAdder superAdder_6 (
    .enable(enable), .carryIn(superAdder_5_carryout), .lastNumber(5'b00010), .clockIn(clock),
    .setBits(dataSet[29:25]), .setSignal(setSignal), .reset(or_2_out), .stopEnd(1'b0),
    .outBits(segementData[29:25]));  // open: carryOut
  timeSetting_over24h over24h_1 (.dataUnit(segementData[24:20]), .dataTen(segementData[29:25]), .over(over24h_1_over));
endmodule

module alarm_main (
  input  [29:0] alarmSet,
  input  [29:0] actualHour,
  input  setSignal,
  input  longActionPress,
  input  reset,
  output [29:0] alarmMemorised,
  output alarmSignal,
  output alarmPoint
);

  wire and_1_out, and_2_out, clock_1_out, comparator5Bits_1_i, comparator5Bits_2_i, comparator5Bits_3_i,
       comparator5Bits_4_i, comparator5Bits_5_i, comparator5Bits_6_i;
  wire [29:0] hourMemorised_1_alarmhourt;

  alarm_hourMemorised hourMemorised_1 (
    .alarmSet(alarmSet), .setSignal(setSignal), .reset(reset), .alarmHourt(hourMemorised_1_alarmhourt));
  Clock clock_1 (.out(clock_1_out));
  S_R_Flip_Flop s_r_ff_1 (
    .S(setSignal), .R(longActionPress), .clk(clock_1_out), .Q(alarmPoint), .reset(reset));  // open: Qn, preset
  tools_comparator5Bits comparator5Bits_1 (
    .alarmHour(hourMemorised_1_alarmhourt[4:0]), .actualHour(actualHour[4:0]), .i(comparator5Bits_1_i));
  tools_comparator5Bits comparator5Bits_2 (
    .alarmHour(hourMemorised_1_alarmhourt[9:5]), .actualHour(actualHour[9:5]), .i(comparator5Bits_2_i));
  tools_comparator5Bits comparator5Bits_3 (
    .alarmHour(hourMemorised_1_alarmhourt[14:10]), .actualHour(actualHour[14:10]), .i(comparator5Bits_3_i));
  tools_comparator5Bits comparator5Bits_4 (
    .alarmHour(hourMemorised_1_alarmhourt[19:15]), .actualHour(actualHour[19:15]), .i(comparator5Bits_4_i));
  tools_comparator5Bits comparator5Bits_5 (
    .alarmHour(hourMemorised_1_alarmhourt[24:20]), .actualHour(actualHour[24:20]), .i(comparator5Bits_5_i));
  tools_comparator5Bits comparator5Bits_6 (
    .alarmHour(hourMemorised_1_alarmhourt[29:25]), .actualHour(actualHour[29:25]), .i(comparator5Bits_6_i));
  and and_1 (and_1_out, comparator5Bits_1_i, comparator5Bits_2_i, comparator5Bits_3_i, comparator5Bits_4_i, comparator5Bits_5_i, comparator5Bits_6_i);
  and and_2 (and_2_out, and_1_out, alarmPoint);
  Multiplexer #(.width(30), .enable("false")) multiplexer_1 (
    .in0(30'h2d7d95db), .in1(hourMemorised_1_alarmhourt), .out(alarmMemorised), .sel(alarmPoint));
  tools_logicEdge logicEdge_1 (.inSignal(and_2_out), .reset(reset), .up(alarmSignal));  // open: down

  // Notes on the sheet:
  //   avant de setl l'heure
  //   reset quand on entre dans le mode alarme,
endmodule

module alarm_hourMemorised (
  input  [29:0] alarmSet,
  input  setSignal,
  input  reset,
  output [29:0] alarmHourt
);

  wire clock_1_out;

  Clock clock_1 (.out(clock_1_out));
  tools_fiveBitsDFF fiveBitsDFF_1 (
    .inBits(alarmSet[4:0]), .setSignal(setSignal), .reset(reset), .clock(clock_1_out),
    .outBits(alarmHourt[4:0]));
  tools_fiveBitsDFF fiveBitsDFF_2 (
    .inBits(alarmSet[9:5]), .setSignal(setSignal), .reset(reset), .clock(clock_1_out),
    .outBits(alarmHourt[9:5]));
  tools_fiveBitsDFF fiveBitsDFF_3 (
    .inBits(alarmSet[14:10]), .setSignal(setSignal), .reset(reset), .clock(clock_1_out),
    .outBits(alarmHourt[14:10]));
  tools_fiveBitsDFF fiveBitsDFF_4 (
    .inBits(alarmSet[19:15]), .setSignal(setSignal), .reset(reset), .clock(clock_1_out),
    .outBits(alarmHourt[19:15]));
  tools_fiveBitsDFF fiveBitsDFF_5 (
    .inBits(alarmSet[24:20]), .setSignal(setSignal), .reset(reset), .clock(clock_1_out),
    .outBits(alarmHourt[24:20]));
  tools_fiveBitsDFF fiveBitsDFF_6 (
    .inBits(alarmSet[29:25]), .setSignal(setSignal), .reset(reset), .clock(clock_1_out),
    .outBits(alarmHourt[29:25]));
endmodule

module timeZoneChange_gofront (
  input  [29:0] currentHour,
  input  [2:0] CapitalSelected,
  output [29:0] modifiedHour
);

  wire [4:0] deconvertB24_2_outbits, multiplexer_1_out, timeZoneChange_adderHour_1_outhour,
       timeZoneChange_adderHour_2_outhour, timeZoneChange_adderHour_3_outhour,
       timeZoneChange_adderHour_4_outhour;

  tools_deconvertB24 deconvertB24_2 (
    .inUnit(currentHour[24:20]), .inTen(currentHour[29:25]), .outBits(deconvertB24_2_outbits));
  timeZoneChange_adderHour timeZoneChange_adderHour_1 (
    .currentHour(deconvertB24_2_outbits), .addHour(5'b00101), .outHour(timeZoneChange_adderHour_1_outhour));
  timeZoneChange_adderHour timeZoneChange_adderHour_2 (
    .currentHour(deconvertB24_2_outbits), .addHour(5'b01000), .outHour(timeZoneChange_adderHour_2_outhour));
  timeZoneChange_adderHour timeZoneChange_adderHour_3 (
    .currentHour(deconvertB24_2_outbits), .addHour(5'b10100), .outHour(timeZoneChange_adderHour_3_outhour));
  timeZoneChange_adderHour timeZoneChange_adderHour_4 (
    .currentHour(deconvertB24_2_outbits), .addHour(5'b10010), .outHour(timeZoneChange_adderHour_4_outhour));
  Multiplexer #(.select(3), .width(5), .enable("false")) multiplexer_1 (
    .in0(deconvertB24_2_outbits), .in1(timeZoneChange_adderHour_1_outhour),
    .in2(timeZoneChange_adderHour_2_outhour), .in3(timeZoneChange_adderHour_3_outhour),
    .in4(timeZoneChange_adderHour_4_outhour), .out(multiplexer_1_out), .sel(CapitalSelected));  // open: in5, in6, in7
  tools_convertB24 convertB24_1 (.intBits(multiplexer_1_out), .unit(modifiedHour[24:20]), .ten(modifiedHour[29:25]));

  assign modifiedHour[19:0] = currentHour[19:0];

  // Notes on the sheet:
  //   Add 5 hours
  //   Add 8 hours
  //   substract 4 hours
  //   substract 6 hours
endmodule

module timeZoneChange_selector (
  input  enable2,
  input  button2,
  input  reset2,
  output [2:0] capitalSelected,
  output [29:0] capital
);

  wire [4:3] superAdder_1_outbits;

  tools_superAdder superAdder_1 (
    .enable(enable2), .carryIn(button2), .lastNumber(5'b00100), .clockIn(button2), .setBits({5{1'b0}}),
    .setSignal(1'b0), .reset(reset2), .stopEnd(1'b0), .outBits({superAdder_1_outbits, capitalSelected}));  // open: carryOut
  timeZoneChange_countryLetters countryLetters_2 (.code(capitalSelected), .city(capital));
endmodule

module timeZoneChange_goback (
  input  [29:0] setHour,
  input  [2:0] capitalState,
  output [29:0] outHours
);

  wire [4:0] multiplexer_1_out, timeZoneChange_adderHour_1_outhour, timeZoneChange_adderHour_2_outhour,
       timeZoneChange_adderHour_3_outhour, timeZoneChange_adderHour_4_outhour, tools_deconvertB24_1_outbits;

  tools_deconvertB24 tools_deconvertB24_1 (
    .inUnit(setHour[24:20]), .inTen(setHour[29:25]), .outBits(tools_deconvertB24_1_outbits));
  timeZoneChange_adderHour timeZoneChange_adderHour_1 (
    .currentHour(tools_deconvertB24_1_outbits), .addHour(5'b10011),
    .outHour(timeZoneChange_adderHour_1_outhour));
  timeZoneChange_adderHour timeZoneChange_adderHour_2 (
    .currentHour(tools_deconvertB24_1_outbits), .addHour(5'b10000),
    .outHour(timeZoneChange_adderHour_2_outhour));
  timeZoneChange_adderHour timeZoneChange_adderHour_3 (
    .currentHour(tools_deconvertB24_1_outbits), .addHour(5'b00100),
    .outHour(timeZoneChange_adderHour_3_outhour));
  timeZoneChange_adderHour timeZoneChange_adderHour_4 (
    .currentHour(tools_deconvertB24_1_outbits), .addHour(5'b00110),
    .outHour(timeZoneChange_adderHour_4_outhour));
  Multiplexer #(.select(3), .width(5), .enable("false")) multiplexer_1 (
    .in0(tools_deconvertB24_1_outbits), .in1(timeZoneChange_adderHour_1_outhour),
    .in2(timeZoneChange_adderHour_2_outhour), .in3(timeZoneChange_adderHour_3_outhour),
    .in4(timeZoneChange_adderHour_4_outhour), .out(multiplexer_1_out), .sel(capitalState));  // open: in5, in6, in7
  tools_convertB24 tools_convertB24_1 (.intBits(multiplexer_1_out), .unit(outHours[24:20]), .ten(outHours[29:25]));

  assign outHours[19:0] = setHour[19:0];

  // Notes on the sheet:
  //   substract 5 hours
  //   substract 8 hours
  //   add 4 hours
  //   add 6 hours
endmodule

module timeZoneChange_adderHour (
  input  [4:0] currentHour,
  input  [4:0] addHour,
  output [4:0] outHour
);

  wire comparator_1_eq, comparator_1_gt, or_1_out;
  wire [4:0] adder_1_out;
  wire [5:0] subtractor_1_out;
  wire [5:5] adder_1_cout, multiplexer_1_out;

  Adder #(.width(5)) adder_1 (.a(currentHour), .b(addHour), .out(adder_1_out), .cout(adder_1_cout[5]));  // open: cin
  Comparator #(.width(6), .mode("unsigned")) comparator_1 (
    .a({adder_1_cout[5], adder_1_out}), .b(6'b011000), .gt(comparator_1_gt), .eq(comparator_1_eq));  // open: lt
  or or_1 (or_1_out, comparator_1_gt, comparator_1_eq);
  Subtractor #(.width(6)) subtractor_1 (
    .a({adder_1_cout[5], adder_1_out}), .b(6'b011000), .out(subtractor_1_out));  // open: bin, bout
  Multiplexer #(.width(6), .enable("false")) multiplexer_1 (
    .in0({adder_1_cout[5], adder_1_out}), .in1(subtractor_1_out), .out({multiplexer_1_out[5], outHour}),
    .sel(or_1_out));
endmodule

module timeZoneChange_countryLetters (
  input  [2:0] code,
  output [29:0] city
);

  Multiplexer #(.select(3), .width(30), .enable("false")) multiplexer_1 (
    .in0(30'h615a), .in1(30'h28bb), .in2(30'h6ef3), .in3(30'h2f4a), .in4(30'h79ac), .in5({30{1'b0}}),
    .in6({30{1'b0}}), .in7({30{1'b0}}), .out(city), .sel(code));
endmodule

module chronometre_main (
  input  enable,
  input  shortAction,
  input  longAction,
  input  reset,
  output [29:0] segmentOut
);

  wire and_1_out, and_2_out, clock_1_out, clock_2_out, d_ff_1_q, d_ff_2_q, or_1_out, or_2_out, t_ff_1_q;

  Clock clock_1 (.out(clock_1_out));
  D_Flip_Flop d_ff_1 (.D(shortAction), .clk(clock_1_out), .Q(d_ff_1_q), .reset(reset));  // open: Qn, preset
  D_Flip_Flop d_ff_2 (.D(longAction), .clk(clock_1_out), .Q(d_ff_2_q), .reset(reset));  // open: Qn, preset
  and and_1 (and_1_out, t_ff_1_q, d_ff_2_q);
  or or_1 (or_1_out, and_1_out, d_ff_1_q);
  and and_2 (and_2_out, enable, or_1_out);
  T_Flip_Flop t_ff_1 (.T(and_2_out), .clk(clock_2_out), .Q(t_ff_1_q), .reset(reset));  // open: Qn, preset
  Clock clock_2 (.out(clock_2_out));
  or or_2 (or_2_out, d_ff_2_q, reset);
  hour_main hour_main_1 (
    .enable(t_ff_1_q), .dataSet({30{1'b0}}), .setSignal(1'b0), .reset(or_2_out), .segementData(segmentOut));
endmodule

module countdown_main (
  input  enable,
  input  shortActionPress,
  input  [29:0] inData,
  input  setSignal,
  input  reset,
  output musicPlay,
  output [29:0] outData
);

  wire and_1_out, and_3_out, clk, clock_1_out, clock_3_out, enable_t, s_r_ff_1_q, stop,
       superSubstracter_1_output_1, superSubstracter_2_output_1, superSubstracter_3_output_1,
       superSubstracter_4_output_1, superSubstracter_5_output_1, t_ff_1_q;

  T_Flip_Flop t_ff_1 (.T(and_1_out), .clk(clock_1_out), .Q(t_ff_1_q));  // open: Qn, reset, preset
  and and_1 (and_1_out, enable, shortActionPress);
  Clock clock_1 (.out(clock_1_out));
  Clock #(.highDuration(2), .lowDuration(199998)) clock_2 (.out(clk));
  and and_2 (enable_t, t_ff_1_q, ~stop);  // AND_Gate
  S_R_Flip_Flop s_r_ff_1 (
    .S(enable_t), .R(reset), .clk(clock_3_out), .Q(s_r_ff_1_q), .reset(reset));  // open: Qn, preset
  Clock clock_3 (.out(clock_3_out));
  tools_superSubstracter superSubstracter_1 (
    .enable(enable_t), .carryIn(1'b1), .initialValue(5'b01001), .clockIn(clk), .setNumber(inData[4:0]),
    .setSignal(setSignal), .reset(reset), .stopEnd(1'b0), .Output_bus_1(outData[4:0]),
    .Output_1(superSubstracter_1_output_1));
  tools_superSubstracter superSubstracter_2 (
    .enable(enable_t), .carryIn(superSubstracter_1_output_1), .initialValue(5'b00101), .clockIn(clk),
    .setNumber(inData[9:5]), .setSignal(setSignal), .reset(reset), .stopEnd(1'b0),
    .Output_bus_1(outData[9:5]), .Output_1(superSubstracter_2_output_1));
  tools_superSubstracter superSubstracter_3 (
    .enable(enable_t), .carryIn(superSubstracter_2_output_1), .initialValue(5'b01001), .clockIn(clk),
    .setNumber(inData[14:10]), .setSignal(setSignal), .reset(reset), .stopEnd(1'b0),
    .Output_bus_1(outData[14:10]), .Output_1(superSubstracter_3_output_1));
  tools_superSubstracter superSubstracter_4 (
    .enable(enable_t), .carryIn(superSubstracter_3_output_1), .initialValue(5'b00101), .clockIn(clk),
    .setNumber(inData[19:15]), .setSignal(setSignal), .reset(reset), .stopEnd(1'b0),
    .Output_bus_1(outData[19:15]), .Output_1(superSubstracter_4_output_1));
  tools_superSubstracter superSubstracter_5 (
    .enable(enable_t), .carryIn(superSubstracter_4_output_1), .initialValue(5'b01001), .clockIn(clk),
    .setNumber(inData[24:20]), .setSignal(setSignal), .reset(reset), .stopEnd(1'b0),
    .Output_bus_1(outData[24:20]), .Output_1(superSubstracter_5_output_1));
  tools_superSubstracter superSubstracter_6 (
    .enable(enable_t), .carryIn(superSubstracter_5_output_1), .initialValue(5'b00010), .clockIn(clk),
    .setNumber(inData[29:25]), .setSignal(setSignal), .reset(reset), .stopEnd(1'b0),
    .Output_bus_1(outData[29:25]));  // open: Output_1
  Comparator #(.width(30), .mode("unsigned")) comparator_1 (.a(outData), .b({30{1'b0}}), .eq(stop));  // open: gt, lt
  and and_3 (and_3_out, s_r_ff_1_q, stop);
  tools_logicEdge logicEdge_1 (.inSignal(and_3_out), .reset(reset), .up(musicPlay));  // open: down
endmodule

module game_main (
  input  enable,
  input  buttonInput,
  input  reset,
  output [5:0] bits,
  output [29:0] outData,
  output playMario
);

  wire clock_1_out, clock_2_out, clock_3_out, clock_4_out, clock_5_out, clock_6_out, clock_7_out,
       clock_8_out, clock_9_out, clock_10_out, clock_11_out, clock_12_out, clock_13_out, clock_14_out,
       clock_15_out, clock_16_out, clock_17_out, clock_18_out, clock_19_out, clock_20_out, clock_21_out,
       clock_22_out, clock_23_out, comparator_1_eq, game7Segment_9_out1, game7Segment_9_out2,
       gameFilter_1_out1, gameFilter_1_out2, gameLogicEdge_1_pinout, gameLogicEdge_2_pinout,
       gamePlayerManager_S1_endgame, gamerRandom_1_random1, gamerRandom_1_random2, multiplexer_1_out,
       multiplexer_2_out, or_1_out, or_2_out, tools_logicEdge_1_up;
  wire [4:0] superAdder_2_outbits;

  Clock #(.highDuration(2), .lowDuration(1999998)) clock_1 (.out(clock_1_out));
  tools_logicEdge tools_logicEdge_1 (.inSignal(enable), .reset(reset), .up(tools_logicEdge_1_up));  // open: down
  Clock #(.highDuration(2), .lowDuration(199998)) clock_2 (.out(clock_2_out));
  and and_1 (playMario, clock_1_out, enable);
  or or_1 (or_1_out, tools_logicEdge_1_up, reset);
  tools_superAdder superAdder_1 (
    .enable(enable), .carryIn(1'b1), .lastNumber(5'b01001), .clockIn(clock_1_out), .setBits({5{1'b0}}),
    .setSignal(1'b0), .reset(or_2_out), .stopEnd(1'b1), .outBits(outData[29:25]));  // open: carryOut
  Clock #(.highDuration(2), .lowDuration(199998)) clock_3 (.out(clock_3_out));
  Clock #(.highDuration(2), .lowDuration(179998)) clock_4 (.out(clock_4_out));
  Clock #(.highDuration(2), .lowDuration(119998)) clock_5 (.out(clock_5_out));
  Clock #(.highDuration(2), .lowDuration(79998)) clock_6 (.out(clock_6_out));
  Clock #(.highDuration(2), .lowDuration(59998)) clock_7 (.out(clock_7_out));
  Clock #(.highDuration(2), .lowDuration(49998)) clock_8 (.out(clock_8_out));
  Clock #(.highDuration(2), .lowDuration(49998)) clock_9 (.out(clock_9_out));
  Clock #(.highDuration(2), .lowDuration(49998)) clock_10 (.out(clock_10_out));
  Clock #(.highDuration(2), .lowDuration(49998)) clock_11 (.out(clock_11_out));
  Clock #(.highDuration(2), .lowDuration(39998)) clock_12 (.out(clock_12_out));
  Clock #(.highDuration(2), .lowDuration(19998)) clock_13 (.out(clock_13_out));
  Clock #(.highDuration(2), .lowDuration(17998)) clock_14 (.out(clock_14_out));
  Clock #(.highDuration(2), .lowDuration(15998)) clock_15 (.out(clock_15_out));
  Clock #(.highDuration(2), .lowDuration(13998)) clock_16 (.out(clock_16_out));
  Clock #(.highDuration(2), .lowDuration(11998)) clock_17 (.out(clock_17_out));
  Clock #(.highDuration(2), .lowDuration(9998)) clock_18 (.out(clock_18_out));
  Clock #(.highDuration(2), .lowDuration(7998)) clock_19 (.out(clock_19_out));
  Clock #(.highDuration(2), .lowDuration(5998)) clock_20 (.out(clock_20_out));
  Clock #(.highDuration(2), .lowDuration(3998)) clock_21 (.out(clock_21_out));
  Clock #(.highDuration(2), .lowDuration(1998)) clock_22 (.out(clock_22_out));
  Clock #(.highDuration(2), .lowDuration(998)) clock_23 (.out(clock_23_out));
  tools_superAdder superAdder_2 (
    .enable(enable), .carryIn(enable), .lastNumber(5'b00010), .clockIn(clock_2_out), .setBits({5{1'b0}}),
    .setSignal(clock_1_out), .reset(or_1_out), .stopEnd(1'b1), .outBits(superAdder_2_outbits));  // open: carryOut
  Comparator #(.width(5), .mode("unsigned")) comparator_1 (
    .a(5'b00010), .b(superAdder_2_outbits), .eq(comparator_1_eq));  // open: gt, lt
  not not_1 (bits[5], comparator_1_eq);
  Multiplexer #(.select(4), .enable("false")) multiplexer_1 (
    .in0(clock_3_out), .in1(clock_4_out), .in2(clock_5_out), .in3(clock_6_out), .in4(clock_7_out),
    .in5(clock_8_out), .in6(clock_9_out), .in7(clock_10_out), .in8(clock_11_out), .in9(clock_12_out),
    .in10(1'b0), .in11(1'b0), .in12(1'b0), .in13(1'b0), .in14(1'b0), .in15(1'b0), .out(multiplexer_1_out),
    .sel(outData[28:25]));
  Multiplexer #(.select(4), .enable("false")) multiplexer_2 (
    .in0(clock_13_out), .in1(clock_14_out), .in2(clock_15_out), .in3(clock_16_out), .in4(clock_17_out),
    .in5(clock_18_out), .in6(clock_19_out), .in7(clock_20_out), .in8(clock_21_out), .in9(clock_22_out),
    .in10(clock_23_out), .in11(1'b0), .in12(1'b0), .in13(1'b0), .in14(1'b0), .in15(1'b0),
    .out(multiplexer_2_out), .sel(outData[28:25]));
  game_random gamerRandom_1 (
    .clk(multiplexer_1_out), .reset(or_2_out), .random1(gamerRandom_1_random1),
    .random2(gamerRandom_1_random2));
  game_filter gameFilter_1 (
    .in1(gamerRandom_1_random1), .in2(gamerRandom_1_random2), .pIn1(outData[1]), .pIn2(outData[0]),
    .out1(gameFilter_1_out1), .out2(gameFilter_1_out2));
  game_logicEdge gameLogicEdge_1 (
    .pinIn(gameFilter_1_out1), .clockIn(multiplexer_2_out), .pinOut(gameLogicEdge_1_pinout));
  game_logicEdge gameLogicEdge_2 (
    .pinIn(gameFilter_1_out2), .clockIn(multiplexer_2_out), .pinOut(gameLogicEdge_2_pinout));
  game_7Segment game7Segment_1 (
    .in11(gameLogicEdge_1_pinout), .in22(gameLogicEdge_2_pinout), .reset2(or_2_out),
    .clockIn(multiplexer_2_out), .out1(outData[1]), .out2(outData[0]));
  game_7Segment game7Segment_2 (
    .in11(outData[1]), .in22(outData[0]), .reset2(or_2_out), .clockIn(multiplexer_2_out), .out1(outData[2]),
    .out2(outData[3]));
  game_7Segment game7Segment_3 (
    .in11(outData[2]), .in22(outData[3]), .reset2(or_2_out), .clockIn(multiplexer_2_out), .out1(outData[6]),
    .out2(outData[5]));
  game_7Segment game7Segment_4 (
    .in11(outData[6]), .in22(outData[5]), .reset2(or_2_out), .clockIn(multiplexer_2_out), .out1(outData[7]),
    .out2(outData[8]));
  game_7Segment game7Segment_5 (
    .in11(outData[7]), .in22(outData[8]), .reset2(or_2_out), .clockIn(multiplexer_2_out), .out1(outData[11]),
    .out2(outData[10]));
  game_7Segment game7Segment_6 (
    .in11(outData[11]), .in22(outData[10]), .reset2(or_2_out), .clockIn(multiplexer_2_out),
    .out1(outData[12]), .out2(outData[13]));
  game_7Segment game7Segment_7 (
    .in11(outData[12]), .in22(outData[13]), .reset2(or_2_out), .clockIn(multiplexer_2_out),
    .out1(outData[16]), .out2(outData[15]));
  game_7Segment game7Segment_8 (
    .in11(outData[16]), .in22(outData[15]), .reset2(or_2_out), .clockIn(multiplexer_2_out),
    .out1(outData[17]), .out2(outData[18]));
  game_7Segment game7Segment_9 (
    .in11(outData[17]), .in22(outData[18]), .reset2(or_2_out), .clockIn(multiplexer_2_out),
    .out1(game7Segment_9_out1), .out2(game7Segment_9_out2));
  or or_2 (or_2_out, gamePlayerManager_S1_endgame, or_1_out);
  game_playerManager gamePlayerManager_S1 (
    .buttonInput(buttonInput), .in1(game7Segment_9_out1), .in2(game7Segment_9_out2), .reset(or_2_out),
    .clockIn(multiplexer_2_out), .endGame(gamePlayerManager_S1_endgame), .out7Segment(outData[23:20]));

  assign bits[4:0] = {5{1'b0}};
  assign {outData[24], outData[19], outData[14], outData[9], outData[4]} = {5{1'b0}};
endmodule

module game_logicEdge (
  input  pinIn,
  input  clockIn,
  output pinOut
);

  wire clock_1_out, d_ff_1_q, d_ff_2_q, multiplexer_1_out, multiplexer_2_out, xor_1_out;

  Multiplexer #(.enable("false")) multiplexer_1 (.in0(d_ff_1_q), .in1(pinIn), .out(multiplexer_1_out), .sel(clockIn));
  D_Flip_Flop d_ff_1 (.D(multiplexer_1_out), .clk(clock_1_out), .Q(d_ff_1_q));  // open: Qn, preset, reset
  Clock clock_1 (.out(clock_1_out));
  Multiplexer #(.enable("false")) multiplexer_2 (
    .in0(d_ff_2_q), .in1(d_ff_1_q), .out(multiplexer_2_out), .sel(clockIn));
  D_Flip_Flop d_ff_2 (.D(multiplexer_2_out), .clk(clock_1_out), .Q(d_ff_2_q));  // open: Qn, preset, reset
  xor xor_1 (xor_1_out, d_ff_1_q, d_ff_2_q);
  and and_1 (pinOut, pinIn, xor_1_out);
endmodule

module game_7Segment (
  input  in11,
  input  in22,
  input  reset2,
  input  clockIn,
  output out1,
  output out2
);

  wire clock_1_out, multiplexer_1_out, multiplexer_2_out;

  Multiplexer #(.enable("false")) multiplexer_1 (.in0(out1), .in1(in11), .out(multiplexer_1_out), .sel(clockIn));
  Multiplexer #(.enable("false")) multiplexer_2 (.in0(out2), .in1(in22), .out(multiplexer_2_out), .sel(clockIn));
  Clock clock_1 (.out(clock_1_out));
  D_Flip_Flop d_ff_1 (.D(multiplexer_1_out), .clk(clock_1_out), .Q(out1), .reset(reset2));  // open: Qn, preset
  D_Flip_Flop d_ff_2 (.D(multiplexer_2_out), .clk(clock_1_out), .Q(out2), .reset(reset2));  // open: Qn, preset
endmodule

module game_playerManager (
  input  buttonInput,
  input  in1,
  input  in2,
  input  reset,
  input  clockIn,
  output endGame,
  output [3:0] out7Segment
);

  wire and_1_out, and_2_out, clock_1_out, d_ff_1_q, multiplexer_1_out, multiplexer_2_out, not_1_out;

  Clock clock_1 (.out(clock_1_out));
  D_Flip_Flop d_ff_1 (.D(buttonInput), .clk(clock_1_out), .Q(d_ff_1_q), .reset(reset));  // open: Qn, preset
  or or_1 (out7Segment[1], d_ff_1_q, in1);
  or or_2 (out7Segment[0], ~d_ff_1_q, in2);  // OR_Gate
  not not_1 (not_1_out, d_ff_1_q);
  and and_1 (and_1_out, d_ff_1_q, in1);
  or or_3 (endGame, and_1_out, and_2_out);
  and and_2 (and_2_out, not_1_out, in2);
  Multiplexer #(.enable("false")) multiplexer_1 (
    .in0(out7Segment[2]), .in1(in1), .out(multiplexer_1_out), .sel(clockIn));
  Multiplexer #(.enable("false")) multiplexer_2 (
    .in0(out7Segment[3]), .in1(in2), .out(multiplexer_2_out), .sel(clockIn));
  D_Flip_Flop d_ff_2 (.D(multiplexer_1_out), .clk(clock_1_out), .Q(out7Segment[2]), .reset(reset));  // open: Qn, preset
  D_Flip_Flop d_ff_3 (.D(multiplexer_2_out), .clk(clock_1_out), .Q(out7Segment[3]), .reset(reset));  // open: Qn, preset
endmodule

module game_random (
  input  clk,
  input  reset,
  output random1,
  output random2
);

  wire clock_1_out, clock_2_out, clock_3_out, clock_4_out, clock_5_out, d_ff_1_q, d_ff_2_q, d_ff_3_q,
       d_ff_4_q, d_ff_5_q, d_ff_6_q, d_ff_7_q, d_ff_8_q, multiplexer_1_out, multiplexer_2_out,
       multiplexer_3_out, multiplexer_4_out, multiplexer_5_out, multiplexer_6_out, multiplexer_7_out,
       multiplexer_8_out, multiplexer_9_out, multiplexer_10_out, xor_1_out, xor_2_out;

  Multiplexer #(.enable("false")) multiplexer_1 (.in0(d_ff_1_q), .in1(xor_1_out), .out(multiplexer_1_out), .sel(clk));
  Multiplexer #(.enable("false")) multiplexer_2 (.in0(d_ff_2_q), .in1(xor_2_out), .out(multiplexer_2_out), .sel(clk));
  xor xor_1 (xor_1_out, random1, d_ff_1_q);
  xor xor_2 (xor_2_out, random2, d_ff_2_q);
  Clock clock_1 (.out(clock_1_out));
  D_Flip_Flop d_ff_1 (.D(multiplexer_1_out), .clk(clock_1_out), .Q(d_ff_1_q), .reset(reset));  // open: Qn, preset
  D_Flip_Flop d_ff_2 (.D(multiplexer_2_out), .clk(clock_1_out), .Q(d_ff_2_q), .preset(reset));  // open: Qn, reset
  Multiplexer #(.enable("false")) multiplexer_3 (.in0(d_ff_3_q), .in1(d_ff_1_q), .out(multiplexer_3_out), .sel(clk));
  Multiplexer #(.enable("false")) multiplexer_4 (.in0(d_ff_4_q), .in1(d_ff_2_q), .out(multiplexer_4_out), .sel(clk));
  Clock clock_2 (.out(clock_2_out));
  D_Flip_Flop d_ff_3 (.D(multiplexer_3_out), .clk(clock_2_out), .Q(d_ff_3_q), .reset(reset));  // open: Qn, preset
  D_Flip_Flop d_ff_4 (.D(multiplexer_4_out), .clk(clock_2_out), .Q(d_ff_4_q), .reset(reset));  // open: Qn, preset
  Multiplexer #(.enable("false")) multiplexer_5 (.in0(d_ff_5_q), .in1(d_ff_3_q), .out(multiplexer_5_out), .sel(clk));
  Multiplexer #(.enable("false")) multiplexer_6 (.in0(d_ff_6_q), .in1(d_ff_4_q), .out(multiplexer_6_out), .sel(clk));
  Clock clock_3 (.out(clock_3_out));
  D_Flip_Flop d_ff_5 (.D(multiplexer_5_out), .clk(clock_3_out), .Q(d_ff_5_q), .reset(reset));  // open: Qn, preset
  D_Flip_Flop d_ff_6 (.D(multiplexer_6_out), .clk(clock_3_out), .Q(d_ff_6_q), .reset(reset));  // open: Qn, preset
  Multiplexer #(.enable("false")) multiplexer_7 (.in0(d_ff_7_q), .in1(d_ff_5_q), .out(multiplexer_7_out), .sel(clk));
  Multiplexer #(.enable("false")) multiplexer_8 (.in0(d_ff_8_q), .in1(d_ff_6_q), .out(multiplexer_8_out), .sel(clk));
  D_Flip_Flop d_ff_7 (.D(multiplexer_7_out), .clk(clock_4_out), .Q(d_ff_7_q), .reset(reset));  // open: Qn, preset
  D_Flip_Flop d_ff_8 (.D(multiplexer_8_out), .clk(clock_4_out), .Q(d_ff_8_q), .reset(reset));  // open: Qn, preset
  Clock clock_4 (.out(clock_4_out));
  Multiplexer #(.enable("false")) multiplexer_9 (.in0(random1), .in1(d_ff_7_q), .out(multiplexer_9_out), .sel(clk));
  Multiplexer #(.enable("false")) multiplexer_10 (.in0(random2), .in1(d_ff_8_q), .out(multiplexer_10_out), .sel(clk));
  D_Flip_Flop d_ff_9 (.D(multiplexer_9_out), .clk(clock_5_out), .Q(random1), .preset(reset));  // open: Qn, reset
  D_Flip_Flop d_ff_10 (.D(multiplexer_10_out), .clk(clock_5_out), .Q(random2), .reset(reset));  // open: Qn, preset
  Clock clock_5 (.out(clock_5_out));
endmodule

module game_filter (
  input  in1,
  input  in2,
  input  pIn1,
  input  pIn2,
  output out1,
  output out2
);

  wire not_1_out, not_2_out, not_3_out, not_4_out;

  not not_1 (not_1_out, in2);
  not not_2 (not_2_out, pIn2);
  not not_3 (not_3_out, in1);
  not not_4 (not_4_out, pIn1);
  and and_1 (out1, in1, not_1_out, not_2_out);
  and and_2 (out2, not_3_out, in2, not_4_out);
endmodule

module buttonManager_main (
  input  buttonNext,
  input  buttonAction,
  input  reset,
  output longActionPress,
  output longNextPress,
  output shortActionPress,
  output shortNextPress,
  output resetButton
);

  wire and_1_out, buttonsDetectLongPress_1_longpress, buttonsDetectLongPress_2_longpress;

  buttonManager_detectLongPress buttonsDetectLongPress_1 (
    .buttonInput(buttonNext), .reset(reset), .shortPress(shortNextPress),
    .LongPress(buttonsDetectLongPress_1_longpress));
  buttonManager_detectLongPress buttonsDetectLongPress_2 (
    .buttonInput(buttonAction), .reset(reset), .shortPress(shortActionPress),
    .LongPress(buttonsDetectLongPress_2_longpress));
  and and_1 (and_1_out, buttonsDetectLongPress_1_longpress, buttonsDetectLongPress_2_longpress);
  tools_logicEdge tools_logicEdge_2 (
    .inSignal(buttonsDetectLongPress_2_longpress), .reset(reset), .up(longActionPress));  // open: down
  tools_logicEdge tools_logicEdge_3 (
    .inSignal(buttonsDetectLongPress_1_longpress), .reset(reset), .up(longNextPress));  // open: down
  tools_logicEdge tools_logicEdge_1 (.inSignal(and_1_out), .reset(reset), .down(resetButton));  // open: up
endmodule

module buttonManager_detectLongPress (
  input  buttonInput,
  input  reset,
  output shortPress,
  output LongPress
);

  wire clock_1_out, logicEdge_1_down, logicEdge_1_up, or_1_out, tools_superAdder_1_carryout;
  wire [4:0] tools_superAdder_1_outbits;

  tools_logicEdge logicEdge_1 (.inSignal(buttonInput), .reset(reset), .up(logicEdge_1_up), .down(logicEdge_1_down));
  or or_1 (or_1_out, logicEdge_1_up, reset);
  Clock #(.highDuration(2), .lowDuration(19998)) clock_1 (.out(clock_1_out));
  tools_superAdder tools_superAdder_1 (
    .enable(1'b1), .carryIn(1'b1), .lastNumber(5'b01010), .clockIn(clock_1_out), .setBits({5{1'b0}}),
    .setSignal(1'b0), .reset(or_1_out), .stopEnd(1'b1), .outBits(tools_superAdder_1_outbits),
    .carryOut(tools_superAdder_1_carryout));
  and and_1 (LongPress, buttonInput, tools_superAdder_1_carryout);
  and and_2 (shortPress, logicEdge_1_down, ~tools_superAdder_1_carryout);  // AND_Gate
endmodule

module display_displaySegment (
  input  [6:0] S0,
  input  [6:0] S1,
  input  [6:0] S2,
  input  [6:0] S3,
  input  [6:0] S4,
  input  [6:0] S5,
  input  [5:0] pointData
);

  wire display_5_a, display_5_b, display_5_c, display_5_d, display_5_e, display_5_f, display_5_g,
       display_6_a, display_6_b, display_6_c, display_6_d, display_6_e, display_6_f, display_6_g,
       displaySegmentDisplay_1_a, displaySegmentDisplay_1_b, displaySegmentDisplay_1_c,
       displaySegmentDisplay_1_d, displaySegmentDisplay_1_e, displaySegmentDisplay_1_f,
       displaySegmentDisplay_1_g, displaySegmentDisplay_2_a, displaySegmentDisplay_2_b,
       displaySegmentDisplay_2_c, displaySegmentDisplay_2_d, displaySegmentDisplay_2_e,
       displaySegmentDisplay_2_f, displaySegmentDisplay_2_g, displaySegmentDisplay_3_a,
       displaySegmentDisplay_3_b, displaySegmentDisplay_3_c, displaySegmentDisplay_3_d,
       displaySegmentDisplay_3_e, displaySegmentDisplay_3_f, displaySegmentDisplay_3_g,
       displaySegmentDisplay_4_a, displaySegmentDisplay_4_b, displaySegmentDisplay_4_c,
       displaySegmentDisplay_4_d, displaySegmentDisplay_4_e, displaySegmentDisplay_4_f,
       displaySegmentDisplay_4_g;

  display_displayTransistion displaySegmentDisplay_1 (
    .B4(S0[4]), .B3(S0[3]), .B2(S0[2]), .B1(S0[1]), .B0(S0[0]), .enable(S0[5]), .noConvert(S0[6]),
    .a(displaySegmentDisplay_1_a), .b(displaySegmentDisplay_1_b), .c(displaySegmentDisplay_1_c),
    .d(displaySegmentDisplay_1_d), .e(displaySegmentDisplay_1_e), .f(displaySegmentDisplay_1_f),
    .g(displaySegmentDisplay_1_g));
  display_displayTransistion displaySegmentDisplay_2 (
    .B4(S1[4]), .B3(S1[3]), .B2(S1[2]), .B1(S1[1]), .B0(S1[0]), .enable(S1[5]), .noConvert(S1[6]),
    .a(displaySegmentDisplay_2_a), .b(displaySegmentDisplay_2_b), .c(displaySegmentDisplay_2_c),
    .d(displaySegmentDisplay_2_d), .e(displaySegmentDisplay_2_e), .f(displaySegmentDisplay_2_f),
    .g(displaySegmentDisplay_2_g));
  display_displayTransistion displaySegmentDisplay_3 (
    .B4(S2[4]), .B3(S2[3]), .B2(S2[2]), .B1(S2[1]), .B0(S2[0]), .enable(S2[5]), .noConvert(S2[6]),
    .a(displaySegmentDisplay_3_a), .b(displaySegmentDisplay_3_b), .c(displaySegmentDisplay_3_c),
    .d(displaySegmentDisplay_3_d), .e(displaySegmentDisplay_3_e), .f(displaySegmentDisplay_3_f),
    .g(displaySegmentDisplay_3_g));
  display_displayTransistion displaySegmentDisplay_4 (
    .B4(S3[4]), .B3(S3[3]), .B2(S3[2]), .B1(S3[1]), .B0(S3[0]), .enable(S3[5]), .noConvert(S3[6]),
    .a(displaySegmentDisplay_4_a), .b(displaySegmentDisplay_4_b), .c(displaySegmentDisplay_4_c),
    .d(displaySegmentDisplay_4_d), .e(displaySegmentDisplay_4_e), .f(displaySegmentDisplay_4_f),
    .g(displaySegmentDisplay_4_g));
  display_displayTransistion display_5 (
    .B4(S4[4]), .B3(S4[3]), .B2(S4[2]), .B1(S4[1]), .B0(S4[0]), .enable(S4[5]), .noConvert(S4[6]),
    .a(display_5_a), .b(display_5_b), .c(display_5_c), .d(display_5_d), .e(display_5_e), .f(display_5_f),
    .g(display_5_g));
  display_displayTransistion display_6 (
    .B4(S5[4]), .B3(S5[3]), .B2(S5[2]), .B1(S5[1]), .B0(S5[0]), .enable(S5[5]), .noConvert(S5[6]),
    .a(display_6_a), .b(display_6_b), .c(display_6_c), .d(display_6_d), .e(display_6_e), .f(display_6_f),
    .g(display_6_g));
  _7_Segment_Display L_7_Segment_Display_1 (
    .g(displaySegmentDisplay_1_g), .f(displaySegmentDisplay_1_f), .a(displaySegmentDisplay_1_a),
    .b(displaySegmentDisplay_1_b), .e(displaySegmentDisplay_1_e), .d(displaySegmentDisplay_1_d),
    .c(displaySegmentDisplay_1_c), .dp(pointData[0]));
  _7_Segment_Display L_7_Segment_Display_2 (
    .g(displaySegmentDisplay_2_g), .f(displaySegmentDisplay_2_f), .a(displaySegmentDisplay_2_a),
    .b(displaySegmentDisplay_2_b), .e(displaySegmentDisplay_2_e), .d(displaySegmentDisplay_2_d),
    .c(displaySegmentDisplay_2_c), .dp(pointData[1]));
  _7_Segment_Display L_7_Segment_Display_3 (
    .g(displaySegmentDisplay_3_g), .f(displaySegmentDisplay_3_f), .a(displaySegmentDisplay_3_a),
    .b(displaySegmentDisplay_3_b), .e(displaySegmentDisplay_3_e), .d(displaySegmentDisplay_3_d),
    .c(displaySegmentDisplay_3_c), .dp(pointData[2]));
  _7_Segment_Display L_7_Segment_Display_4 (
    .g(displaySegmentDisplay_4_g), .f(displaySegmentDisplay_4_f), .a(displaySegmentDisplay_4_a),
    .b(displaySegmentDisplay_4_b), .e(displaySegmentDisplay_4_e), .d(displaySegmentDisplay_4_d),
    .c(displaySegmentDisplay_4_c), .dp(pointData[3]));
  _7_Segment_Display L_7_Segment_Display_5 (
    .g(display_5_g), .f(display_5_f), .a(display_5_a), .b(display_5_b), .e(display_5_e), .d(display_5_d),
    .c(display_5_c), .dp(pointData[4]));
  _7_Segment_Display L_7_Segment_Display_6 (
    .g(display_6_g), .f(display_6_f), .a(display_6_a), .b(display_6_b), .e(display_6_e), .d(display_6_d),
    .c(display_6_c), .dp(pointData[5]));
endmodule

module display_displayTransistion (
  input  B4,
  input  B3,
  input  B2,
  input  B1,
  input  B0,
  input  enable,
  input  noConvert,
  output a,
  output b,
  output c,
  output d,
  output e,
  output f,
  output g
);

  wire and_1_out, and_2_out, and_3_out, and_4_out, and_5_out, and_6_out, and_7_out, and_8_out, and_9_out,
       and_10_out, and_11_out, and_12_out, and_13_out, and_14_out, and_15_out, and_16_out, and_17_out,
       and_18_out, and_19_out, and_20_out, and_21_out, and_22_out, and_23_out, and_24_out, and_25_out,
       and_26_out, and_27_out, and_28_out, and_29_out, and_30_out, and_31_out, and_32_out, and_33_out,
       and_34_out, and_35_out, and_36_out, and_37_out, and_38_out, and_39_out, and_40_out, and_41_out,
       and_42_out, and_43_out, and_44_out, and_45_out, and_46_out, and_47_out, and_48_out, and_49_out,
       and_50_out, and_51_out, and_52_out, and_53_out, and_54_out, and_55_out, and_56_out, and_57_out,
       and_58_out, and_59_out, and_60_out, and_61_out, not_1_out, not_2_out, not_3_out, not_4_out, not_5_out,
       not_6_out, not_7_out, not_8_out, not_9_out, not_10_out, not_11_out, not_12_out, not_13_out,
       not_14_out, not_15_out, not_16_out, not_17_out, not_18_out, not_19_out, not_20_out, not_21_out,
       not_22_out, not_23_out, not_24_out, not_25_out, not_26_out, not_27_out, not_28_out, not_29_out,
       not_30_out, not_31_out, not_32_out, not_33_out, not_34_out, not_35_out, not_36_out, not_37_out,
       not_38_out, not_39_out, not_40_out, not_41_out, not_42_out, not_43_out, not_44_out, not_45_out,
       not_46_out, not_47_out, not_48_out, not_49_out, not_50_out, not_51_out, not_52_out, not_53_out,
       not_54_out, not_55_out, not_56_out, not_57_out, not_58_out, not_59_out, not_60_out, not_61_out,
       not_62_out, not_63_out, not_64_out, not_65_out, not_66_out, not_67_out, not_68_out, not_69_out,
       not_70_out, not_71_out, not_72_out, not_73_out, not_74_out, not_75_out, not_76_out, not_77_out,
       not_78_out, not_79_out, not_80_out, not_81_out, not_82_out, not_83_out, not_84_out, not_85_out,
       not_86_out, not_87_out, not_88_out, not_89_out, not_90_out, not_91_out, not_92_out, or_1_out,
       or_2_out, or_3_out, or_4_out, or_5_out, or_6_out, or_7_out;

  not not_1 (not_1_out, B2);
  not not_2 (not_2_out, B1);
  not not_3 (not_3_out, B0);
  not not_4 (not_4_out, B4);
  not not_5 (not_5_out, B3);
  not not_6 (not_6_out, B3);
  not not_7 (not_7_out, B2);
  not not_8 (not_8_out, B3);
  not not_9 (not_9_out, B1);
  not not_10 (not_10_out, B4);
  not not_11 (not_11_out, B3);
  not not_12 (not_12_out, B0);
  not not_13 (not_13_out, B4);
  not not_14 (not_14_out, B0);
  not not_15 (not_15_out, B2);
  not not_16 (not_16_out, B1);
  not not_17 (not_17_out, B2);
  not not_18 (not_18_out, B0);
  not not_19 (not_19_out, B4);
  not not_20 (not_20_out, B3);
  not not_21 (not_21_out, B2);
  not not_22 (not_22_out, B4);
  not not_23 (not_23_out, B3);
  not not_24 (not_24_out, B1);
  not not_25 (not_25_out, B0);
  not not_26 (not_26_out, B2);
  not not_27 (not_27_out, B1);
  not not_28 (not_28_out, B4);
  not not_29 (not_29_out, B3);
  not not_30 (not_30_out, B2);
  not not_31 (not_31_out, B0);
  not not_32 (not_32_out, B1);
  not not_33 (not_33_out, B0);
  not not_34 (not_34_out, B4);
  not not_35 (not_35_out, B3);
  not not_36 (not_36_out, B1);
  not not_37 (not_37_out, B3);
  not not_38 (not_38_out, B2);
  not not_39 (not_39_out, B1);
  not not_40 (not_40_out, B3);
  not not_41 (not_41_out, B1);
  not not_42 (not_42_out, B3);
  not not_43 (not_43_out, B4);
  not not_44 (not_44_out, B2);
  not not_45 (not_45_out, B1);
  not not_46 (not_46_out, B4);
  not not_47 (not_47_out, B3);
  not not_48 (not_48_out, B2);
  not not_49 (not_49_out, B0);
  not not_50 (not_50_out, B4);
  not not_51 (not_51_out, B3);
  not not_52 (not_52_out, B0);
  not not_53 (not_53_out, B4);
  not not_54 (not_54_out, B2);
  not not_55 (not_55_out, B4);
  not not_56 (not_56_out, B1);
  not not_57 (not_57_out, B4);
  not not_58 (not_58_out, B1);
  not not_59 (not_59_out, B2);
  not not_60 (not_60_out, B1);
  not not_61 (not_61_out, B0);
  not not_62 (not_62_out, B3);
  not not_63 (not_63_out, B1);
  not not_64 (not_64_out, B0);
  not not_65 (not_65_out, B2);
  not not_66 (not_66_out, B0);
  not not_67 (not_67_out, B3);
  not not_68 (not_68_out, B0);
  not not_69 (not_69_out, B2);
  not not_70 (not_70_out, B4);
  not not_71 (not_71_out, B3);
  not not_72 (not_72_out, B1);
  not not_73 (not_73_out, B0);
  not not_74 (not_74_out, B1);
  not not_75 (not_75_out, B0);
  not not_76 (not_76_out, B4);
  not not_77 (not_77_out, B3);
  not not_78 (not_78_out, B1);
  not not_79 (not_79_out, B0);
  not not_80 (not_80_out, B2);
  not not_81 (not_81_out, B2);
  not not_82 (not_82_out, B4);
  not not_83 (not_83_out, B2);
  not not_84 (not_84_out, B4);
  not not_85 (not_85_out, B0);
  not not_86 (not_86_out, B4);
  not not_87 (not_87_out, B3);
  not not_88 (not_88_out, B1);
  not not_89 (not_89_out, B2);
  not not_90 (not_90_out, B1);
  not not_91 (not_91_out, B4);
  not not_92 (not_92_out, B2);
  and and_1 (and_1_out, not_1_out, not_2_out, not_3_out);
  and and_2 (and_2_out, not_4_out, not_5_out, B1);
  and and_3 (and_3_out, not_6_out, not_7_out, B1, B0);
  and and_4 (and_4_out, not_8_out, B2, not_9_out, B0);
  and and_5 (and_5_out, not_10_out, B2, B1);
  and and_6 (and_6_out, not_11_out, B2, B1, not_12_out);
  and and_7 (and_7_out, not_13_out, B3, not_14_out);
  and and_8 (and_8_out, B3, not_15_out, not_16_out);
  and and_9 (and_9_out, B3, not_17_out, not_18_out);
  and and_10 (and_10_out, not_19_out, not_20_out, not_21_out);
  and and_11 (and_11_out, not_22_out, not_23_out, not_24_out, not_25_out);
  and and_12 (and_12_out, not_26_out, not_27_out, B0);
  and and_13 (and_13_out, not_28_out, not_29_out, B1, B0);
  and and_14 (and_14_out, B3, not_30_out, not_31_out);
  and and_15 (and_15_out, B3, not_32_out, B0);
  and and_16 (and_16_out, B4, B2, B1, not_33_out);
  and and_17 (and_17_out, B4, B3, B2);
  and and_18 (and_18_out, not_34_out, not_35_out, not_36_out);
  and and_19 (and_19_out, not_37_out, not_38_out, not_39_out);
  and and_20 (and_20_out, not_40_out, B0);
  and and_21 (and_21_out, not_41_out, B0);
  and and_22 (and_22_out, not_42_out, B2, B1);
  and and_23 (and_23_out, not_43_out, B3, not_44_out);
  and and_24 (and_24_out, B4, B2, B0);
  and and_25 (and_25_out, B4, B3, B2, not_45_out);
  and and_26 (and_26_out, not_46_out, not_47_out, not_48_out, not_49_out);
  and and_27 (and_27_out, not_50_out, not_51_out, B1, not_52_out);
  and and_28 (and_28_out, not_53_out, not_54_out, B1, B0);
  and and_29 (and_29_out, not_55_out, B2, not_56_out, B0);
  and and_30 (and_30_out, not_57_out, B3, not_58_out);
  and and_31 (and_31_out, B3, not_59_out, B1, B0);
  and and_32 (and_32_out, B3, B2, not_60_out);
  and and_33 (and_33_out, B3, B2, not_61_out);
  and and_34 (and_34_out, B4, not_62_out, not_63_out, not_64_out);
  and and_35 (and_35_out, B4, B2, B1, B0);
  and and_36 (and_36_out, not_65_out, not_66_out);
  and and_37 (and_37_out, not_67_out, B1, not_68_out);
  and and_38 (and_38_out, B3, not_69_out, B1);
  and and_39 (and_39_out, not_70_out, B3, B2);
  and and_40 (and_40_out, B4, not_71_out);
  and and_41 (and_41_out, B4, not_72_out, not_73_out);
  and and_42 (and_42_out, not_74_out, not_75_out);
  and and_43 (and_43_out, not_76_out, not_77_out, B2, not_78_out);
  and and_44 (and_44_out, B2, not_79_out);
  and and_45 (and_45_out, B3, not_80_out);
  and and_46 (and_46_out, B3, B1);
  and and_47 (and_47_out, B4, not_81_out);
  and and_48 (and_48_out, B4, B3);
  and and_49 (and_49_out, not_82_out, not_83_out, B1, enable);
  and and_50 (and_50_out, not_84_out, B1, not_85_out, enable);
  and and_51 (and_51_out, not_86_out, not_87_out, B2, not_88_out, enable);
  and and_52 (and_52_out, B3, not_89_out, not_90_out, enable);
  and and_53 (and_53_out, not_91_out, B3, B0, enable);
  and and_54 (and_54_out, B4, not_92_out, B0, enable);
  and and_55 (and_55_out, B4, B1, B0, enable);
  or or_1 (or_1_out, and_1_out, and_2_out, and_3_out, and_4_out, and_5_out, and_6_out, and_7_out, and_8_out, and_9_out);
  or or_2 (or_2_out, and_10_out, and_11_out, and_12_out, and_13_out, and_14_out, and_15_out, and_16_out, and_17_out);
  or or_3 (or_3_out, and_18_out, and_19_out, and_20_out, and_21_out, and_22_out, and_23_out, and_24_out, and_25_out);
  or or_4 (or_4_out, and_26_out, and_27_out, and_28_out, and_29_out, and_30_out, and_31_out, and_32_out, and_33_out, and_34_out, and_35_out);
  or or_5 (or_5_out, and_36_out, and_37_out, and_38_out, and_39_out, and_40_out, and_41_out);
  or or_6 (or_6_out, and_42_out, and_43_out, and_44_out, and_45_out, and_46_out, and_47_out, and_48_out);
  or or_7 (or_7_out, and_49_out, and_50_out, and_51_out, and_52_out, and_53_out, and_54_out, and_55_out);
  and and_56 (and_56_out, or_1_out, enable);
  and and_57 (and_57_out, or_2_out, enable);
  and and_58 (and_58_out, or_3_out, enable);
  and and_59 (and_59_out, or_4_out, enable);
  and and_60 (and_60_out, or_5_out, enable);
  and and_61 (and_61_out, or_6_out, enable);
  Multiplexer #(.enable("false")) multiplexer_1 (.in0(and_57_out), .in1(B1), .out(b), .sel(noConvert));
  Multiplexer #(.enable("false")) multiplexer_2 (.in0(and_58_out), .in1(B0), .out(c), .sel(noConvert));
  Multiplexer #(.enable("false")) multiplexer_3 (.in0(and_59_out), .in1(1'b0), .out(d), .sel(noConvert));
  Multiplexer #(.enable("false")) multiplexer_4 (.in0(and_60_out), .in1(B3), .out(e), .sel(noConvert));
  Multiplexer #(.enable("false")) multiplexer_5 (.in0(and_61_out), .in1(B2), .out(f), .sel(noConvert));
  Multiplexer #(.enable("false")) multiplexer_6 (.in0(or_7_out), .in1(1'b0), .out(g), .sel(noConvert));
  Multiplexer #(.enable("false")) multiplexer_7 (.in0(and_56_out), .in1(1'b0), .out(a), .sel(noConvert));
endmodule

module display_displayManager (
  input  [29:0] segmentData1,
  input  [5:0] bitSelectedSegment1,
  input  [29:0] segmentData2,
  input  [5:0] bitSelectedSegment2,
  input  [29:0] segmentData3,
  input  [5:0] bitSelectedSegment3,
  input  [29:0] segmentData4,
  input  [5:0] bitSelectedSegment4,
  input  [29:0] segmentData5,
  input  [5:0] bitSelectedSegment5,
  input  [29:0] segmentData6,
  input  [5:0] bitSelectedSegment6,
  input  [29:0] segmentData7,
  input  [5:0] bitSelectedSegment7,
  input  [29:0] segmentData8,
  input  [5:0] bitSelectedSegment8,
  input  [29:0] segmentData9,
  input  [5:0] bitSelectedSegment9,
  input  [3:0] state,
  input  alarmSignal,
  input  reset,
  input  alarmPoint,
  output [6:0] s0,
  output [6:0] s1,
  output [6:0] s2,
  output [6:0] s3,
  output [6:0] s4,
  output [6:0] s5,
  output [5:0] pointDataSelected
);

  wire clock_1_out, comparator_1_eq, not_1_out, tools_superAdder_1_carryout;
  wire [4:4] clock_2_out;
  wire [5:0] bitSeclection_1_q0, multiplexer_1_out, multiplexer_3_out, multiplexer_4_out, multiplexer_7_out;
  wire [29:0] multiplexer_2_out;

  Clock #(.highDuration(2), .lowDuration(199998)) clock_1 (.out(clock_1_out));
  Multiplexer #(.width(6), .enable("false")) multiplexer_1 (
    .in0({6{1'b0}}), .in1(6'b010100), .out(multiplexer_1_out), .sel(alarmPoint));
  tools_superAdder tools_superAdder_1 (
    .enable(1'b1), .carryIn(1'b1), .lastNumber(5'b00101), .clockIn(clock_1_out), .setBits(5'b00101),
    .setSignal(reset), .reset(alarmSignal), .stopEnd(1'b1), .carryOut(tools_superAdder_1_carryout));  // open: outBits
  Multiplexer #(.select(4), .width(30), .enable("false")) multiplexer_2 (
    .in0(segmentData1), .in1(segmentData2), .in2(segmentData3), .in3(segmentData4), .in4(segmentData5),
    .in5(segmentData6), .in6(segmentData7), .in7(segmentData8), .in8(segmentData9), .in9({30{1'b0}}),
    .in10({30{1'b0}}), .in11({30{1'b0}}), .in12({30{1'b0}}), .in13({30{1'b0}}), .in14({30{1'b0}}),
    .in15({30{1'b0}}), .out(multiplexer_2_out), .sel(state));
  Multiplexer #(.select(4), .width(6), .enable("false")) multiplexer_3 (
    .in0(bitSelectedSegment1), .in1(bitSelectedSegment2), .in2(bitSelectedSegment3),
    .in3(bitSelectedSegment4), .in4(bitSelectedSegment5), .in5(bitSelectedSegment6),
    .in6(bitSelectedSegment7), .in7(bitSelectedSegment8), .in8(bitSelectedSegment9), .in9({6{1'b0}}),
    .in10({6{1'b0}}), .in11({6{1'b0}}), .in12({6{1'b0}}), .in13({6{1'b0}}), .in14({6{1'b0}}),
    .in15({6{1'b0}}), .out(multiplexer_3_out), .sel(state));
  Multiplexer #(.select(4), .width(6), .enable("false")) multiplexer_4 (
    .in0(6'b010100), .in1(6'b010100), .in2(multiplexer_1_out), .in3(6'b010100), .in4({6{1'b0}}),
    .in5(6'b010100), .in6(6'b010100), .in7(6'b010100), .in8({6{1'b0}}), .in9({6{1'b0}}), .in10({6{1'b0}}),
    .in11({6{1'b0}}), .in12({6{1'b0}}), .in13({6{1'b0}}), .in14({6{1'b0}}), .in15({6{1'b0}}),
    .out(multiplexer_4_out), .sel(state));
  not not_1 (not_1_out, tools_superAdder_1_carryout);
  Multiplexer #(.width(30), .enable("false")) multiplexer_5 (
    .in0(multiplexer_2_out), .in1(30'haa2b55), .out({s5[4:0], s4[4:0], s3[4:0], s2[4:0], s1[4:0], s0[4:0]}),
    .sel(not_1_out));
  Comparator #(.width(4)) comparator_1 (.a(state), .b(4'b0100), .eq(comparator_1_eq));  // open: gt, lt
  Multiplexer #(.width(6), .enable("false")) multiplexer_6 (
    .in0(multiplexer_4_out), .in1({6{1'b0}}), .out(pointDataSelected), .sel(not_1_out));
  Comparator #(.width(4)) comparator_2 (.a(state), .b(4'b1000), .eq(s0[6]));  // open: gt, lt
  Clock #(.highDuration(100000), .lowDuration(100000)) clock_2 (.out(clock_2_out[4]));
  display_bitSeclection bitSeclection_1 (
    .b0(multiplexer_3_out[0]), .b1(multiplexer_3_out[1]), .b2(multiplexer_3_out[2]),
    .b3(multiplexer_3_out[3]), .b4(multiplexer_3_out[4]), .b5(multiplexer_3_out[5]), .clock(clock_2_out[4]),
    .q0(bitSeclection_1_q0[0]), .q1(bitSeclection_1_q0[1]), .q2(bitSeclection_1_q0[2]),
    .q3(bitSeclection_1_q0[3]), .q4(bitSeclection_1_q0[4]), .q5(bitSeclection_1_q0[5]));
  Multiplexer #(.width(6), .enable("false")) multiplexer_7 (
    .in0(bitSeclection_1_q0), .in1(6'b000111), .out(multiplexer_7_out), .sel(comparator_1_eq));
  Multiplexer #(.width(6), .enable("false")) multiplexer_8 (
    .in0(multiplexer_7_out), .in1({1'b0, {5{clock_2_out[4]}}}),
    .out({s5[5], s4[5], s3[5], s2[5], s1[5], s0[5]}), .sel(not_1_out));

  assign s1[6] = s0[6];
  assign s2[6] = s0[6];
  assign s3[6] = s0[6];
  assign s4[6] = s0[6];
  assign s5[6] = 1'b0;
endmodule

module display_bitSeclection (
  input  b0,
  input  b1,
  input  b2,
  input  b3,
  input  b4,
  input  b5,
  input  clock,
  output q0,
  output q1,
  output q2,
  output q3,
  output q4,
  output q5
);

  or or_1 (q0, ~b0, clock);  // OR_Gate
  or or_2 (q1, ~b1, clock);  // OR_Gate
  or or_3 (q2, ~b2, clock);  // OR_Gate
  or or_4 (q3, ~b3, clock);  // OR_Gate
  or or_5 (q4, ~b4, clock);  // OR_Gate
  or or_6 (q5, ~b5, clock);  // OR_Gate
endmodule

module musique_main (
  input  playHarry,
  input  playMario,
  input  reset,
  output signalOutput,
  output ground
);

  wire and_1_out, and_2_out, clock_1_out, clock_2_out, clock_3_out, clock_4_out, clock_5_out, clock_6_out,
       clock_7_out, clock_8_out, clock_9_out, clock_10_out, clock_11_out, clock_12_out, clock_13_out,
       clock_14_out, clock_15_out, clock_16_out, clock_17_out, clock_18_out, clock_19_out, clock_20_out,
       clock_21_out, clock_22_out, clock_23_out, clock_24_out, clock_25_out, d_ff_5_q,
       harryPotterFSMHarryPotterLogicTransistion_1_d0, harryPotterFSMHarryPotterLogicTransistion_1_d1,
       harryPotterFSMHarryPotterLogicTransistion_1_d2, harryPotterFSMHarryPotterLogicTransistion_1_d3,
       harryPotterFSMHarryPotterLogicTransistion_1_reset, multiplexer_1_out, multiplexer_2_out, or_1_out,
       or_2_out, or_3_out, play, playHarryOut, playMarioOut, superAdder_2_carryout,
       tools_superAdder_1_carryout;
  wire [2:0] tools_superAdder_1_outbits;
  wire [3:0] d_ff_4_q;
  wire [4:0] superAdder_1_outbits;
  wire [4:3] tools_superAdder_1_outbits_2;

  Clock #(.highDuration(2), .lowDuration(199998)) clock_1 (.out(clock_1_out));
  Clock #(.highDuration(2), .lowDuration(29998)) clock_2 (.out(clock_2_out));
  tools_superAdder superAdder_2 (
    .enable(1'b1), .carryIn(1'b1), .lastNumber(5'b01111), .clockIn(clock_1_out), .setBits(5'b01111),
    .setSignal(reset), .reset(playHarry), .stopEnd(1'b1), .carryOut(superAdder_2_carryout));  // open: outBits
  or or_1 (or_1_out, playHarry, playMario);
  Clock clock_3 (.out(clock_3_out));
  S_R_Flip_Flop s_r_ff_1 (.S(or_1_out), .R(reset), .clk(clock_3_out), .Q(play), .reset(reset));  // open: Qn, preset
  tools_superAdder tools_superAdder_1 (
    .enable(1'b1), .carryIn(1'b1), .lastNumber(5'b00110), .clockIn(clock_2_out), .setBits(5'b00110),
    .setSignal(reset), .reset(playMario), .stopEnd(1'b1),
    .outBits({tools_superAdder_1_outbits_2, tools_superAdder_1_outbits}),
    .carryOut(tools_superAdder_1_carryout));
  not not_1 (playMarioOut, tools_superAdder_1_carryout);
  not not_2 (playHarryOut, superAdder_2_carryout);
  or or_2 (or_2_out, reset, playHarry, d_ff_5_q);
  Clock #(.highDuration(2), .lowDuration(39998)) clock_4 (.out(clock_4_out));
  tools_superAdder superAdder_1 (
    .enable(playHarryOut), .carryIn(playHarryOut), .lastNumber(5'b00111), .clockIn(clock_4_out),
    .setBits({5{1'b0}}), .setSignal(1'b0), .reset(or_2_out), .stopEnd(1'b0), .outBits(superAdder_1_outbits));  // open: carryOut
  musique_harryPotterLogicTransistion harryPotterFSMHarryPotterLogicTransistion_1 (
    .C3(d_ff_4_q[3]), .C2(d_ff_4_q[2]), .C1(d_ff_4_q[1]), .C0(d_ff_4_q[0]), .T2(superAdder_1_outbits[2]),
    .T1(superAdder_1_outbits[1]), .T0(superAdder_1_outbits[0]),
    .D3(harryPotterFSMHarryPotterLogicTransistion_1_d3), .D2(harryPotterFSMHarryPotterLogicTransistion_1_d2),
    .D1(harryPotterFSMHarryPotterLogicTransistion_1_d1), .D0(harryPotterFSMHarryPotterLogicTransistion_1_d0),
    .Reset(harryPotterFSMHarryPotterLogicTransistion_1_reset));
  Clock clock_5 (.out(clock_5_out));
  D_Flip_Flop d_ff_1 (
    .D(harryPotterFSMHarryPotterLogicTransistion_1_d3), .clk(clock_5_out), .Q(d_ff_4_q[3]), .reset(playHarry));  // open: Qn, preset
  D_Flip_Flop d_ff_2 (
    .D(harryPotterFSMHarryPotterLogicTransistion_1_d2), .clk(clock_5_out), .Q(d_ff_4_q[2]), .reset(playHarry));  // open: Qn, preset
  D_Flip_Flop d_ff_3 (
    .D(harryPotterFSMHarryPotterLogicTransistion_1_d1), .clk(clock_5_out), .Q(d_ff_4_q[1]), .reset(playHarry));  // open: Qn, preset
  D_Flip_Flop d_ff_4 (
    .D(harryPotterFSMHarryPotterLogicTransistion_1_d0), .clk(clock_5_out), .Q(d_ff_4_q[0]), .reset(playHarry));  // open: Qn, preset
  D_Flip_Flop d_ff_5 (
    .D(harryPotterFSMHarryPotterLogicTransistion_1_reset), .clk(clock_5_out), .Q(d_ff_5_q), .reset(playHarry));  // open: Qn, preset
  Clock #(.highDuration(162), .lowDuration(162)) clock_6 (.out(clock_6_out));
  Clock #(.highDuration(121), .lowDuration(121)) clock_7 (.out(clock_7_out));
  Clock #(.highDuration(102), .lowDuration(102)) clock_8 (.out(clock_8_out));
  Clock #(.highDuration(115), .lowDuration(115)) clock_9 (.out(clock_9_out));
  Clock #(.highDuration(121), .lowDuration(121)) clock_10 (.out(clock_10_out));
  Clock #(.highDuration(81), .lowDuration(81)) clock_11 (.out(clock_11_out));
  Clock #(.highDuration(91), .lowDuration(91)) clock_12 (.out(clock_12_out));
  Clock #(.highDuration(108), .lowDuration(108)) clock_13 (.out(clock_13_out));
  Clock #(.highDuration(121), .lowDuration(121)) clock_14 (.out(clock_14_out));
  Clock #(.highDuration(102), .lowDuration(102)) clock_15 (.out(clock_15_out));
  Clock #(.highDuration(115), .lowDuration(115)) clock_16 (.out(clock_16_out));
  Clock #(.highDuration(129), .lowDuration(129)) clock_17 (.out(clock_17_out));
  Clock #(.highDuration(115), .lowDuration(115)) clock_18 (.out(clock_18_out));
  Clock #(.highDuration(162), .lowDuration(162)) clock_19 (.out(clock_19_out));
  Clock #(.highDuration(152), .lowDuration(152)) clock_20 (.out(clock_20_out));
  Clock #(.highDuration(128), .lowDuration(128)) clock_21 (.out(clock_21_out));
  Clock #(.highDuration(76), .lowDuration(76)) clock_22 (.out(clock_22_out));
  Clock #(.highDuration(96), .lowDuration(96)) clock_23 (.out(clock_23_out));
  Clock #(.highDuration(85), .lowDuration(85)) clock_24 (.out(clock_24_out));
  Clock #(.highDuration(64), .lowDuration(64)) clock_25 (.out(clock_25_out));
  Multiplexer #(.select(3), .enable("false")) multiplexer_1 (
    .in0(clock_20_out), .in1(clock_21_out), .in2(clock_22_out), .in3(clock_23_out), .in4(clock_24_out),
    .in5(clock_25_out), .in6(1'b0), .in7(1'b0), .out(multiplexer_1_out), .sel(tools_superAdder_1_outbits));
  Multiplexer #(.select(4), .enable("false")) multiplexer_2 (
    .in0(clock_6_out), .in1(clock_7_out), .in2(clock_8_out), .in3(clock_9_out), .in4(clock_10_out),
    .in5(clock_11_out), .in6(clock_12_out), .in7(clock_13_out), .in8(clock_14_out), .in9(clock_15_out),
    .in10(clock_16_out), .in11(clock_17_out), .in12(clock_18_out), .in13(clock_19_out), .in14(1'b0),
    .in15(1'b0), .out(multiplexer_2_out), .sel(d_ff_4_q));
  and and_1 (and_1_out, multiplexer_2_out, playHarryOut);
  and and_2 (and_2_out, playMarioOut, multiplexer_1_out);
  or or_3 (or_3_out, and_1_out, and_2_out);
  and and_3 (signalOutput, or_3_out, play);

  assign ground = 1'b0;
endmodule

module musique_harryPotterLogicTransistion (
  input  C3,
  input  C2,
  input  C1,
  input  C0,
  input  T2,
  input  T1,
  input  T0,
  output D3,
  output D2,
  output D1,
  output D0,
  output Reset
);

  wire and_1_out, and_2_out, and_3_out, and_4_out, and_5_out, and_6_out, and_7_out, and_8_out, and_9_out,
       and_10_out, and_11_out, and_12_out, and_13_out, and_14_out, and_15_out, and_16_out, and_17_out,
       and_18_out, and_19_out, and_20_out, and_21_out, and_22_out, and_23_out, and_24_out, and_25_out,
       and_26_out, and_27_out, and_28_out, and_29_out, and_30_out, and_31_out, and_32_out, and_33_out,
       and_34_out, and_35_out, and_36_out, and_37_out, and_38_out, and_39_out, and_40_out, and_41_out,
       and_42_out, and_43_out, and_44_out, and_45_out, and_46_out, and_47_out, and_48_out, and_49_out,
       and_50_out, and_51_out, and_52_out, and_53_out, and_54_out, and_55_out, and_56_out, not_1_out,
       not_2_out, not_3_out, not_4_out, not_5_out, not_6_out, not_7_out, not_8_out, not_9_out, not_10_out,
       not_11_out, not_12_out, not_13_out, not_14_out, not_15_out, not_16_out, not_17_out, not_18_out,
       not_19_out, not_20_out, not_21_out, not_22_out, not_23_out, not_24_out, not_25_out, not_26_out,
       not_27_out, not_28_out, not_29_out, not_30_out, not_31_out, not_32_out, not_33_out, not_34_out,
       not_35_out, not_36_out, not_37_out, not_38_out, not_39_out, not_40_out, not_41_out, not_42_out,
       not_43_out, not_44_out, not_45_out, not_46_out, not_47_out, not_48_out, not_49_out, not_50_out,
       not_51_out, not_52_out, not_53_out, not_54_out, not_55_out, not_56_out, not_57_out, not_58_out,
       not_59_out, not_60_out, not_61_out, not_62_out, not_63_out, not_64_out, not_65_out, not_66_out,
       not_67_out, not_68_out, not_69_out, not_70_out, not_71_out, not_72_out, not_73_out, not_74_out,
       not_75_out, not_76_out, not_77_out, not_78_out, not_79_out, not_80_out, not_81_out, not_82_out,
       not_83_out, not_84_out, not_85_out, not_86_out, not_87_out, not_88_out, not_89_out, not_90_out,
       not_91_out, not_92_out, not_93_out, not_94_out, not_95_out, not_96_out, not_97_out, not_98_out,
       not_99_out, not_100_out, not_101_out, not_102_out, not_103_out, not_104_out, not_105_out, not_106_out,
       not_107_out, not_108_out, not_109_out, not_110_out, not_111_out, not_112_out, not_113_out,
       not_114_out, not_115_out, not_116_out, not_117_out, not_118_out, not_119_out, not_120_out,
       not_121_out, not_122_out, not_123_out, not_124_out, not_125_out;

  not not_1 (not_1_out, T1);
  not not_2 (not_2_out, C2);
  not not_3 (not_3_out, C0);
  not not_4 (not_4_out, T2);
  not not_5 (not_5_out, T0);
  not not_6 (not_6_out, C3);
  not not_7 (not_7_out, T2);
  not not_8 (not_8_out, T0);
  not not_9 (not_9_out, C3);
  not not_10 (not_10_out, C1);
  not not_11 (not_11_out, C0);
  not not_12 (not_12_out, T2);
  not not_13 (not_13_out, T0);
  not not_14 (not_14_out, T1);
  not not_15 (not_15_out, T0);
  not not_16 (not_16_out, C3);
  not not_17 (not_17_out, C2);
  not not_18 (not_18_out, T2);
  not not_19 (not_19_out, C3);
  not not_20 (not_20_out, T1);
  not not_21 (not_21_out, T0);
  not not_22 (not_22_out, C0);
  not not_23 (not_23_out, T2);
  not not_24 (not_24_out, T1);
  not not_25 (not_25_out, C2);
  not not_26 (not_26_out, C3);
  not not_27 (not_27_out, T2);
  not not_28 (not_28_out, T0);
  not not_29 (not_29_out, T2);
  not not_30 (not_30_out, T0);
  not not_31 (not_31_out, C2);
  not not_32 (not_32_out, T2);
  not not_33 (not_33_out, T1);
  not not_34 (not_34_out, C3);
  not not_35 (not_35_out, C2);
  not not_36 (not_36_out, C1);
  not not_37 (not_37_out, T2);
  not not_38 (not_38_out, T0);
  not not_39 (not_39_out, C3);
  not not_40 (not_40_out, C2);
  not not_41 (not_41_out, T1);
  not not_42 (not_42_out, C3);
  not not_43 (not_43_out, C1);
  not not_44 (not_44_out, T1);
  not not_45 (not_45_out, T2);
  not not_46 (not_46_out, T1);
  not not_47 (not_47_out, T0);
  not not_48 (not_48_out, C2);
  not not_49 (not_49_out, C1);
  not not_50 (not_50_out, C3);
  not not_51 (not_51_out, C2);
  not not_52 (not_52_out, T2);
  not not_53 (not_53_out, T1);
  not not_54 (not_54_out, C2);
  not not_55 (not_55_out, C3);
  not not_56 (not_56_out, C1);
  not not_57 (not_57_out, T1);
  not not_58 (not_58_out, T0);
  not not_59 (not_59_out, T2);
  not not_60 (not_60_out, C3);
  not not_61 (not_61_out, C0);
  not not_62 (not_62_out, T1);
  not not_63 (not_63_out, T0);
  not not_64 (not_64_out, C2);
  not not_65 (not_65_out, C1);
  not not_66 (not_66_out, T2);
  not not_67 (not_67_out, C1);
  not not_68 (not_68_out, T0);
  not not_69 (not_69_out, C2);
  not not_70 (not_70_out, T2);
  not not_71 (not_71_out, T0);
  not not_72 (not_72_out, C1);
  not not_73 (not_73_out, T2);
  not not_74 (not_74_out, T0);
  not not_75 (not_75_out, C3);
  not not_76 (not_76_out, C2);
  not not_77 (not_77_out, C1);
  not not_78 (not_78_out, C0);
  not not_79 (not_79_out, T2);
  not not_80 (not_80_out, T0);
  not not_81 (not_81_out, C3);
  not not_82 (not_82_out, C2);
  not not_83 (not_83_out, C1);
  not not_84 (not_84_out, T2);
  not not_85 (not_85_out, C3);
  not not_86 (not_86_out, C2);
  not not_87 (not_87_out, C0);
  not not_88 (not_88_out, T2);
  not not_89 (not_89_out, T1);
  not not_90 (not_90_out, C3);
  not not_91 (not_91_out, C2);
  not not_92 (not_92_out, T2);
  not not_93 (not_93_out, T0);
  not not_94 (not_94_out, C3);
  not not_95 (not_95_out, C1);
  not not_96 (not_96_out, C0);
  not not_97 (not_97_out, T1);
  not not_98 (not_98_out, T0);
  not not_99 (not_99_out, C3);
  not not_100 (not_100_out, C1);
  not not_101 (not_101_out, T2);
  not not_102 (not_102_out, T0);
  not not_103 (not_103_out, C3);
  not not_104 (not_104_out, T1);
  not not_105 (not_105_out, C2);
  not not_106 (not_106_out, C1);
  not not_107 (not_107_out, C0);
  not not_108 (not_108_out, T2);
  not not_109 (not_109_out, C2);
  not not_110 (not_110_out, C1);
  not not_111 (not_111_out, T2);
  not not_112 (not_112_out, T1);
  not not_113 (not_113_out, C2);
  not not_114 (not_114_out, C0);
  not not_115 (not_115_out, T2);
  not not_116 (not_116_out, T0);
  not not_117 (not_117_out, C2);
  not not_118 (not_118_out, T1);
  not not_119 (not_119_out, T0);
  not not_120 (not_120_out, C1);
  not not_121 (not_121_out, C0);
  not not_122 (not_122_out, T2);
  not not_123 (not_123_out, T0);
  not not_124 (not_124_out, C1);
  not not_125 (not_125_out, T1);
  and and_1 (and_1_out, C2, C1, C0, T2, not_1_out, T0);
  and and_2 (and_2_out, C3, not_2_out);
  and and_3 (and_3_out, C3, not_3_out);
  and and_4 (and_4_out, C3, not_4_out);
  and and_5 (and_5_out, C3, not_5_out);
  and and_6 (and_6_out, C3, T1);
  and and_7 (and_7_out, not_6_out, C1, C0, not_7_out, T1, not_8_out);
  and and_8 (and_8_out, not_9_out, C2, not_10_out);
  and and_9 (and_9_out, C2, not_11_out);
  and and_10 (and_10_out, C2, not_12_out);
  and and_11 (and_11_out, C2, not_13_out);
  and and_12 (and_12_out, C2, T1);
  and and_13 (and_13_out, C3, C1, C0, T2, not_14_out, not_15_out);
  and and_14 (and_14_out, C3, C2, C1);
  and and_15 (and_15_out, not_16_out, not_17_out, C0, not_18_out, T1, T0);
  and and_16 (and_16_out, not_19_out, C1, not_20_out, not_21_out);
  and and_17 (and_17_out, C1, not_22_out);
  and and_18 (and_18_out, C1, not_23_out, not_24_out);
  and and_19 (and_19_out, not_25_out, C1, T0);
  and and_20 (and_20_out, C1, T2, T1);
  and and_21 (and_21_out, not_26_out, C2, C0, not_27_out, T1, not_28_out);
  and and_22 (and_22_out, C2, C1, not_29_out);
  and and_23 (and_23_out, C2, C1, not_30_out);
  and and_24 (and_24_out, C3, not_31_out, C0, not_32_out, not_33_out, T0);
  and and_25 (and_25_out, C3, C1, T1);
  and and_26 (and_26_out, C3, C2, C1);
  and and_27 (and_27_out, not_34_out, not_35_out, not_36_out, not_37_out, T1, not_38_out);
  and and_28 (and_28_out, not_39_out, not_40_out, C0, not_41_out);
  and and_29 (and_29_out, not_42_out, not_43_out, C0, not_44_out);
  and and_30 (and_30_out, C0, not_45_out, not_46_out, not_47_out);
  and and_31 (and_31_out, not_48_out, not_49_out, C0, T2);
  and and_32 (and_32_out, C0, T2, T1);
  and and_33 (and_33_out, not_50_out, not_51_out, C1, not_52_out, not_53_out, T0);
  and and_34 (and_34_out, not_54_out, C1, C0, T0);
  and and_35 (and_35_out, not_55_out, C2, not_56_out, T2, not_57_out, not_58_out);
  and and_36 (and_36_out, C2, C0, not_59_out, T0);
  and and_37 (and_37_out, not_60_out, C2, C1, not_61_out, T2, not_62_out, T0);
  and and_38 (and_38_out, C2, C1, C0, not_63_out);
  and and_39 (and_39_out, C3, not_64_out, not_65_out, not_66_out, T1, T0);
  and and_40 (and_40_out, C3, not_67_out, C0, not_68_out);
  and and_41 (and_41_out, C3, not_69_out, C1, not_70_out, T1, not_71_out);
  and and_42 (and_42_out, C3, C1, C0, T0);
  and and_43 (and_43_out, C3, C2, not_72_out, not_73_out, T1, not_74_out);
  and and_44 (and_44_out, not_75_out, not_76_out, not_77_out, not_78_out, not_79_out, T1, not_80_out);
  and and_45 (and_45_out, not_81_out, not_82_out, not_83_out, C0, not_84_out, T1, T0);
  and and_46 (and_46_out, not_85_out, not_86_out, C1, not_87_out, not_88_out, not_89_out, T0);
  and and_47 (and_47_out, not_90_out, not_91_out, C1, C0, not_92_out, T1, not_93_out);
  and and_48 (and_48_out, not_94_out, C2, not_95_out, not_96_out, T2, not_97_out, not_98_out);
  and and_49 (and_49_out, not_99_out, C2, not_100_out, C0, not_101_out, T1, not_102_out);
  and and_50 (and_50_out, not_103_out, C2, C1, T2, not_104_out, T0);
  and and_51 (and_51_out, C3, not_105_out, not_106_out, not_107_out, not_108_out, T1, T0);
  and and_52 (and_52_out, C3, not_109_out, not_110_out, C0, not_111_out, not_112_out, T0);
  and and_53 (and_53_out, C3, not_113_out, C1, not_114_out, not_115_out, T1, not_116_out);
  and and_54 (and_54_out, C3, not_117_out, C1, C0, T2, not_118_out, not_119_out);
  and and_55 (and_55_out, C3, C2, not_120_out, not_121_out, not_122_out, T1, not_123_out);
  and and_56 (and_56_out, C3, C2, not_124_out, C0, T2, not_125_out, T0);
  or or_1 (D3, and_1_out, and_2_out, and_3_out, and_4_out, and_5_out, and_6_out);
  or or_2 (D2, and_7_out, and_8_out, and_9_out, and_10_out, and_11_out, and_12_out, and_13_out, and_14_out);
  or or_3 (D1, and_15_out, and_16_out, and_17_out, and_18_out, and_19_out, and_20_out, and_21_out, and_22_out, and_23_out, and_24_out, and_25_out, and_26_out);
  or or_4 (Reset, and_44_out, and_45_out, and_46_out, and_47_out, and_48_out, and_49_out, and_50_out, and_51_out, and_52_out, and_53_out, and_54_out, and_55_out, and_56_out);
  or or_5 (D0, and_27_out, and_28_out, and_29_out, and_30_out, and_31_out, and_32_out, and_33_out, and_34_out, and_35_out, and_36_out, and_37_out, and_38_out, and_39_out, and_40_out, and_41_out, and_42_out, and_43_out);
endmodule

module tools_convertB24 (
  input  [4:0] intBits,
  output [4:0] unit,
  output [4:0] ten
);

  wire and_2_out, and_3_out, and_4_out, and_5_out, and_6_out, and_7_out, and_8_out, and_9_out, and_10_out,
       and_11_out, and_12_out, and_13_out, not_1_out, not_2_out, not_3_out, not_4_out, not_5_out, not_6_out,
       not_7_out, not_8_out, not_9_out, not_10_out, not_11_out, not_12_out, not_13_out, not_14_out,
       not_15_out;

  and and_1 (ten[1], intBits[4], intBits[2]);
  not not_1 (not_1_out, intBits[2]);
  not not_2 (not_2_out, intBits[2]);
  not not_3 (not_3_out, intBits[1]);
  not not_4 (not_4_out, intBits[2]);
  not not_5 (not_5_out, intBits[4]);
  not not_6 (not_6_out, intBits[3]);
  not not_7 (not_7_out, intBits[4]);
  not not_8 (not_8_out, intBits[2]);
  not not_9 (not_9_out, intBits[1]);
  not not_10 (not_10_out, intBits[4]);
  not not_11 (not_11_out, intBits[3]);
  not not_12 (not_12_out, intBits[3]);
  not not_13 (not_13_out, intBits[1]);
  not not_14 (not_14_out, intBits[2]);
  not not_15 (not_15_out, intBits[1]);
  and and_2 (and_2_out, intBits[3], intBits[1]);
  and and_3 (and_3_out, intBits[3], intBits[2]);
  and and_4 (and_4_out, intBits[4], not_1_out);
  and and_5 (and_5_out, intBits[3], not_2_out, not_3_out);
  and and_6 (and_6_out, intBits[4], not_4_out, intBits[1]);
  and and_7 (and_7_out, not_5_out, not_6_out, intBits[2]);
  and and_8 (and_8_out, not_7_out, intBits[2], intBits[1]);
  and and_9 (and_9_out, intBits[4], not_8_out, not_9_out);
  and and_10 (and_10_out, not_10_out, not_11_out, intBits[1]);
  and and_11 (and_11_out, not_12_out, intBits[2], intBits[1]);
  and and_12 (and_12_out, intBits[3], intBits[2], not_13_out);
  and and_13 (and_13_out, intBits[4], not_14_out, not_15_out);
  or or_1 (ten[0], and_2_out, and_3_out, and_4_out);
  or or_2 (unit[3], and_5_out, and_6_out);
  or or_3 (unit[2], and_7_out, and_8_out, and_9_out);
  or or_4 (unit[1], and_10_out, and_11_out, and_12_out, and_13_out);

  assign ten[4:2] = 3'b000;
  assign {unit[4], unit[0]} = {1'b0, intBits[0]};
endmodule

module tools_deconvertB24 (
  input  [4:0] inUnit,
  input  [4:0] inTen,
  output [4:0] outBits
);

  wire and_1_out, and_2_out, and_3_out, and_4_out, and_5_out, and_6_out, and_7_out, and_8_out, and_9_out,
       and_10_out, not_1_out, not_2_out, not_3_out, not_4_out, not_5_out, not_6_out, not_7_out, not_8_out,
       not_9_out, not_10_out;

  and and_1 (and_1_out, inTen[0], inUnit[2], inUnit[1]);
  and and_2 (and_2_out, inTen[0], inUnit[3]);
  not not_1 (not_1_out, inTen[0]);
  not not_2 (not_2_out, inUnit[3]);
  not not_3 (not_3_out, inUnit[2]);
  not not_4 (not_4_out, inUnit[3]);
  not not_5 (not_5_out, inUnit[1]);
  not not_6 (not_6_out, inTen[0]);
  not not_7 (not_7_out, inUnit[1]);
  not not_8 (not_8_out, inUnit[2]);
  not not_9 (not_9_out, inTen[0]);
  not not_10 (not_10_out, inUnit[1]);
  or or_1 (outBits[4], and_1_out, and_2_out, inTen[1]);
  and and_3 (and_3_out, not_1_out, inUnit[3]);
  and and_4 (and_4_out, inTen[0], not_2_out, not_3_out);
  and and_5 (and_5_out, inTen[0], not_4_out, not_5_out);
  and and_6 (and_6_out, not_6_out, inUnit[2]);
  and and_7 (and_7_out, inUnit[2], not_7_out);
  and and_8 (and_8_out, inTen[0], not_8_out, inUnit[1]);
  and and_9 (and_9_out, not_9_out, inUnit[1]);
  and and_10 (and_10_out, inTen[0], not_10_out);
  or or_2 (outBits[3], and_3_out, and_4_out, and_5_out);
  or or_3 (outBits[2], and_6_out, and_7_out, and_8_out, inTen[1]);
  or or_4 (outBits[1], and_9_out, and_10_out);

  assign outBits[0] = inUnit[0];
endmodule

module tools_logicEdge (
  input  inSignal,
  input  reset,
  output up,
  output down
);

  wire clock_1_out, d_ff_1_q, d_ff_2_q, xor_1_out;

  Clock sysclk ();  // open: out
  D_Flip_Flop d_ff_1 (.D(inSignal), .clk(clock_1_out), .Q(d_ff_1_q), .reset(reset));  // open: Qn, preset
  Clock clock_1 (.out(clock_1_out));
  D_Flip_Flop d_ff_2 (.D(d_ff_1_q), .clk(clock_1_out), .Q(d_ff_2_q), .reset(reset));  // open: Qn, preset
  xor xor_1 (xor_1_out, d_ff_1_q, d_ff_2_q);
  and and_1 (up, inSignal, xor_1_out);
  and and_2 (down, xor_1_out, ~inSignal);  // AND_Gate
endmodule

module tools_comparator5Bits (
  input  [4:0] alarmHour,
  input  [4:0] actualHour,
  output i
);

  wire xnor_1_out, xnor_2_out, xnor_3_out, xnor_4_out, xnor_5_out;

  xnor xnor_1 (xnor_1_out, alarmHour[0], actualHour[0]);
  xnor xnor_2 (xnor_2_out, alarmHour[1], actualHour[1]);
  xnor xnor_3 (xnor_3_out, alarmHour[2], actualHour[2]);
  xnor xnor_4 (xnor_4_out, alarmHour[3], actualHour[3]);
  xnor xnor_5 (xnor_5_out, alarmHour[4], actualHour[4]);
  and and_1 (i, xnor_1_out, xnor_2_out, xnor_3_out, xnor_4_out, xnor_5_out);
endmodule

module tools_fiveBitsDFF (
  input  [4:0] inBits,
  input  setSignal,
  input  reset,
  input  clock,
  output [4:0] outBits
);

  wire [4:0] multiplexer_1_out;

  Multiplexer #(.width(5), .enable("false")) multiplexer_1 (
    .in0(outBits), .in1(inBits), .out(multiplexer_1_out), .sel(setSignal));
  D_Flip_Flop d_ff_1 (.D(multiplexer_1_out[0]), .clk(clock), .Q(outBits[0]), .reset(reset));  // open: Qn, preset
  D_Flip_Flop d_ff_2 (.D(multiplexer_1_out[1]), .clk(clock), .Q(outBits[1]), .reset(reset));  // open: Qn, preset
  D_Flip_Flop d_ff_3 (.D(multiplexer_1_out[2]), .clk(clock), .Q(outBits[2]), .reset(reset));  // open: Qn, preset
  D_Flip_Flop d_ff_4 (.D(multiplexer_1_out[3]), .clk(clock), .Q(outBits[3]), .reset(reset));  // open: Qn, preset
  D_Flip_Flop d_ff_5 (.D(multiplexer_1_out[4]), .clk(clock), .Q(outBits[4]), .reset(reset));  // open: Qn, preset
endmodule

module tools_superAdder (
  input  enable,
  input  carryIn,
  input  [4:0] lastNumber,
  input  clockIn,
  input  [4:0] setBits,
  input  setSignal,
  input  reset,
  input  stopEnd,
  output [4:0] outBits,
  output carryOut
);

  wire clock_1_out, comparator_1_gt;
  wire [1:0] superAdderLogicTransistion_1_outmult;
  wire [4:0] adder_1_out, multiplexer_1_out;

  Adder #(.width(5)) adder_1 (.a(outBits), .b({5{1'b0}}), .out(adder_1_out), .cin(carryIn));  // open: cout
  Comparator #(.width(5), .mode("unsigned")) comparator_1 (
    .a(adder_1_out), .b(lastNumber), .gt(comparator_1_gt));  // open: eq, lt
  tools_superLogicTransistion superAdderLogicTransistion_1 (
    .setSignal(setSignal), .stopEnd(stopEnd), .endOfCounting(comparator_1_gt), .enable(enable),
    .clockIn(clockIn), .carryIn(carryIn), .outMult(superAdderLogicTransistion_1_outmult),
    .carryOutSelector(carryOut));
  Multiplexer #(.select(2), .width(5), .enable("false")) multiplexer_1 (
    .in0(outBits), .in1(adder_1_out), .in2({5{1'b0}}), .in3(setBits), .out(multiplexer_1_out),
    .sel(superAdderLogicTransistion_1_outmult));
  D_Flip_Flop d_ff_1 (.D(multiplexer_1_out[0]), .clk(clock_1_out), .Q(outBits[0]), .reset(reset));  // open: Qn, preset
  D_Flip_Flop d_ff_2 (.D(multiplexer_1_out[1]), .clk(clock_1_out), .Q(outBits[1]), .reset(reset));  // open: Qn, preset
  D_Flip_Flop d_ff_3 (.D(multiplexer_1_out[2]), .clk(clock_1_out), .Q(outBits[2]), .reset(reset));  // open: Qn, preset
  D_Flip_Flop d_ff_4 (.D(multiplexer_1_out[3]), .clk(clock_1_out), .Q(outBits[3]), .reset(reset));  // open: Qn, preset
  D_Flip_Flop d_ff_5 (.D(multiplexer_1_out[4]), .clk(clock_1_out), .Q(outBits[4]), .reset(reset));  // open: Qn, preset
  Clock clock_1 (.out(clock_1_out));
endmodule

module tools_superSubstracter (
  input  enable,
  input  carryIn,
  input  [4:0] initialValue,
  input  clockIn,
  input  [4:0] setNumber,
  input  setSignal,
  input  reset,
  input  stopEnd,
  output [4:0] Output_bus_1,
  output Output_1
);

  wire clock_1_out, comparator_1_eq;
  wire [1:0] superAdderLogicTransistion_1_outmult;
  wire [4:0] multiplexer_1_out, subtractor_1_out;

  Subtractor #(.width(5)) subtractor_1 (
    .a(Output_bus_1), .b({5{1'b0}}), .out(subtractor_1_out), .bin(carryIn));  // open: bout
  Comparator #(.width(5), .mode("unsigned")) comparator_1 (
    .a(Output_bus_1), .b({5{1'b0}}), .eq(comparator_1_eq));  // open: gt, lt
  tools_superLogicTransistion superAdderLogicTransistion_1 (
    .setSignal(setSignal), .stopEnd(stopEnd), .endOfCounting(comparator_1_eq), .enable(enable),
    .clockIn(clockIn), .carryIn(carryIn), .outMult(superAdderLogicTransistion_1_outmult),
    .carryOutSelector(Output_1));
  Multiplexer #(.select(2), .width(5), .enable("false")) multiplexer_1 (
    .in0(Output_bus_1), .in1(subtractor_1_out), .in2(initialValue), .in3(setNumber), .out(multiplexer_1_out),
    .sel(superAdderLogicTransistion_1_outmult));
  D_Flip_Flop d_ff_1 (
    .D(multiplexer_1_out[0]), .clk(clock_1_out), .Q(Output_bus_1[0]), .reset(reset));  // open: Qn, preset
  D_Flip_Flop d_ff_2 (
    .D(multiplexer_1_out[1]), .clk(clock_1_out), .Q(Output_bus_1[1]), .reset(reset));  // open: Qn, preset
  D_Flip_Flop d_ff_3 (
    .D(multiplexer_1_out[2]), .clk(clock_1_out), .Q(Output_bus_1[2]), .reset(reset));  // open: Qn, preset
  D_Flip_Flop d_ff_4 (
    .D(multiplexer_1_out[3]), .clk(clock_1_out), .Q(Output_bus_1[3]), .reset(reset));  // open: Qn, preset
  D_Flip_Flop d_ff_5 (
    .D(multiplexer_1_out[4]), .clk(clock_1_out), .Q(Output_bus_1[4]), .reset(reset));  // open: Qn, preset
  Clock clock_1 (.out(clock_1_out));

  // Other names for the same wires on the sheet: carryOut = Output_1
endmodule

module tools_superLogicTransistion (
  input  setSignal,
  input  stopEnd,
  input  endOfCounting,
  input  enable,
  input  clockIn,
  input  carryIn,
  output [1:0] outMult,
  output carryOutSelector
);

  wire and_1_out, and_2_out, and_3_out, not_1_out, not_2_out;

  and and_1 (and_1_out, enable, clockIn, carryIn);
  not not_1 (not_1_out, stopEnd);
  not not_2 (not_2_out, endOfCounting);
  and and_2 (and_2_out, not_1_out, endOfCounting, and_1_out);
  and and_3 (and_3_out, not_2_out, and_1_out);
  and and_4 (carryOutSelector, endOfCounting, enable, carryIn);
  or or_1 (outMult[1], and_2_out, setSignal);
  or or_2 (outMult[0], and_3_out, setSignal);
endmodule
